// Logisim project FISR.circ as structural Verilog: 6 circuits, main circuit Divider
module Divider (
  input  [15:0] X,
  input  [15:0] Y,
  output [15:0] X_Y
);

  wire [15:0] fisr_1_y, multiplier_1_x_y;

  FISR fisr_1 (.X(Y), .Y(fisr_1_y));
  Multiplier multiplier_1 (.X_Y(multiplier_1_x_y), .Y(fisr_1_y), .X(X));  // open: NaN, INF, UNF, OVF
  Multiplier multiplier_2 (.X_Y(X_Y), .Y(fisr_1_y), .X(multiplier_1_x_y));  // open: NaN, INF, UNF, OVF
endmodule

module Rooter (
  input  [15:0] X,
  output [15:0] SQRT
);

  wire [15:0] fisr_1_y;

  FISR fisr_1 (.X(X), .Y(fisr_1_y));
  Multiplier multiplier_1 (.X_Y(SQRT), .Y(fisr_1_y), .X(X));  // open: NaN, INF, UNF, OVF
endmodule

module FISR (
  input  [15:0] X,
  output [15:0] Y
);

  wire [15:0] fisr1_1_y;

  FISR1 fisr1_1 (.X(X), .Y(fisr1_1_y));
  Newton_Raphson newton_raphson_1 (.Y(fisr1_1_y), .X(X), .Z(Y));
endmodule

module FISR1 (
  input  [15:0] X,
  output [15:0] Y
);

  wire comparator_1_eq, comparator_1_lt, comparator_2_eq, comparator_2_lt, comparator_3_eq, comparator_3_lt,
       comparator_4_eq, comparator_4_lt, comparator_5_eq, comparator_5_lt, comparator_6_eq, comparator_6_lt,
       comparator_7_eq, comparator_7_lt, comparator_8_eq, comparator_8_lt, comparator_9_eq, comparator_9_lt,
       or_1_out, or_2_out, or_3_out, or_4_out, or_5_out, or_6_out, or_7_out, or_8_out, or_9_out;
  wire [3:0] priority_encoder_1_out;
  wire [15:0] multiplexer_1_out, shifter_1_out;

  Comparator #(.mode("unsigned"), .width(10)) comparator_1 (
    .a(X[9:0]), .b(10'h399), .eq(comparator_1_eq), .lt(comparator_1_lt));  // open: gt
  Comparator #(.mode("unsigned"), .width(10)) comparator_2 (
    .a(X[9:0]), .b(10'h333), .eq(comparator_2_eq), .lt(comparator_2_lt));  // open: gt
  Comparator #(.mode("unsigned"), .width(10)) comparator_3 (
    .a(X[9:0]), .b(10'h2cc), .eq(comparator_3_eq), .lt(comparator_3_lt));  // open: gt
  Comparator #(.mode("unsigned"), .width(10)) comparator_4 (
    .a(X[9:0]), .b(10'h266), .eq(comparator_4_eq), .lt(comparator_4_lt));  // open: gt
  Comparator #(.mode("unsigned"), .width(10)) comparator_5 (
    .a(X[9:0]), .b(10'h200), .eq(comparator_5_eq), .lt(comparator_5_lt));  // open: gt
  Comparator #(.mode("unsigned"), .width(10)) comparator_6 (
    .a(X[9:0]), .b(10'h199), .eq(comparator_6_eq), .lt(comparator_6_lt));  // open: gt
  Comparator #(.mode("unsigned"), .width(10)) comparator_7 (
    .a(X[9:0]), .b(10'h133), .eq(comparator_7_eq), .lt(comparator_7_lt));  // open: gt
  Comparator #(.mode("unsigned"), .width(10)) comparator_8 (
    .a(X[9:0]), .b(10'hcc), .eq(comparator_8_eq), .lt(comparator_8_lt));  // open: gt
  Comparator #(.mode("unsigned"), .width(10)) comparator_9 (
    .a(X[9:0]), .b(10'h66), .eq(comparator_9_eq), .lt(comparator_9_lt));  // open: gt
  or or_1 (or_1_out, comparator_1_eq, comparator_1_lt);
  or or_2 (or_2_out, comparator_2_eq, comparator_2_lt);
  or or_3 (or_3_out, comparator_3_eq, comparator_3_lt);
  or or_4 (or_4_out, comparator_4_eq, comparator_4_lt);
  or or_5 (or_5_out, comparator_5_eq, comparator_5_lt);
  or or_6 (or_6_out, comparator_6_eq, comparator_6_lt);
  or or_7 (or_7_out, comparator_7_eq, comparator_7_lt);
  or or_8 (or_8_out, comparator_8_eq, comparator_8_lt);
  or or_9 (or_9_out, comparator_9_eq, comparator_9_lt);
  Priority_Encoder #(.select(4)) priority_encoder_1 (
    .in0(1'b1), .in1(or_1_out), .in2(or_2_out), .in3(or_3_out), .in4(or_4_out), .in5(or_5_out),
    .in6(or_6_out), .in7(or_7_out), .in8(or_8_out), .in9(or_9_out), .out(priority_encoder_1_out));  // open: in10, in11, in12, in13, in14, in15, gs, en_out, en_in
  Shifter #(.shift("lr"), .width(16)) shifter_1 (.in(X), .\dist (4'b0001), .out(shifter_1_out));
  Multiplexer #(.enable("false"), .select(4), .width(16)) multiplexer_1 (
    .in0(16'h59ec), .in1(16'h59c7), .in2(16'h59a8), .in3(16'h5991), .in4(16'h5982), .in5(16'h597c),
    .in6(16'h5981), .in7(16'h5992), .in8(16'h59b1), .in9(16'h59e2), .out(multiplexer_1_out),
    .sel(priority_encoder_1_out));  // open: in10, in11, in12, in13, in14, in15
  Subtractor #(.width(16)) subtractor_1 (.a(multiplexer_1_out), .b(shifter_1_out), .out(Y));  // open: bin, bout
endmodule

module Newton_Raphson (
  input  [15:0] Y,
  input  [15:0] X,
  output [15:0] Z
);

  wire [15:0] asm_1_z, asm_2_z, asm_3_z, asm_4_z;

  ASM asm_1 (.X(Y), .sub(1'b0), .mul(1'b1), .Y(Y), .Z(asm_1_z));
  ASM asm_2 (.X(asm_1_z), .sub(1'b0), .mul(1'b1), .Y(X), .Z(asm_2_z));
  ASM asm_3 (.X(asm_2_z), .sub(1'b0), .mul(1'b1), .Y(16'h3800), .Z(asm_3_z));
  ASM asm_4 (.X(16'h3e00), .sub(1'b1), .mul(1'b0), .Y(asm_3_z), .Z(asm_4_z));
  ASM asm_5 (.X(Y), .sub(1'b0), .mul(1'b1), .Y(asm_4_z), .Z(Z));
endmodule

module ASM (
  input  [15:0] X,
  input  sub,
  input  mul,
  input  [15:0] Y,
  output [15:0] Z
);

  wire [15:0] adder_subractor_1_x___y, multiplier_1_x_y;

  Adder_Subractor adder_subractor_1 (.X___Y(adder_subractor_1_x___y), .sub(sub), .X(X), .Y(Y));  // open: ovf, inf, NaN
  Multiplier multiplier_1 (.X_Y(multiplier_1_x_y), .Y(Y), .X(X));  // open: NaN, INF, UNF, OVF
  Multiplexer #(.enable("false"), .width(16)) multiplexer_1 (
    .in0(adder_subractor_1_x___y), .in1(multiplier_1_x_y), .out(Z), .sel(mul));
endmodule
