// Logisim project ADDER SUBTRACTOR EVOLUTION VERSION.circ as structural Verilog
module TOP_LEVEL (
  input  ADD_SUBTRACT
);

  wire clk, minus_zero, NaN, NNN, NNS, Not_Exact, NSN, NSS, overflow__inf, overflow__inf_t, plus_zero, SSN,
       SSS;
  wire [7:0] A;
  wire [31:0] X, X_Y, Y;

  RAM #(.dataWidth(32)) ram_1 (.addr(A), .clk(clk), .dout(X));  // open: we, din
  LED led_1 (.in(NNN));
  LED led_2 (.in(NNS));
  LED led_3 (.in(NSN));
  LED led_4 (.in(NSS));
  LED led_5 (.in(SSN));
  LED led_6 (.in(SSS));
  // Probe on X
  RAM #(.dataWidth(32)) ram_2 (.addr(A), .we(1'b1), .clk(clk), .din(X_Y));  // open: dout
  Clock clock_1 (.out(clk));
  Counter counter_1 (.count(1'b1), .Q(A), .clk(clk));  // open: load, D, carry, clr
  ADD_SUBTRACT add_subtract_1 (
    .out_7(NaN), .out_9(overflow__inf), .out_11(overflow__inf_t), .X_______Y(X_Y), .out_8(NNS),
    .out_10(Not_Exact), .out_12(SSS), .out_4(NSS), .out_13(SSN), .out_5(NSN), .out_6(NNN),
    .out_14(plus_zero), .out_15(minus_zero), .in_3(ADD_SUBTRACT), .X(X), .Y(Y));
  // Probe on X_Y
  RAM #(.dataWidth(32)) ram_3 (.addr(A), .clk(clk), .dout(Y));  // open: we, din
  // Probe on Y
  LED led_7 (.in(Not_Exact));
  LED led_8 (.in(NaN));
  LED led_9 (.in(overflow__inf));
  LED led_10 (.in(overflow__inf_t));
  LED led_11 (.in(plus_zero));
  LED led_12 (.in(minus_zero));

  // Notes on the sheet:
  //   normal
  //   subnormal
  //   flags
endmodule

module ADD_SUBTRACT (
  input  [31:0] Y,
  input  [31:0] X,
  input  in_3,
  output out_4,
  output out_5,
  output out_6,
  output out_7,
  output out_8,
  output out_9,
  output out_10,
  output out_11,
  output out_12,
  output out_13,
  output out_14,
  output out_15,
  output [31:0] X_______Y
);

  wire and_1_out, ex_ey_2, G, go, LSB, mr_2, mr_2_t, Mrns, ne, nf, nn, nof, nx, ny, of, part_1__24,
       part_1__25, R, Sby, sf, sn, Srn, swap, Sx, Sxo, Sy, Syo, Sz;
  wire [4:0] LZC;
  wire [8:0] Er, Ex, ex_emin, ex_ey, ex_t, Ey, ey_t, sub_1_er;
  wire [22:0] exponent_difference_swap_1_out_8, exponent_difference_swap_1_out_11, Mx, My, shift_1_out_8;
  wire [23:0] lzc_shift_1_out_9, mx_my_1_out_4, n1_bt_shift_1_out_3, n1_xxx_1_out_3, n1_xxx_2_out_3,
       normalise_1_out_10, part_1_mr, shift_1_out_6;
  wire [31:0] concatenate_1_x___y, concatenate_2_x___y, path_1_out_4, X___Y_B;

  // Probe on Y
  // Probe on X
  TYPE type_1 (.out_7(nf), .out_8(sn), .out_5(nn), .out_6(sf), .in_3(ex_t), .in_4(LZC), .in_1(Er), .in_2(Srn));
  ADD_SUB_BUTTON add_sub_button_1 (.Sy_2(Sby), .in_1(in_3), .Sy(Sy));
  SPLITTER splitter_1 (.out_8(Sx), .out_3(My), .out_4(Ey), .out_5(Sy), .out_6(Mx), .out_7(Ex), .in_1(Y), .in_2(X));
  SIGN sign_1 (.out_3(Srn), .inputs(Sxo), .in_2(Mrns));
  SUB sub_1 (.ex_emin(ex_emin), .Er(sub_1_er), .in_1(ex_t), .in_2(LZC), .in_3(ey_t), .in_4(sn));
  xor xor_1 (Sz, Sxo, Syo);
  _1_XXX u_1_xxx_1 (.out_3(n1_xxx_1_out_3), .in_2(exponent_difference_swap_1_out_11), .nx___ny(nx));
  mx_my mx_my_1 (.out_4(mx_my_1_out_4), .out_5(Mrns), .in_1(n1_bt_shift_1_out_3), .in_2(n1_xxx_1_out_3), .in_3(ex_ey));
  _1_XXX u_1_xxx_2 (.out_3(n1_xxx_2_out_3), .in_2(exponent_difference_swap_1_out_8), .nx___ny(ny));
  _1_BT_SHIFT u_1_bt_shift_1 (.out_3(n1_bt_shift_1_out_3), .in_1(n1_xxx_2_out_3), .in_2(ex_ey));
  LZC_SHIFT lzc_shift_1 (
    .out_8(LZC), .out_9(lzc_shift_1_out_9), .in_3(nx), .in_4(ny), .in_5(Sz), .in_6(sn), .in_7(ex_emin),
    .in_1(mx_my_1_out_4), .in_2(ex_t));
  CONCATENATE concatenate_1 (.X___Y(concatenate_1_x___y), .in_2(sub_1_er), .in_1(Srn), .in_3(lzc_shift_1_out_9));
  ROUND round_1 (.x_____y_out(X___Y_B), .in_2(G), .in_3(nof), .in_1(R), .x_____y_in(path_1_out_4));
  PATH path_1 (.out_4(path_1_out_4), .N___F(nof), .NEAR(concatenate_1_x___y), .FAR(concatenate_2_x___y));
  circuit part_1 (
    .Mr(part_1_mr), ._24(part_1__24), ._25(part_1__25), .in_1(shift_1_out_6), .in_2(n1_xxx_1_out_3), .in_3(Sz));
  SHIFT shift_1 (
    .out_7(go), .out_6(shift_1_out_6), .out_8(shift_1_out_8), .out_9(G), .in_1(ex_ey), .in_2(n1_xxx_2_out_3),
    .in_3(mr_2), .in_4(mr_2_t), .in_5(LSB));
  CONCATENATE concatenate_2 (.X___Y(concatenate_2_x___y), .in_2(Er), .in_1(Sxo), .in_3(normalise_1_out_10));
  not not_1 (nof, and_1_out);
  SPECIAL_CASES special_cases_1 (
    .X_______Y_O(X_______Y), .out_17(out_7), .out_18(out_6), .out_19(out_8), .out_20(out_5), .out_21(out_4),
    .out_22(out_13), .out_23(out_12), .out_24(out_14), .out_25(out_15), .out_26(out_9), .out_27(out_11),
    .out_28(out_10), .in_7(nn), .in_9(sn), .in_11(nof), .in_3(in_3), .in_4(Sx), .in_5(Sy), .in_12(of),
    .in_13(Sxo), .in_14(Ex), .in_15(Ey), .in_16(ne), .X(X), .Y(Y), .X___Y(X___Y_B), .in_8(nf), .in_10(sf));
  EXPONENT_DIFFERENCE_SWAP exponent_difference_swap_1 (
    .nx(nx), .ny(ny), .ex_ey(ex_ey), .out_8(exponent_difference_swap_1_out_8), .out_9(ey_t), .out_10(swap),
    .out_11(exponent_difference_swap_1_out_11), .out_12(ex_t), .out_13(Sxo), .out_14(Syo), .in_1(My),
    .in_2(Ey), .in_3(Sby), .in_4(Mx), .in_5(Ex), .in_6(Sx));
  STICKY sticky_1 (.NE(ne), .out_3(R), ._1_gaurd_bit(shift_1_out_8));
  NORMALISE normalise_1 (
    .out_12(mr_2), .out_13(mr_2_t), .out_10(normalise_1_out_10), .out_14(LSB), .ex_ey_2(ex_ey_2),
    .out_16(of), .Er(Er), .in_2(part_1_mr), .in_1(ex_t), .in_3(ex_ey), .in_4(go), .nx(nx), .ny(ny),
    .in_7(Sz), .in_8(part_1__25), .in_9(part_1__24));
  and and_1 (and_1_out, ex_ey_2, Sz);

  // Other names for the same wires on the sheet: tunnel = in_3; X___Y_O[31:0] = X_______Y

  // Notes on the sheet:
  //   NEAR
  //   0
  //   1
  //   FAR
endmodule

module SPLITTER (
  input  [31:0] in_1,
  input  [31:0] in_2,
  output [22:0] out_3,
  output [8:0] out_4,
  output out_5,
  output [22:0] out_6,
  output [8:0] out_7,
  output out_8
);

  assign out_7 = {{1{1'b0}}, in_2[30:23]};  // Bit_Extender bit_extender_1
  assign out_4 = {{1{1'b0}}, in_1[30:23]};  // Bit_Extender bit_extender_2

  assign out_3 = in_1[22:0];
  assign out_5 = in_1[31];
  assign out_6 = in_2[22:0];
  assign out_8 = in_2[31];

  // Other names for the same wires on the sheet: Exo[8:0] = out_7; Eyo[8:0] = out_4; Mx[22:0] = in_2[22:0];
  //   X[31:0] = in_2; Ex[7:0] = in_2[30:23]; Sx = in_2[31]; My[22:0] = in_1[22:0]; Y[31:0] = in_1;
  //   Ey[7:0] = in_1[30:23]; Sy = in_1[31]

  // Notes on the sheet:
  //   inputs
  //   Y
  //   inputs
  //   X
  //   split
  //   split
  //   9 bit exponent
  //   outputs
  //   outputs
  //   Y
  //   X
endmodule

module EXPONENT_DIFFERENCE_SWAP (
  input  [22:0] in_1,
  input  [8:0] in_2,
  input  in_3,
  input  [22:0] in_4,
  input  [8:0] in_5,
  input  in_6,
  output [8:0] ex_ey,
  output [22:0] out_8,
  output [8:0] out_9,
  output out_10,
  output [22:0] out_11,
  output [8:0] out_12,
  output out_13,
  output out_14,
  output nx,
  output ny
);

  wire [8:0] bit_extender_1_out, bit_extender_2_out, Exo, Eyo, subtractor_1_out, subtractor_5_out;

  or or_1 (nx, Exo[0], Exo[1], Exo[2], Exo[3], Exo[4], Exo[5], Exo[6], Exo[7]);
  Subtractor #(.width(9)) subtractor_1 (.a(Exo), .b(9'h7e), .out(subtractor_1_out));  // open: bin, bout
  assign bit_extender_1_out = {{8{1'b0}}, nx};  // Bit_Extender bit_extender_1
  Multiplexer multiplexer_1 (.in0(in_6), .in1(in_3), .out(out_13), .sel(out_10));  // open: en
  Multiplexer multiplexer_2 (.in0(in_3), .in1(in_6), .out(out_14), .sel(out_10));  // open: en
  Subtractor #(.width(9)) subtractor_2 (.a(subtractor_1_out), .b(bit_extender_1_out), .out(out_12));  // open: bin, bout
  or or_2 (ny, Eyo[0], Eyo[1], Eyo[2], Eyo[3], Eyo[4], Eyo[5], Eyo[6], Eyo[7]);
  Subtractor #(.width(9)) subtractor_3 (.a(in_5), .b(in_2), .bout(out_10));  // open: out, bin
  Multiplexer #(.width(9)) multiplexer_3 (.in0(in_5), .in1(in_2), .out(Exo), .sel(out_10));  // open: en
  Multiplexer #(.width(9)) multiplexer_4 (.in0(in_2), .in1(in_5), .out(Eyo), .sel(out_10));  // open: en
  Subtractor #(.width(9)) subtractor_4 (.a(out_12), .b(out_9), .out(ex_ey));  // open: bin, bout
  Subtractor #(.width(9)) subtractor_5 (.a(Eyo), .b(9'h7e), .out(subtractor_5_out));  // open: bin, bout
  assign bit_extender_2_out = {{8{1'b0}}, ny};  // Bit_Extender bit_extender_2
  Multiplexer #(.width(23)) multiplexer_5 (.in0(in_4), .in1(in_1), .out(out_11), .sel(out_10));  // open: en
  Multiplexer #(.width(23)) multiplexer_6 (.in0(in_1), .in1(in_4), .out(out_8), .sel(out_10));  // open: en
  Subtractor #(.width(9)) subtractor_6 (.a(subtractor_5_out), .b(bit_extender_2_out), .out(out_9));  // open: bin, bout

  // Other names for the same wires on the sheet: Ex[8:0] = in_5; ex_t[8:0] = out_12; Ey[8:0] = in_2;
  //   ey_t[8:0] = out_9; mx[22:0] = in_4; mxo[22:0] = out_11; my[22:0] = in_1; myo[22:0] = out_8; swap = out_10;
  //   Sx = in_6; Sxo = out_13; Sy = in_3; Syo = out_14

  // Notes on the sheet:
  //   Y inputs
  //   X inputs
  //   test subnormal X
  //   calculate biased exponent ex
  //   ex=Ex-bias +1-nx
  //   Swap Sign
  //   Swap
  //   test subnormal Y
  //   Swap Exponent
  //   difference
  //   test subnormal outputs
  //   Swap Mantissa
  //   nx, ny = 0
  //   calculate biased exponent ey
  //   ey = Ey - bias +1 - ny
  //   nx, ny = 1    normal number
  //   subnormal number
  //   Y out
  //   X out
endmodule

module ADD_SUB_BUTTON (
  input  in_1,
  input  Sy,
  output Sy_2
);

  wire and_1_out, and_2_out, not_1_out, not_2_out;

  not not_1 (not_1_out, in_1);
  not not_2 (not_2_out, Sy);
  and and_1 (and_1_out, not_1_out, Sy);
  and and_2 (and_2_out, in_1, not_2_out);
  or or_1 (Sy_2, and_1_out, and_2_out);

  // Notes on the sheet:
  //   0    0    0
  //   0    1    1
  //   1    0    1
  //   1    1    0
  //   Exclusive Or
  //   Sx passes through with no change
  //   Sy changes from 1 to 0 or 0 to 1 depending on +/-
  //   +/- Sy Syo
endmodule

module SHIFT (
  input  [8:0] in_1,
  input  [23:0] in_2,
  input  in_3,
  input  in_4,
  input  in_5,
  output [23:0] out_6,
  output out_7,
  output [22:0] out_8,
  output out_9
);

  wire and_1_out, and_2_out, not_1_out, not_2_out, not_3_out;
  wire [4:0] bit_extender_1_out, bit_extender_2_out, bit_extender_3_out;
  wire [8:0] subtractor_1_out;
  wire [22:0] rounding_bits;
  wire [23:0] multiplexer_1_out, pull_resistor_1_node, shifter_1_out, shifter_2_out, shifter_4_out, undriven;

  Bit_Extender #(.in_width(9), .out_width(5), .\type ("zero")) bit_extender_1 (.in(in_1), .out(bit_extender_1_out));
  not not_1 (not_1_out, in_3);
  not not_2 (not_2_out, in_3);
  not not_3 (not_3_out, in_4);
  Shifter #(.width(24)) shifter_1 (.in({out_7, rounding_bits}), .\dist (5'b00001), .out(shifter_1_out));
  Shifter #(.shift("lr"), .width(24)) shifter_2 (.in({out_7, rounding_bits}), .\dist (5'b00001), .out(shifter_2_out));
  and and_1 (and_1_out, not_1_out, in_4);
  and and_2 (and_2_out, not_2_out, not_3_out);
  Shifter #(.shift("lr"), .width(24)) shifter_3 (.in(in_2), .\dist (bit_extender_1_out), .out(out_6));
  Multiplexer #(.width(24)) multiplexer_1 (
    .in0(shifter_1_out), .in1({in_5, shifter_2_out[23:1]}), .out(multiplexer_1_out), .sel(and_1_out));  // open: en
  Bit_Extender #(.in_width(9), .out_width(5), .\type ("zero")) bit_extender_2 (.in(in_1), .out(bit_extender_2_out));
  Subtractor #(.width(9)) subtractor_1 (.a(9'h18), .b(in_1), .out(subtractor_1_out));  // open: bin, bout
  Multiplexer #(.width(24)) multiplexer_2 (
    .in0(multiplexer_1_out), .in1({out_7, rounding_bits}), .out({out_9, out_8}), .sel(and_2_out));  // open: en
  Shifter #(.shift("rr"), .width(24)) shifter_4 (.in(in_2), .\dist (bit_extender_2_out), .out(shifter_4_out));
  Bit_Extender #(.in_width(9), .out_width(5), .\type ("zero")) bit_extender_3 (
    .in(subtractor_1_out), .out(bit_extender_3_out));
  Pull_Resistor #(.pull(1)) pull_resistor_1 (.node(pull_resistor_1_node));
  Shifter #(.width(24)) shifter_5 (.in(undriven), .\dist (bit_extender_3_out), .out(pull_resistor_1_node));
  assign {out_7, rounding_bits} = shifter_4_out & pull_resistor_1_node;  // AND_Gate and_3, 24 bits wide

  // Other names for the same wires on the sheet: LSB = in_5; sticky[22:0] = out_8; gaurd = out_9; ex_ey[8:0] = in_1;
  //   Mout[23:0] = out_6; mr_2 = in_3; mr_2_t = in_4; My[23:0] = in_2; rounding_bits[23] = out_7

  // Notes on the sheet:
  //   inputs
  //   3
  //   2
  //   1
  //   shift my right by ex-ey
  //   left shift
  //   right shift
  //   no shift
  //   multiplexer control bits
  //   1 - Addition without ripple no change in LSB , G , R bit positions
  //   Change in LSB , G , R bit positions due to normalisation
  //   2 - Addition with ripple increase exponent by 1 and decrease mantissa mr/2. LSB, G, R shift 1 right
  //   3 - Subtraction  with cancellation. Exponent decreases by 1 and increase mantissa mr*2. LSB, G , Rshift 1 left
  //   keep a copy of the shift out for rounding
  //   gaurd bit injection
  //   mantissa output Y
  //   rounding outputs
endmodule

module _1_XXX (
  input  nx___ny,
  input  [22:0] in_2,
  output [23:0] out_3
);

  assign out_3 = {{1{nx___ny}}, in_2};  // Bit_Extender bit_extender_1

  // Notes on the sheet:
  //   hidden bit 0, 1 for subnormal / normal
endmodule

module circuit (
  input  [23:0] in_1,
  input  [23:0] in_2,
  input  in_3,
  output _24,
  output [23:0] Mr,
  output _25
);

  wire _25_minus, _25_plus;
  wire [23:0] adder_1_out, mxmy, not_1_out, out;

  assign not_1_out = ~in_1;  // NOT_Gate not_1, 24 bits wide
  Adder #(.width(24)) adder_1 (.a(in_2), .b(in_1), .out(adder_1_out), .cout(_25_plus));  // open: cin
  Adder #(.width(24)) adder_2 (.a(in_2), .b(mxmy), .out(out), .cout(_25_minus));  // open: cin
  Multiplexer #(.width(24)) multiplexer_1 (
    .in0(adder_1_out), .in1(out), .out({_24, Mr[22:0]}), .sel(in_3));  // open: en
  Adder #(.width(24)) adder_3 (.a(not_1_out), .b(24'h1), .out(mxmy));  // open: cin, cout
  Multiplexer multiplexer_2 (.in0(_25_plus), .in1(_25_minus), .out(_25), .sel(in_3));  // open: en

  assign Mr[23] = _24;

  // Other names for the same wires on the sheet: _1_Mx[23:0] = in_2; _1_My[23:0] = in_1; Sz = in_3

  // Notes on the sheet:
  //   inputs mx and my
  //   addition = 0 subtraction = 1
  //   addition
  //   subtraction
  //   2's complement
  //   add
  //   outputs
  //   choose correct 25th bit
endmodule

module NORMALISE (
  input  [8:0] in_1,
  input  [23:0] in_2,
  input  [8:0] in_3,
  input  in_4,
  input  nx,
  input  ny,
  input  in_7,
  input  in_8,
  input  in_9,
  output [23:0] out_10,
  output [8:0] Er,
  output out_12,
  output out_13,
  output out_14,
  output ex_ey_2,
  output out_16
);

  wire and_2_out, and_4_out, and_5_out, comparator_2_gt, comparator_3_lt, er3, mr1, mr_can, not_1_out,
       not_2_out, not_3_out, not_4_out, not_5_out, not_6_out, not_7_out, not_8_out, not_9_out, not_10_out,
       not_11_out, or_1_out, sub_norm;
  wire [8:0] adder_1_out, er_t, multiplexer_1_out, subtractor_1_out;
  wire [23:0] Mrout_1, multiplexer_2_out, shifter_1_out, shifter_2_out;

  not not_1 (not_1_out, out_13);
  not not_2 (not_2_out, nx);
  not not_3 (not_3_out, ny);
  not not_4 (not_4_out, in_7);
  not not_5 (not_5_out, in_9);
  and and_1 (mr_can, out_12, not_1_out);
  and and_2 (and_2_out, not_2_out, not_4_out, not_3_out);
  and and_3 (sub_norm, and_2_out, not_5_out);
  Adder #(.width(9)) adder_1 (.a(in_1), .b(9'h1), .out(adder_1_out));  // open: cin, cout
  Subtractor #(.width(9)) subtractor_1 (.a(in_1), .b(9'h1), .out(subtractor_1_out));  // open: bin, bout
  Shifter #(.shift("lr"), .width(24)) shifter_1 (.in(in_2), .\dist (5'b00001), .out(shifter_1_out));
  Shifter #(.width(24)) shifter_2 (.in(in_2), .\dist (5'b00001), .out(shifter_2_out));
  Multiplexer #(.width(9)) multiplexer_1 (
    .in0(in_1), .in1(adder_1_out), .out(multiplexer_1_out), .sel(er3));  // open: en
  not not_6 (not_6_out, in_9);
  Multiplexer #(.width(24)) multiplexer_2 (
    .in0(in_2), .in1(shifter_1_out), .out(multiplexer_2_out), .sel(mr1));  // open: en
  not not_7 (not_7_out, in_9);
  not not_8 (not_8_out, in_7);
  and and_4 (and_4_out, in_7, not_6_out);
  Multiplexer #(.width(24)) multiplexer_3 (
    .in0(multiplexer_2_out), .in1(shifter_2_out), .out(Mrout_1), .sel(and_5_out));  // open: en
  and and_5 (and_5_out, in_7, not_7_out);
  and and_6 (mr1, not_8_out, in_8);
  Multiplexer #(.width(9)) multiplexer_4 (
    .in0(multiplexer_1_out), .in1(subtractor_1_out), .out(er_t), .sel(or_1_out));  // open: en
  or or_1 (or_1_out, and_4_out, sub_norm);
  Comparator #(.mode("unsigned"), .width(9)) comparator_1 (.a(in_3), .b(9'h2), .lt(ex_ey_2));  // open: gt, eq
  Comparator #(.mode("unsigned"), .width(9)) comparator_2 (.a(er_t), .b(9'h7f), .gt(comparator_2_gt));  // open: eq, lt
  Comparator #(.mode("unsigned"), .width(9)) comparator_3 (.a(er_t), .b(9'h100), .lt(comparator_3_lt));  // open: gt, eq
  Adder #(.width(9)) adder_2 (.a(er_t), .b(9'h7f), .out(Er));  // open: cin, cout
  not not_9 (not_9_out, in_7);
  and and_7 (out_16, comparator_2_gt, comparator_3_lt);
  and and_8 (er3, not_9_out, in_8);
  not not_10 (not_10_out, in_7);
  and and_9 (out_13, not_10_out, in_8);
  and and_10 (out_12, in_7, not_11_out);
  not not_11 (not_11_out, in_9);
  Multiplexer #(.width(24)) multiplexer_5 (
    .in0(Mrout_1), .in1({Mrout_1[23:1], in_4}), .out(out_10), .sel(out_12));  // open: en

  assign out_14 = in_2[0];

  // Other names for the same wires on the sheet: go = in_4; _24 = in_9; _25 = in_8; ex[8:0] = in_1; ex_ey[8:0] = in_3;
  //   LSB = in_2[0]; Mr[23:0] = in_2; mr_2 = out_12; mr_2_t = out_13; Mrout[23:0] = out_10; OF = out_16; Sz = in_7

  // Notes on the sheet:
  //   inputs
  //   bit 24 high then norm
  //   if bit 24 low then sub
  //   adding 2 subn getting norm / sub
  //   ex
  //   ex+1
  //   ex-1
  //   mr
  //   mr/2
  //   control for mr
  //   choose the correct er value
  //   (ex or ex+1)
  //   choose correct mr value
  //   mr or mr/2
  //   test for near far choice
  //   test for overflow
  //   (ex or ex+1)
  //   ex-1
  //   add 127 for unbiased
  //   control for er
  //   outputs
  //   rounding
  //   addition ripple , mr/2 guard bit is lsb
  //   if sub cancellation then mr*2 LSB = gaurd bit
  //   subtraction cancellation , mr*2 guard bit is msb of shift
endmodule

module CONCATENATE (
  input  in_1,
  input  [8:0] in_2,
  input  [23:0] in_3,
  output [31:0] X___Y
);

  Bit_Extender #(.in_width(9), .out_width(8), .\type ("zero")) bit_extender_1 (.in(in_2), .out(X___Y[30:23]));
  // Probe on in_3[22:0]

  assign {X___Y[31], X___Y[22:0]} = {in_1, in_3[22:0]};

  // Other names for the same wires on the sheet: Er[8:0] = in_2; Mr[23:0] = in_3; Mrout[22:0] = in_3[22:0];
  //   X__Y[31:0] = {in_1, X___Y[30:23], in_3[22:0]}; Ero[7:0] = X___Y[30:23]; Sr = in_1

  // Notes on the sheet:
  //   inputs
  //   unbiased exponent 8 bits
  //   mantissa remove hidden bit
  //   concatenate
  //   leading 1 not required
  //   outputs
endmodule

module PATH (
  input  [31:0] NEAR,
  input  [31:0] FAR,
  input  N___F,
  output [31:0] out_4
);

  Multiplexer #(.width(32)) multiplexer_1 (.in0(NEAR), .in1(FAR), .out(out_4), .sel(N___F));  // open: en

  // Notes on the sheet:
  //   inputs
  //   choose near of far path result
  //   outputs
endmodule

module SIGN (
  input  inputs,
  input  in_2,
  output out_3
);

  wire not_1_out;

  not not_1 (not_1_out, inputs);
  Multiplexer multiplexer_1 (.in0(inputs), .in1(not_1_out), .out(out_3), .sel(in_2));  // open: en

  // Other names for the same wires on the sheet: Mrns = in_2; Srn = out_3; Sx = inputs

  // Notes on the sheet:
  //   sign for near path
  //   outputs
endmodule

module _1_BT_SHIFT (
  input  [23:0] in_1,
  input  [8:0] in_2,
  output [23:0] out_3
);

  wire comparator_1_eq;
  wire [4:0] bit_extender_1_out;
  wire [23:0] shifter_1_out;

  Comparator #(.width(9)) comparator_1 (.a(in_2), .b(9'h1), .eq(comparator_1_eq));  // open: gt, lt
  assign bit_extender_1_out = {{4{1'b0}}, comparator_1_eq};  // Bit_Extender bit_extender_1
  Shifter #(.shift("lr"), .width(24)) shifter_1 (.in(in_1), .\dist (bit_extender_1_out), .out(shifter_1_out));
  Multiplexer #(.width(24)) multiplexer_1 (
    .in0(in_1), .in1(shifter_1_out), .out(out_3), .sel(comparator_1_eq));  // open: en

  // Other names for the same wires on the sheet: ex_ey[8:0] = in_2; my[23:0] = in_1; my_out[23:0] = out_3

  // Notes on the sheet:
  //   inputs
  //   1 bit shift
  //   outputs
endmodule

module mx_my (
  input  [23:0] in_1,
  input  [23:0] in_2,
  input  [8:0] in_3,
  output [23:0] out_4,
  output out_5
);

  wire comparator_2_eq, not_1_out;
  wire [23:0] multiplexer_1_out, multiplexer_2_out, mx_my, not_2_out, smallest;

  Comparator #(.mode("unsigned"), .width(24)) comparator_1 (.a(in_2), .b(in_1), .lt(out_5));  // open: gt, eq
  Comparator #(.width(9)) comparator_2 (.a(in_3), .b(9'h1), .eq(comparator_2_eq));  // open: gt, lt
  Multiplexer #(.width(24)) multiplexer_1 (.in0(in_2), .in1(in_1), .out(multiplexer_1_out), .sel(out_5));  // open: en
  not not_1 (not_1_out, out_5);
  assign not_2_out = ~smallest;  // NOT_Gate not_2, 24 bits wide
  Multiplexer #(.width(24)) multiplexer_2 (
    .in0(24'h1), .in1({24{1'b0}}), .out(multiplexer_2_out), .sel(comparator_2_eq));  // open: en
  Multiplexer #(.width(24)) multiplexer_3 (.in0(in_2), .in1(in_1), .out(smallest), .sel(not_1_out));  // open: en
  Adder #(.width(24)) adder_1 (.a(not_2_out), .b(multiplexer_2_out), .out(mx_my));  // open: cin, cout
  Adder #(.width(24)) adder_2 (.a(multiplexer_1_out), .b(mx_my), .out(out_4));  // open: cin, cout

  // Other names for the same wires on the sheet: ex_ey[8:0] = in_3; mr_out[23:0] = out_4; Mrns = out_5;
  //   mx[23:0] = in_2; my[23:0] = in_1

  // Notes on the sheet:
  //   inputs
  //   add
  //   find smallest mantissa value mx or my
  //   swap y/n
  //   2's complement smallest value
  //   outputs
endmodule

module LZC_SHIFT (
  input  [23:0] in_1,
  input  [8:0] in_2,
  input  in_3,
  input  in_4,
  input  in_5,
  input  in_6,
  input  [8:0] in_7,
  output [4:0] out_8,
  output [23:0] out_9
);

  wire [4:0] bit_extender_1_out, bitfinder_1_index;
  wire [23:0] shifter_1_out, shifter_2_out;

  BitFinder #(.\type ("high1"), .width(24)) bitfinder_1 (.in(in_1), .index(bitfinder_1_index));  // open: found
  // Probe on bitfinder_1_index
  Bit_Extender #(.in_width(9), .out_width(5), .\type ("zero")) bit_extender_1 (.in(in_7), .out(bit_extender_1_out));
  Subtractor #(.width(5)) subtractor_1 (.a(5'b10111), .b(bitfinder_1_index), .out(out_8));  // open: bin, bout
  Shifter #(.width(24)) shifter_1 (.in(in_1), .\dist (out_8), .out(shifter_1_out));
  Shifter #(.width(24)) shifter_2 (.in(in_1), .\dist (bit_extender_1_out), .out(shifter_2_out));
  Multiplexer #(.width(24)) multiplexer_1 (
    .in0(shifter_1_out), .in1(shifter_2_out), .out(out_9), .sel(in_6));  // open: en

  // Other names for the same wires on the sheet: ex[8:0] = in_2; ex_emin[8:0] = in_7; LZC[4:0] = out_8;
  //   mr[23:0] = in_1; Mrout[23:0] = out_9; nx = in_3; ny = in_4; s = in_6; Sz = in_5

  // Notes on the sheet:
  //   inputs
  //   LZC
  //   normal result
  //   mr.2^LZC
  //   subnormal result
  //   mr.2^ex-emin
  //   For a normal result the mantissa is shifted left by the LZC.
  //   For a subnormal result the matissa is shifted left by ex-emin
  //   is the result subnormal
  //   outputs
endmodule

module SUB (
  input  [8:0] in_1,
  input  [4:0] in_2,
  input  [8:0] in_3,
  input  in_4,
  output [8:0] Er,
  output [8:0] ex_emin
);

  wire [8:0] adder_2_out, adder_3_out, bit_extender_1_out, subtractor_1_out, subtractor_2_out;

  assign bit_extender_1_out = {{4{1'b0}}, in_2};  // Bit_Extender bit_extender_1
  Adder #(.width(9)) adder_1 (.a(in_1), .b(9'h7e), .out(ex_emin));  // open: cin, cout
  Subtractor #(.width(9)) subtractor_1 (.a(in_1), .b(bit_extender_1_out), .out(subtractor_1_out));  // open: bin, bout
  Subtractor #(.width(9)) subtractor_2 (.a(in_1), .b(ex_emin), .out(subtractor_2_out));  // open: bin, bout
  Adder #(.width(9)) adder_2 (.a(subtractor_1_out), .b(9'h7f), .out(adder_2_out));  // open: cin, cout
  Adder #(.width(9)) adder_3 (.a(subtractor_2_out), .b(9'h7e), .out(adder_3_out));  // open: cin, cout
  Multiplexer #(.width(9)) multiplexer_1 (.in0(adder_2_out), .in1(adder_3_out), .out(Er), .sel(in_4));  // open: en

  // Other names for the same wires on the sheet: ex[8:0] = in_1; ey[8:0] = in_3; LZC[4:0] = in_2; sn = in_4

  // Notes on the sheet:
  //   inputs
  //   ex-emin
  //   (ex- (-126)) = ex+126
  //   subtraction of two subnormal inputs giving a subnormal result
  //   The near path covers subtraction resulting in cancellation when result is normal and
  //   normal result (cancellation)
  //   ex-LZC
  //   subnormal result (sub - sub)
  //   ex-(ex-emin)=emin
  //   add 127 to unbias
  //   add 126 to unbias
  //   ex-LZC
  //   emin
  //   ex-LZC or emin
  //   is result subnormal
  //   output unbiased exponent
endmodule

module STICKY (
  input  [22:0] _1_gaurd_bit,
  output NE,
  output out_3
);

  or or_1 (NE, _1_gaurd_bit[22], out_3);
  or or_2 (out_3, _1_gaurd_bit[21], _1_gaurd_bit[20], _1_gaurd_bit[19], _1_gaurd_bit[18], _1_gaurd_bit[17], _1_gaurd_bit[16], _1_gaurd_bit[15], _1_gaurd_bit[14], _1_gaurd_bit[13], _1_gaurd_bit[12], _1_gaurd_bit[11], _1_gaurd_bit[10], _1_gaurd_bit[9], _1_gaurd_bit[8], _1_gaurd_bit[7], _1_gaurd_bit[6], _1_gaurd_bit[5], _1_gaurd_bit[4], _1_gaurd_bit[3], _1_gaurd_bit[2], _1_gaurd_bit[1], _1_gaurd_bit[0]);

  // Notes on the sheet:
  //   input
  //   not exact
  //   22 bits of sticky bit
  //   sticky
  //   if any of these 23 bits goes high then we will have a not exact output
  //   outputs
endmodule

// GF
module ROUND (
  input  in_1,
  input  in_2,
  input  in_3,
  input  [31:0] x_____y_in,
  output [31:0] x_____y_out
);

  wire and_1_out, and_2_out, and_3_out, round;
  wire [30:0] bit_extender_1_out;

  and and_1 (and_1_out, round, in_3);
  and and_2 (and_2_out, in_2, in_1);
  and and_3 (and_3_out, x_____y_in[0], in_2);
  assign bit_extender_1_out = {{30{1'b0}}, and_1_out};  // Bit_Extender bit_extender_1
  or or_1 (round, and_2_out, and_3_out);
  Adder #(.width(31)) adder_1 (
    .a(x_____y_in[30:0]), .b(bit_extender_1_out), .out(x_____y_out[30:0]));  // open: cin, cout

  assign x_____y_out[31] = x_____y_in[31];

  // Other names for the same wires on the sheet: G = in_2; N_F = in_3; R = in_1; LSBM = x_____y_in[0]

  // Notes on the sheet:
  //   inputs
  //   lsbm
  //   inject / overflow
  //   only pass on rounding bit if far path
  //   rounding logic
  //   tie
  //   tie
  //   nearest even rounding truth table
  //   lsbm   g    r    o
  //   0    0    0    0
  //   0    0    1    0
  //   0    1    0    0
  //   0    1    1    1
  //   1    0    0    0
  //   1    0    1    0
  //   1    1    0    1
  //   1    1    1    1
  //   outputs
endmodule

module SPECIAL_CASES (
  input  [31:0] X,
  input  [31:0] Y,
  input  in_3,
  input  in_4,
  input  in_5,
  input  [31:0] X___Y,
  input  in_7,
  input  in_8,
  input  in_9,
  input  in_10,
  input  in_11,
  input  in_12,
  input  in_13,
  input  [8:0] in_14,
  input  [8:0] in_15,
  input  in_16,
  output out_17,
  output out_18,
  output out_19,
  output out_20,
  output out_21,
  output out_22,
  output out_23,
  output out_24,
  output out_25,
  output out_26,
  output out_27,
  output out_28,
  output [31:0] X_______Y_O
);

  wire NNN, NNS, NSN, NSS, special_cases_comparators_1_out_3, special_cases_comparators_1_out_4,
       special_cases_comparators_1_out_5, special_cases_comparators_1_out_6,
       special_cases_comparators_1_out_7, special_cases_comparators_1_out_8,
       special_cases_comparators_1_out_9, special_cases_comparators_1_out_10,
       special_cases_comparators_1_out_11, special_cases_comparators_1_out_12,
       special_cases_comparators_1_out_13, special_cases_comparators_1_out_14,
       special_cases_comparators_1_out_15, special_cases_comparators_1_out_16,
       special_cases_comparators_1_out_17, special_cases_comparators_1_out_18,
       special_cases_comparators_1_out_19, special_cases_comparators_1_out_20,
       special_cases_test_addition_1_out_24, special_cases_test_addition_1_out_25,
       special_cases_test_addition_1_out_26, special_cases_test_addition_1_out_27,
       special_cases_test_addition_1_out_28, special_cases_test_addition_1_out_29,
       special_cases_test_addition_1_out_30, special_cases_test_addition_1_out_31,
       special_cases_test_addition_1_out_32, special_cases_test_addition_1_out_33, SSN, SSS;

  SPECIAL_CASES_COMPARATORS special_cases_comparators_1 (
    .out_5(special_cases_comparators_1_out_5), .out_8(special_cases_comparators_1_out_8),
    .out_13(special_cases_comparators_1_out_13), .out_18(special_cases_comparators_1_out_18),
    .out_3(special_cases_comparators_1_out_3), .out_6(special_cases_comparators_1_out_6),
    .out_9(special_cases_comparators_1_out_9), .out_11(special_cases_comparators_1_out_11),
    .out_14(special_cases_comparators_1_out_14), .out_17(special_cases_comparators_1_out_17),
    .out_19(special_cases_comparators_1_out_19), .out_4(special_cases_comparators_1_out_4),
    .out_7(special_cases_comparators_1_out_7), .out_10(special_cases_comparators_1_out_10),
    .out_12(special_cases_comparators_1_out_12), .out_15(special_cases_comparators_1_out_15),
    .out_16(special_cases_comparators_1_out_16), .out_20(special_cases_comparators_1_out_20), .X(X), .Y(Y));
  SPECIAL_CASES_TEST_ADDITION special_cases_test_addition_1 (
    .out_24(special_cases_test_addition_1_out_24), .out_25(special_cases_test_addition_1_out_25),
    .out_31(special_cases_test_addition_1_out_31), .out_32(special_cases_test_addition_1_out_32),
    .out_33(special_cases_test_addition_1_out_33), .out_34(out_17),
    .out_26(special_cases_test_addition_1_out_26), .out_27(special_cases_test_addition_1_out_27),
    .out_28(special_cases_test_addition_1_out_28), .out_29(special_cases_test_addition_1_out_29),
    .out_30(special_cases_test_addition_1_out_30), .in_13(in_3), .in_20(special_cases_comparators_1_out_13),
    .in_21(special_cases_comparators_1_out_18), .in_22(in_12), .in_23(in_13),
    .in_4(special_cases_comparators_1_out_4), .in_5(special_cases_comparators_1_out_6),
    .in_6(special_cases_comparators_1_out_7), .in_7(special_cases_comparators_1_out_14),
    .in_8(special_cases_comparators_1_out_15), .in_1(in_4), .in_9(special_cases_comparators_1_out_9),
    .in_10(special_cases_comparators_1_out_10), .in_11(special_cases_comparators_1_out_11),
    .in_12(special_cases_comparators_1_out_12), .in_2(in_5), .in_14(special_cases_comparators_1_out_17),
    .in_15(special_cases_comparators_1_out_19), .in_16(special_cases_comparators_1_out_16),
    .in_17(special_cases_comparators_1_out_20), .in_18(special_cases_comparators_1_out_5),
    .in_19(special_cases_comparators_1_out_8), .in_3(special_cases_comparators_1_out_3));
  OUTPUT_TYPE output_type_1 (
    .NNN(NNN), .NNS(NNS), .SSN(SSN), .SSS(SSS), .NSN(NSN), .NSS(NSS), .in_1(in_7), .in_5(in_9), .in_7(in_11),
    .in_2(in_8), .in_6(in_10), .in_8(in_3), .Ey(in_15), .Ex(in_14));
  SPECIAL_CASES_MULTIPLEX special_cases_multiplex_1 (
    .X___Y_O(X_______Y_O), .overflow___inf_2(out_27), .not_exact(out_28), .NNN(out_18), .NNS(out_19),
    .NSN(out_20), .NSS(out_21), .SSN(out_22), .SSS(out_23), .pluus_zero(out_24), .minus_zero(out_25),
    .overflow___inf(out_26), .in_13(special_cases_test_addition_1_out_26),
    .in_14(special_cases_test_addition_1_out_27), .in_15(special_cases_test_addition_1_out_32),
    .in_16(special_cases_test_addition_1_out_29), .in_17(out_17),
    .in_18(special_cases_test_addition_1_out_28), .in_19(special_cases_test_addition_1_out_30),
    .in_20(special_cases_test_addition_1_out_31), .in_21(special_cases_test_addition_1_out_33),
    .in_3(special_cases_test_addition_1_out_25), .in_4(NNN), .in_5(NNS), .in_6(NSN), .in_7(NSS), .in_9(SSN),
    .in_10(SSS), .in_12(in_16), .in_1(special_cases_test_addition_1_out_24), .X(X), .Y(Y), .X___Y_B(X___Y));

  // Other names for the same wires on the sheet: Ex[8:0] = in_14; Ey[8:0] = in_15; NaN = out_17; ne = in_16;
  //   nf = in_8; nn = in_7; nof = in_11; of = in_12; sf = in_10; sn = in_9; Sx = in_4; Sxo = in_13; Sy = in_5;
  //   tunnel = in_3; X___Y_B[31:0] = X___Y

  // Notes on the sheet:
  //   inputs
  //   comparators
  //   test circuits
  //   number types
  //   multiplex circuits
  //   outputs
endmodule

module SPECIAL_CASES_COMPARATORS (
  input  [31:0] X,
  input  [31:0] Y,
  output out_3,
  output out_4,
  output out_5,
  output out_6,
  output out_7,
  output out_8,
  output out_9,
  output out_10,
  output out_11,
  output out_12,
  output out_13,
  output out_14,
  output out_15,
  output out_16,
  output out_17,
  output out_18,
  output out_19,
  output out_20
);

  wire and_1_out, and_2_out, and_3_out, and_4_out, and_5_out, and_6_out, comparator_11_eq, comparator_12_eq,
       comparator_13_eq, comparator_14_eq, not_1_out, not_2_out, not_3_out, not_4_out;

  Comparator #(.mode("unsigned"), .width(32)) comparator_1 (.a(X), .b(32'h7f800000), .eq(out_3));  // open: gt, lt
  Comparator #(.mode("unsigned"), .width(32)) comparator_2 (.a(X), .b(32'hff800000), .eq(out_6));  // open: gt, lt
  Comparator #(.mode("unsigned"), .width(32)) comparator_3 (.a(X), .b({32{1'b0}}), .eq(out_9));  // open: gt, lt
  Comparator #(.mode("unsigned"), .width(32)) comparator_4 (.a(X), .b(32'h80000000), .eq(out_11));  // open: gt, lt
  Comparator #(.mode("unsigned"), .width(32)) comparator_5 (.a(X), .b(32'h7fc00000), .eq(out_14));  // open: gt, lt
  nor nor_1 (out_17, out_3, out_9, X[31], out_14);
  nor nor_2 (out_19, out_4, out_10, Y[31], out_15);
  Comparator #(.mode("unsigned"), .width(32)) comparator_6 (.a(Y), .b(32'h7f800000), .eq(out_4));  // open: gt, lt
  Comparator #(.mode("unsigned"), .width(32)) comparator_7 (.a(Y), .b(32'hff800000), .eq(out_7));  // open: gt, lt
  Comparator #(.mode("unsigned"), .width(32)) comparator_8 (.a(Y), .b({32{1'b0}}), .eq(out_10));  // open: gt, lt
  Comparator #(.mode("unsigned"), .width(32)) comparator_9 (.a(Y), .b(32'h80000000), .eq(out_12));  // open: gt, lt
  Comparator #(.mode("unsigned"), .width(32)) comparator_10 (.a(Y), .b(32'h7fc00000), .eq(out_15));  // open: gt, lt
  not not_1 (not_1_out, X[31]);
  not not_2 (not_2_out, Y[31]);
  nor nor_3 (out_16, out_6, out_11, not_1_out, out_14);
  nor nor_4 (out_20, out_7, out_12, not_2_out, out_15);
  and and_1 (and_1_out, out_17, out_19);
  Comparator #(.mode("unsigned"), .width(32)) comparator_11 (.a(X), .b(Y), .eq(comparator_11_eq));  // open: gt, lt
  and and_2 (and_2_out, out_16, out_20);
  Comparator #(.mode("unsigned"), .width(32)) comparator_12 (.a(X), .b(Y), .eq(comparator_12_eq));  // open: gt, lt
  Comparator #(.mode("unsigned"), .width(31)) comparator_13 (
    .a(X[30:0]), .b(Y[30:0]), .eq(comparator_13_eq));  // open: gt, lt
  not not_3 (not_3_out, X[31]);
  and and_3 (and_3_out, not_3_out, Y[31]);
  and and_4 (and_4_out, out_17, out_20);
  Comparator #(.mode("unsigned"), .width(31)) comparator_14 (
    .a(X[30:0]), .b(Y[30:0]), .eq(comparator_14_eq));  // open: gt, lt
  and and_5 (and_5_out, X[31], not_4_out);
  not not_4 (not_4_out, Y[31]);
  and and_6 (and_6_out, out_16, out_19);
  and and_7 (out_5, and_1_out, comparator_11_eq);
  and and_8 (out_8, and_2_out, comparator_12_eq);
  and and_9 (out_13, comparator_13_eq, and_3_out, and_4_out);
  and and_10 (out_18, comparator_14_eq, and_5_out, and_6_out);

  // Other names for the same wires on the sheet: minus_inf_x = out_6; minus_inf_y = out_7; minus_X = out_16;
  //   minus_Y = out_20; minus_zero_y = out_12; minuszero_x = out_11; NaNx = out_14; NaNy = out_15; plus_inf_x = out_3;
  //   plus_inf_y = out_4; Plus_X = out_17; Plus_Y = out_19; plus_zero_x = out_9; plus_zero_y = out_10;
  //   X31[30:0] = X[30:0]; Sx = X[31]; X__Y_minus = out_13; X__Y_plus = out_18; X_Y_minus = out_8; X_Y_plus = out_5;
  //   Y31[30:0] = Y[30:0]; Sy = Y[31]

  // Notes on the sheet:
  //   inputs
  //   plus zero x
  //   minus zero x
  //   plus infinity x
  //   minus infinity x
  //   NaN x
  //   comparators
  //   plus infinity y
  //   minus infinity y
  //   plus zero y
  //   minus zero y
  //   NaN y
  //   2 positives equal
  //   2 negatives equal
  //   X positive and  Y negative equal
  //   X negative and  Y positive equal
endmodule

module SPECIAL_CASES_TEST_ADDITION (
  input  in_1,
  input  in_2,
  input  in_3,
  input  in_4,
  input  in_5,
  input  in_6,
  input  in_7,
  input  in_8,
  input  in_9,
  input  in_10,
  input  in_11,
  input  in_12,
  input  in_13,
  input  in_14,
  input  in_15,
  input  in_16,
  input  in_17,
  input  in_18,
  input  in_19,
  input  in_20,
  input  in_21,
  input  in_22,
  input  in_23,
  output out_24,
  output out_25,
  output out_26,
  output out_27,
  output out_28,
  output out_29,
  output out_30,
  output out_31,
  output out_32,
  output out_33,
  output out_34
);

  wire and_1_out, and_2_out, and_3_out, and_4_out, and_5_out, and_6_out, and_7_out, and_8_out, and_9_out,
       and_10_out, and_11_out, and_12_out, and_13_out, and_14_out, and_15_out, and_16_out, and_17_out,
       and_18_out, and_19_out, and_20_out, and_21_out, and_22_out, and_23_out, and_24_out, and_25_out,
       and_26_out, and_27_out, and_28_out, and_29_out, and_30_out, and_31_out, and_32_out, and_33_out,
       and_34_out, and_35_out, and_36_out, and_37_out, and_38_out, and_39_out, and_40_out, and_41_out,
       and_42_out, and_43_out, and_44_out, and_45_out, and_46_out, and_47_out, and_48_out, and_49_out,
       and_50_out, and_51_out, and_52_out, and_53_out, and_54_out, and_55_out, and_56_out, and_57_out,
       and_58_out, and_59_out, and_60_out, NaN, not_1_out, not_2_out, not_3_out, or_2_out, or_3_out,
       or_4_out, or_5_out, or_6_out, or_7_out, or_8_out, or_9_out, or_12_out, or_13_out, or_14_out,
       or_15_out, or_16_out, or_17_out;

  or or_1 (NaN, in_7, in_8);
  and and_1 (and_1_out, in_3, in_4);
  and and_2 (and_2_out, in_3, in_10);
  and and_3 (and_3_out, in_3, in_12);
  and and_4 (and_4_out, in_3, in_15);
  and and_5 (and_5_out, in_3, in_17);
  and and_6 (and_6_out, in_9, in_4);
  and and_7 (and_7_out, in_11, in_4);
  and and_8 (and_8_out, in_14, in_4);
  and and_9 (and_9_out, in_16, in_4);
  and and_10 (and_10_out, in_3, in_6);
  and and_11 (and_11_out, in_3, in_10);
  and and_12 (and_12_out, in_3, in_12);
  and and_13 (and_13_out, in_3, in_15);
  and and_14 (and_14_out, in_3, in_17);
  and and_15 (and_15_out, in_9, in_6);
  and and_16 (and_16_out, in_11, in_6);
  and and_17 (and_17_out, in_14, in_6);
  and and_18 (and_18_out, in_16, in_6);
  and and_19 (and_19_out, in_3, in_6);
  and and_20 (and_20_out, in_5, in_4);
  and and_21 (and_21_out, in_3, in_4);
  and and_22 (and_22_out, in_5, in_6);
  or or_2 (or_2_out, and_1_out, and_2_out, and_3_out, and_4_out, and_5_out, and_6_out, and_7_out, and_8_out, and_9_out);
  or or_3 (or_3_out, and_10_out, and_11_out, and_12_out, and_13_out, and_14_out, and_15_out, and_16_out, and_17_out, and_18_out);
  or or_4 (or_4_out, and_19_out, and_20_out, NaN);
  or or_5 (or_5_out, and_21_out, and_22_out, NaN);
  Multiplexer multiplexer_1 (.in0(or_2_out), .in1(or_3_out), .out(out_26), .sel(in_13));  // open: en
  Multiplexer multiplexer_2 (.in0(or_4_out), .in1(or_5_out), .out(out_34), .sel(in_13));  // open: en
  and and_23 (and_23_out, in_5, in_6);
  and and_24 (and_24_out, in_5, in_10);
  and and_25 (and_25_out, in_5, in_12);
  and and_26 (and_26_out, in_5, in_15);
  and and_27 (and_27_out, in_5, in_17);
  and and_28 (and_28_out, in_9, in_6);
  and and_29 (and_29_out, in_11, in_6);
  and and_30 (and_30_out, in_14, in_6);
  and and_31 (and_31_out, in_16, in_6);
  and and_32 (and_32_out, in_5, in_4);
  and and_33 (and_33_out, in_5, in_10);
  and and_34 (and_34_out, in_5, in_12);
  and and_35 (and_35_out, in_5, in_15);
  and and_36 (and_36_out, in_5, in_17);
  and and_37 (and_37_out, in_9, in_4);
  and and_38 (and_38_out, in_11, in_4);
  and and_39 (and_39_out, in_14, in_4);
  and and_40 (and_40_out, in_16, in_4);
  and and_41 (and_41_out, in_11, in_12);
  and and_42 (and_42_out, in_11, in_10);
  or or_6 (or_6_out, and_42_out, in_19);
  or or_7 (or_7_out, and_23_out, and_24_out, and_25_out, and_26_out, and_27_out, and_28_out, and_29_out, and_30_out, and_31_out);
  or or_8 (or_8_out, and_32_out, and_33_out, and_34_out, and_35_out, and_36_out, and_37_out, and_38_out, and_39_out, and_40_out);
  or or_9 (or_9_out, and_41_out, in_21);
  Multiplexer multiplexer_3 (.in0(or_9_out), .in1(or_6_out), .out(out_29), .sel(in_13));  // open: en
  Multiplexer multiplexer_4 (.in0(or_7_out), .in1(or_8_out), .out(out_27), .sel(in_13));  // open: en
  and and_43 (and_43_out, in_16, in_10);
  and and_44 (and_44_out, in_16, in_12);
  and and_45 (and_45_out, in_14, in_10);
  and and_46 (and_46_out, in_14, in_12);
  and and_47 (and_47_out, in_9, in_10);
  and and_48 (and_48_out, in_9, in_12);
  and and_49 (and_49_out, in_11, in_10);
  and and_50 (and_50_out, in_9, in_10);
  and and_51 (and_51_out, in_9, in_12);
  and and_52 (and_52_out, in_11, in_12);
  and and_53 (and_53_out, in_9, in_17);
  and and_54 (and_54_out, in_11, in_17);
  and and_55 (and_55_out, in_9, in_15);
  and and_56 (and_56_out, in_11, in_15);
  or or_10 (out_28, and_45_out, and_46_out);
  or or_11 (out_30, and_43_out, and_44_out);
  or or_12 (or_12_out, and_47_out, and_48_out, and_49_out, in_20);
  or or_13 (or_13_out, and_53_out, and_54_out);
  or or_14 (or_14_out, and_55_out, and_56_out);
  or or_15 (or_15_out, and_50_out, and_51_out, and_52_out, in_18);
  Multiplexer multiplexer_5 (.in0(or_12_out), .in1(or_15_out), .out(out_32), .sel(in_13));  // open: en
  Multiplexer multiplexer_6 (.in0(or_13_out), .in1(or_14_out), .out(out_33), .sel(in_13));  // open: en
  not not_1 (not_1_out, in_23);
  not not_2 (not_2_out, out_34);
  and and_57 (and_57_out, in_9, in_15);
  and and_58 (and_58_out, in_11, in_15);
  and and_59 (and_59_out, in_9, in_17);
  and and_60 (and_60_out, in_11, in_17);
  and and_61 (out_24, not_1_out, not_2_out, in_22);
  or or_16 (or_16_out, and_57_out, and_58_out);
  or or_17 (or_17_out, and_59_out, and_60_out);
  not not_3 (not_3_out, out_34);
  Multiplexer multiplexer_7 (.in0(or_16_out), .in1(or_17_out), .out(out_31), .sel(in_13));  // open: en
  and and_62 (out_25, in_23, not_3_out, in_22);

  // Other names for the same wires on the sheet: minus_inf_out = out_27; minus_inf_x = in_5; minus_inf_y = in_6;
  //   minus_X = in_16; minus_X_out = out_30; minus_Y = in_17; minus_Y_out = out_33; minus_zero_out = out_29;
  //   minus_zero_x = in_11; minus_zero_y = in_12; NaN_out = out_34; NaNx = in_7; NaNy = in_8; o_minus = out_25;
  //   o_plus = out_24; of = in_22; plus_inf_out = out_26; plus_inf_x = in_3; plus_inf_y = in_4; plus_X = in_14;
  //   plus_X_out = out_28; plus_Y = in_15; plus_Y_out = out_31; plus_zero_out = out_32; plus_zero_x = in_9;
  //   plus_zero_y = in_10; Sx = in_1; Sxo = in_23; Sy = in_2; tunnel = in_13; x_y_minus = in_20; x_y_minus_t = in_19;
  //   x_y_plus = in_21; x_y_plus_t = in_18

  // Notes on the sheet:
  //   plus infinity addition
  //   plus infinity subtraction
  //   NaN addition 
  //   NaN subtraction
  //   add
  //   subtract
  //   NaN
  //   plus infinity
  //   (-x)-(-x)
  //   minus infinity addition
  //   minus infinity subtraction
  //   minus zero addition
  //   minus zero subtraction
  //   add
  //   minus infinity
  //   subtract
  //   minus zero
  //   (+x)-(+x)
  //   plus x addition and subtraction
  //   minus x addition and subtraction
  //   plus zero addition
  //   plus zero subtraction
  //   minus y addition
  //   minus y subtraction
  //   plus x
  //   minus x
  //   plus zero
  //   minus y
  //   overflow + inf
  //   plus y addition
  //   plus y subtraction
  //   overflow
  //   Only get an overflow if the NaN result is zero
  //   overflow - inf
  //   plus y
endmodule

module SPECIAL_CASES_MULTIPLEX (
  input  in_1,
  input  [31:0] X___Y_B,
  input  in_3,
  input  in_4,
  input  in_5,
  input  in_6,
  input  in_7,
  input  [31:0] X,
  input  in_9,
  input  in_10,
  input  [31:0] Y,
  input  in_12,
  input  in_13,
  input  in_14,
  input  in_15,
  input  in_16,
  input  in_17,
  input  in_18,
  input  in_19,
  input  in_20,
  input  in_21,
  output [31:0] X___Y_O,
  output pluus_zero,
  output minus_zero,
  output overflow___inf,
  output overflow___inf_2,
  output not_exact,
  output NNN,
  output NNS,
  output NSN,
  output NSS,
  output SSN,
  output SSS
);

  wire and_1_out, nor_1_out, nor_2_out, or_1_out, or_2_out, or_3_out, or_4_out, or_5_out, or_6_out;
  wire [2:0] priority_encoder_1_out;
  wire [31:31] multiplexer_1_out, multiplexer_2_out;

  nor nor_1 (nor_1_out, in_13, in_14, in_18, in_16, in_19, in_20, in_15, in_21, in_17, in_1, in_3);
  or or_1 (or_1_out, in_21, in_19, in_18, in_20);
  or or_2 (or_2_out, or_1_out, nor_1_out);
  Multiplexer multiplexer_1 (.in0(1'b0), .in1(1'b1), .out(multiplexer_1_out[31]), .sel(in_19));  // open: en
  Multiplexer multiplexer_2 (.in0(1'b0), .in1(1'b1), .out(multiplexer_2_out[31]), .sel(in_21));  // open: en
  and and_1 (and_1_out, or_2_out, in_12);
  and and_2 (NNN, or_2_out, in_4);
  and and_3 (NNS, or_2_out, in_5);
  and and_4 (NSN, or_2_out, in_6);
  and and_5 (NSS, or_2_out, in_7);
  and and_6 (SSN, or_2_out, in_9);
  and and_7 (SSS, or_2_out, in_10);
  nor nor_2 (nor_2_out, in_1, in_3);
  or or_3 (or_3_out, in_13, in_1);
  or or_4 (or_4_out, in_14, in_3);
  or or_5 (or_5_out, in_18, in_19);
  or or_6 (or_6_out, in_20, in_21);
  or or_7 (overflow___inf, in_13, in_1);
  or or_8 (overflow___inf_2, in_14, in_3);
  and and_8 (not_exact, and_1_out, nor_2_out);
  Multiplexer #(.select(3), .width(32)) multiplexer_3 (
    .in0(X___Y_B), .in1(32'h7f800000), .in2(32'hff800000), .in3({32{1'b0}}), .in4(32'h80000000),
    .in5(32'h7fc00000), .in6({multiplexer_1_out[31], X[30:0]}), .in7({multiplexer_2_out[31], Y[30:0]}),
    .out(X___Y_O), .sel(priority_encoder_1_out));  // open: en
  Priority_Encoder priority_encoder_1 (
    .in0(nor_1_out), .in1(or_3_out), .in2(or_4_out), .in3(in_15), .in4(in_16), .in5(in_17), .in6(or_5_out),
    .in7(or_6_out), .out(priority_encoder_1_out));  // open: en_in, gs, en_out

  assign minus_zero = in_16;
  assign pluus_zero = in_15;

  // Other names for the same wires on the sheet: minus_inf = in_14; minus_X = in_19; minus_Y = in_21; NaN = in_17;
  //   ne = in_12; NNN_t = in_4; NNS_t = in_5; NSN_t = in_6; NSS_t = in_7; o_minus = in_3; o_plus = in_1;
  //   plus_inf = in_13; Plus_X = in_18; plus_Y = in_20; plus_zero = in_15; SSN_t = in_9; SSS_t = in_10

  // Notes on the sheet:
  //   inputs
  //   plus infinity
  //   minus infinity
  //   plus zero
  //   minus zero
  //   NaN
  //   multiplex
  //   outputs
endmodule

module TYPE (
  input  [8:0] in_1,
  input  in_2,
  input  [8:0] in_3,
  input  [4:0] in_4,
  output out_5,
  output out_6,
  output out_7,
  output out_8
);

  wire and_3_out, and_4_out, and_5_out, and_6_out, comparator_1_gt, comparator_2_lt, comparator_3_gt,
       comparator_4_lt, comparator_5_eq, comparator_5_gt, comparator_6_lt, comparator_7_gt, comparator_8_eq,
       comparator_8_lt, comparator_9_eq, comparator_9_gt, comparator_10_lt, comparator_11_gt,
       comparator_12_eq, comparator_12_lt, or_1_out, or_2_out, or_4_out, or_5_out;
  wire [8:0] bit_extender_1_out, er_t, ex_LZC_9bit;

  Subtractor #(.width(9)) subtractor_1 (.a(in_1), .b(9'h7f), .out(er_t));  // open: bin, bout
  // Probe on ex_LZC_9bit
  Comparator #(.mode("unsigned"), .width(9)) comparator_1 (
    .a(ex_LZC_9bit), .b(9'h16a), .gt(comparator_1_gt));  // open: eq, lt
  Comparator #(.mode("unsigned"), .width(9)) comparator_2 (
    .a(ex_LZC_9bit), .b(9'h182), .lt(comparator_2_lt));  // open: gt, eq
  Subtractor #(.width(9)) subtractor_2 (.a(in_3), .b(bit_extender_1_out), .out(ex_LZC_9bit));  // open: bin, bout
  assign bit_extender_1_out = {{4{1'b0}}, in_4};  // Bit_Extender bit_extender_1
  and and_1 (out_8, comparator_1_gt, comparator_2_lt);
  Comparator #(.mode("unsigned"), .width(9)) comparator_3 (.a(er_t), .b(9'h16a), .gt(comparator_3_gt));  // open: eq, lt
  Comparator #(.mode("unsigned"), .width(9)) comparator_4 (.a(er_t), .b(9'h182), .lt(comparator_4_lt));  // open: gt, eq
  and and_2 (out_6, comparator_3_gt, comparator_4_lt);
  Comparator #(.mode("unsigned"), .width(9)) comparator_5 (
    .a(ex_LZC_9bit), .b({9{1'b0}}), .gt(comparator_5_gt), .eq(comparator_5_eq));  // open: lt
  Comparator #(.mode("unsigned"), .width(9)) comparator_6 (
    .a(ex_LZC_9bit), .b(9'h80), .lt(comparator_6_lt));  // open: gt, eq
  Comparator #(.mode("unsigned"), .width(9)) comparator_7 (
    .a(ex_LZC_9bit), .b(9'h181), .gt(comparator_7_gt));  // open: eq, lt
  Comparator #(.mode("unsigned"), .width(9)) comparator_8 (
    .a(ex_LZC_9bit), .b({9{1'b1}}), .eq(comparator_8_eq), .lt(comparator_8_lt));  // open: gt
  or or_1 (or_1_out, comparator_8_eq, comparator_8_lt);
  or or_2 (or_2_out, comparator_5_gt, comparator_5_eq);
  and and_3 (and_3_out, comparator_7_gt, or_1_out);
  and and_4 (and_4_out, or_2_out, comparator_6_lt);
  Comparator #(.mode("unsigned"), .width(9)) comparator_9 (
    .a(er_t), .b({9{1'b0}}), .gt(comparator_9_gt), .eq(comparator_9_eq));  // open: lt
  Comparator #(.mode("unsigned"), .width(9)) comparator_10 (
    .a(er_t), .b(9'h80), .lt(comparator_10_lt));  // open: gt, eq
  Comparator #(.mode("unsigned"), .width(9)) comparator_11 (
    .a(er_t), .b(9'h181), .gt(comparator_11_gt));  // open: eq, lt
  Comparator #(.mode("unsigned"), .width(9)) comparator_12 (
    .a(er_t), .b({9{1'b1}}), .eq(comparator_12_eq), .lt(comparator_12_lt));  // open: gt
  or or_3 (out_5, and_4_out, and_3_out);
  or or_4 (or_4_out, comparator_9_gt, comparator_9_eq);
  or or_5 (or_5_out, comparator_12_eq, comparator_12_lt);
  and and_5 (and_5_out, comparator_11_gt, or_5_out);
  and and_6 (and_6_out, or_4_out, comparator_10_lt);
  or or_6 (out_7, and_6_out, and_5_out);

  // Other names for the same wires on the sheet: Er[8:0] = in_1; ex[8:0] = in_3; LZC[4:0] = in_4; normal_f = out_7;
  //   normal_n = out_5; Srn = in_2; subnormal_f = out_6; subnormal_n = out_8

  // Notes on the sheet:
  //   inputs
  //   result type
  //   result subnormal
  //   outputs
  //   result type
  //   NEAR SIDE ONLY
  //   FAR SIDE ONLY
  //   result subnormal
  //   see biased exponent sheet
  //   in excel tool for all test values
  //   result normal
  //   result normal
  //   result normal
  //   result normal
endmodule

module OUTPUT_TYPE (
  input  in_1,
  input  in_2,
  input  [8:0] Ex,
  input  [8:0] Ey,
  input  in_5,
  input  in_6,
  input  in_7,
  input  in_8,
  output NNN,
  output NNS,
  output NSN,
  output NSS,
  output SSN,
  output SSS
);

  wire and_3_out, and_4_out, and_5_out, and_6_out, norm, not_1_out, not_2_out, not_3_out, not_4_out,
       not_5_out, not_6_out, not_7_out, not_8_out, not_9_out, not_10_out, not_11_out, not_12_out, sub, Xn, Yn;

  or or_1 (Xn, Ex[7], Ex[6], Ex[5], Ex[4], Ex[3], Ex[2], Ex[1], Ex[0]);
  Multiplexer multiplexer_1 (.in0(in_1), .in1(in_2), .out(norm), .sel(in_7));  // open: en
  Multiplexer multiplexer_2 (.in0(in_5), .in1(in_6), .out(sub), .sel(in_7));  // open: en
  or or_2 (Yn, Ey[7], Ey[6], Ey[5], Ey[4], Ey[3], Ey[2], Ey[1], Ey[0]);
  and and_1 (NNN, Xn, Yn, norm);
  and and_2 (NNS, Xn, Yn, not_1_out);
  not not_1 (not_1_out, norm);
  not not_2 (not_2_out, Yn);
  and and_3 (and_3_out, Xn, not_2_out, norm);
  not not_3 (not_3_out, Xn);
  and and_4 (and_4_out, Yn, not_3_out, norm);
  not not_4 (not_4_out, Yn);
  and and_5 (and_5_out, Xn, not_4_out, not_5_out);
  not not_5 (not_5_out, norm);
  not not_6 (not_6_out, Xn);
  and and_6 (and_6_out, Yn, not_6_out, not_7_out);
  not not_7 (not_7_out, norm);
  not not_8 (not_8_out, Xn);
  not not_9 (not_9_out, Yn);
  and and_7 (SSN, not_8_out, not_9_out, norm);
  not not_10 (not_10_out, Xn);
  not not_11 (not_11_out, Yn);
  and and_8 (SSS, not_10_out, not_11_out, not_12_out);
  not not_12 (not_12_out, norm);
  or or_3 (NSN, and_3_out, and_4_out);
  or or_4 (NSS, and_5_out, and_6_out);

  // Other names for the same wires on the sheet: nf = in_2; nn = in_1; nof = in_7; sf = in_6; sn = in_5;
  //   tunnel = in_8

  // Notes on the sheet:
  //   test for normal or subnormal inputs
  //   normal = 1 
  //   subnormal =0
  //   test for normal or subnormal outputs
  //   n
  //   n
  //   n
  //   n
  //   n
  //   n
  //   n
  //   s
  //   n
  //   n
  //   s
  //   n
  //   n
  //   s
  //   s
  //   n
  //   s
  //   s
  //   s
  //   s
  //   n
  //   s
  //   s
  //   s
  //   test number types
  //   inputs
endmodule

module N_F_TEST (
  input  in_1,
  input  in_2,
  input  in_3,
  input  in_4,
  output out_5
);

  wire and_1_out, and_3_out;

  not not_1 (out_5, and_1_out);
  and and_1 (and_1_out, in_2, in_1);
  // AND_Gate and_2 has open pins: in1=and_3_out, out=open
  and and_3 (and_3_out, in_3, in_4);

  // Other names for the same wires on the sheet: ex_ey_2 = in_2; nx = in_3; ny = in_4; Sz = in_1

  // Notes on the sheet:
  //   test for subtraction
  //   near side for subtraction and ex-ey<2
  //   unless we have 2 subnormal inputs
  //   so for sub - sub we use the far side
endmodule
