// Logisim project FULL FPU.circ as structural Verilog
module FISR (
  input  [31:0] x,
  output [31:0] out_2
);

  wire comparator_1_eq, comparator_1_lt, comparator_2_eq, comparator_2_lt, comparator_3_eq, comparator_3_lt,
       comparator_4_eq, comparator_4_lt, comparator_5_eq, comparator_5_lt, comparator_6_eq, comparator_6_lt,
       comparator_7_eq, comparator_7_lt, comparator_8_eq, comparator_8_lt, comparator_9_eq, comparator_9_lt,
       or_1_out, or_2_out, or_3_out, or_4_out, or_5_out, or_6_out, or_7_out, or_8_out, or_9_out;
  wire [3:0] priority_encoder_1_out;
  wire [4:0] bit_extender_2_out;
  wire [23:0] bit_extender_1_out, shifter_1_out;
  wire [31:0] multiplexer_1_out, shifter_2_out;

  assign bit_extender_1_out = {{1{1'b0}}, x[22:0]};  // Bit_Extender bit_extender_1
  Shifter #(.width(24)) shifter_1 (.in(bit_extender_1_out), .\dist (5'b00001), .out(shifter_1_out));
  // Probe on shifter_1_out
  Comparator #(.mode("unsigned"), .width(24)) comparator_1 (
    .a(shifter_1_out), .b(24'he66666), .eq(comparator_1_eq), .lt(comparator_1_lt));  // open: gt
  or or_1 (or_1_out, comparator_1_eq, comparator_1_lt);
  Comparator #(.mode("unsigned"), .width(24)) comparator_2 (
    .a(shifter_1_out), .b(24'hcccccc), .eq(comparator_2_eq), .lt(comparator_2_lt));  // open: gt
  or or_2 (or_2_out, comparator_2_eq, comparator_2_lt);
  Comparator #(.mode("unsigned"), .width(24)) comparator_3 (
    .a(shifter_1_out), .b(24'hb33333), .eq(comparator_3_eq), .lt(comparator_3_lt));  // open: gt
  or or_3 (or_3_out, comparator_3_eq, comparator_3_lt);
  Comparator #(.mode("unsigned"), .width(24)) comparator_4 (
    .a(shifter_1_out), .b(24'h999999), .eq(comparator_4_eq), .lt(comparator_4_lt));  // open: gt
  or or_4 (or_4_out, comparator_4_eq, comparator_4_lt);
  Comparator #(.mode("unsigned"), .width(24)) comparator_5 (
    .a(shifter_1_out), .b(24'h800000), .eq(comparator_5_eq), .lt(comparator_5_lt));  // open: gt
  or or_5 (or_5_out, comparator_5_eq, comparator_5_lt);
  Comparator #(.mode("unsigned"), .width(24)) comparator_6 (
    .a(shifter_1_out), .b(24'h666666), .eq(comparator_6_eq), .lt(comparator_6_lt));  // open: gt
  or or_6 (or_6_out, comparator_6_eq, comparator_6_lt);
  Comparator #(.mode("unsigned"), .width(24)) comparator_7 (
    .a(shifter_1_out), .b(24'h4ccccd), .eq(comparator_7_eq), .lt(comparator_7_lt));  // open: gt
  or or_7 (or_7_out, comparator_7_eq, comparator_7_lt);
  Comparator #(.mode("unsigned"), .width(24)) comparator_8 (
    .a(shifter_1_out), .b(24'h333332), .eq(comparator_8_eq), .lt(comparator_8_lt));  // open: gt
  or or_8 (or_8_out, comparator_8_eq, comparator_8_lt);
  Comparator #(.mode("unsigned"), .width(24)) comparator_9 (
    .a(shifter_1_out), .b(24'h199998), .eq(comparator_9_eq), .lt(comparator_9_lt));  // open: gt
  or or_9 (or_9_out, comparator_9_eq, comparator_9_lt);
  // Probe on nothing
  // Probe on priority_encoder_1_out
  Priority_Encoder #(.select(4)) priority_encoder_1 (
    .in0(1'b1), .in1(or_1_out), .in2(or_2_out), .in3(or_3_out), .in4(or_4_out), .in5(or_5_out),
    .in6(or_6_out), .in7(or_7_out), .in8(or_8_out), .in9(or_9_out), .out(priority_encoder_1_out));  // open: in10, in11, in12, in13, in14, in15, gs, en_out, en_in
  // Probe on 32'h5f3d7247
  assign bit_extender_2_out = {{1{1'b0}}, 4'b0001};  // Bit_Extender bit_extender_2
  Multiplexer #(.enable("false"), .select(4), .width(32)) multiplexer_1 (
    .in0(32'h5f3d7247), .in1(32'h5f38d6a1), .in2(32'h5f350481), .in3(32'h5f322339), .in4(32'h5f304189),
    .in5(32'h5f2f86c2), .in6(32'h5f30240b), .in7(32'h5f3245a1), .in8(32'h5f362b6a), .in9(32'h5f3c32ca),
    .out(multiplexer_1_out), .sel(priority_encoder_1_out));  // open: in10, in11, in12, in13, in14, in15
  Shifter #(.shift("lr"), .width(32)) shifter_2 (.in(x), .\dist (bit_extender_2_out), .out(shifter_2_out));
  // Probe on multiplexer_1_out
  // Probe on shifter_2_out
  Subtractor #(.width(32)) subtractor_1 (.a(multiplexer_1_out), .b(shifter_2_out), .out(out_2));  // open: bin, bout

  // Other names for the same wires on the sheet: Mx[22:0] = x[22:0]; Ex[7:0] = x[30:23]; Sx = x[31]

  // Notes on the sheet:
  //   input
  //   magic numbers
  //   3 x 2^22 x (B - (alpha)
  //   split
  //   comparators
  //   magic number
  //   Ix/2
  //   magic number - Ix/2
endmodule

module FISR_AND_NR (
  input  [31:0] X,
  output [31:0] Out,
  output NaN,
  output plus_inf,
  output minus_inf,
  output zero
);

  wire [31:0] fisr_1_out_2;

  FISR fisr_1 (.out_2(fisr_1_out_2), .x(X));
  NR nr_1 (.zero(zero), .Out(Out), .NaN(NaN), .plus_inf(plus_inf), .minus_inf(minus_inf), .Y1(fisr_1_out_2), .X(X));
endmodule

module FPAS (
  input  [31:0] X,
  input  [31:0] Y,
  input  in_3,
  output NaN,
  output plus_inf,
  output minus_inf,
  output zero,
  output [31:0] X_____Y
);

  wire add_subtract_1_out_14, add_subtract_1_out_15;

  ADD_SUBTRACT add_subtract_1 (
    .out_7(NaN), .out_9(plus_inf), .out_11(minus_inf), .X_______Y(X_____Y), .out_14(add_subtract_1_out_14),
    .out_15(add_subtract_1_out_15), .in_3(in_3), .X(X), .Y(Y));  // open: out_8, out_10, out_12, out_4, out_13, out_5, out_6
  or or_1 (zero, add_subtract_1_out_14, add_subtract_1_out_15);
endmodule

module FPM (
  input  [31:0] X,
  input  [31:0] Y,
  output NaN,
  output [31:0] X_Y,
  output zero,
  output minus_inf,
  output plus_inf
);

  wire fpm_multiplier_nnn_1_minus_0u, fpm_multiplier_nnn_1_plus_0u;

  FPM_MULTIPLIER_NNN fpm_multiplier_nnn_1 (
    .minus_0U(fpm_multiplier_nnn_1_minus_0u), .plus_iO(plus_inf), .minus_iO(minus_inf),
    .plus_0U(fpm_multiplier_nnn_1_plus_0u), .NaN(NaN), .X_Y(X_Y), .X(X), .Y(Y));  // open: NNS, NSN, NSS, NNN, not_exact
  or or_1 (zero, fpm_multiplier_nnn_1_minus_0u, fpm_multiplier_nnn_1_plus_0u);
endmodule

module FPDIV (
  input  [31:0] X,
  input  [31:0] Y,
  output [31:0] X_Y,
  output NaN,
  output plus_inf,
  output minus_inf,
  output zero
);

  wire minus_inf1, minus_inf2, minus_inf3, NaN1, NaN2, NaN3, plus_inf1, plus_inf2, plus_inf3, zero1, zero2,
       zero3;
  wire [31:0] fisr_and_nr_1_out, fpm_1_x_y;

  // Probe on X
  FISR_AND_NR fisr_and_nr_1 (
    .Out(fisr_and_nr_1_out), .NaN(NaN1), .plus_inf(plus_inf1), .minus_inf(minus_inf1), .zero(zero1), .X(Y));
  or or_1 (NaN, NaN1, NaN2, NaN3);
  or or_2 (plus_inf, plus_inf1, plus_inf2, plus_inf3);
  FPM fpm_1 (
    .X_Y(fpm_1_x_y), .NaN(NaN2), .zero(zero2), .minus_inf(minus_inf2), .plus_inf(plus_inf2), .X(X),
    .Y(fisr_and_nr_1_out));
  // Probe on fpm_1_x_y
  or or_3 (minus_inf, minus_inf1, minus_inf2, minus_inf3);
  FPM fpm_2 (
    .X_Y(X_Y), .NaN(NaN3), .zero(zero3), .minus_inf(minus_inf3), .plus_inf(plus_inf3), .X(fpm_1_x_y),
    .Y(fisr_and_nr_1_out));
  // Probe on X_Y
  or or_4 (zero, zero1, zero2, zero3);
endmodule

module NR (
  input  [31:0] Y1,
  input  [31:0] X,
  output [31:0] Out,
  output NaN,
  output plus_inf,
  output minus_inf,
  output zero
);

  wire minus_inf1, minus_inf2, minus_inf3, minus_inf4, minus_inf5, NaN1, NaN2, NaN3, NaN4, NaN5, plus_inf1,
       plus_inf2, plus_inf3, plus_inf4, plus_inf5, zero1, zero2, zero3, zero4, zero5;
  wire [31:0] fpas_1_x_____y, fpm_1_x_y, fpm_2_x_y, fpm_3_x_y;

  or or_1 (NaN, NaN1, NaN2, NaN3, NaN4, NaN5);
  FPM fpm_1 (.X_Y(fpm_1_x_y), .NaN(NaN1), .zero(zero1), .minus_inf(minus_inf1), .plus_inf(plus_inf1), .X(Y1), .Y(Y1));
  // Probe on fpm_1_x_y
  or or_2 (plus_inf, plus_inf1, plus_inf2, plus_inf3, plus_inf4, plus_inf5);
  FPM fpm_2 (
    .X_Y(fpm_2_x_y), .NaN(NaN2), .zero(zero2), .minus_inf(minus_inf2), .plus_inf(plus_inf2), .X(fpm_1_x_y),
    .Y(X));
  // Probe on fpm_2_x_y
  or or_3 (minus_inf, minus_inf1, minus_inf2, minus_inf3, minus_inf4, minus_inf5);
  FPM fpm_3 (
    .X_Y(fpm_3_x_y), .NaN(NaN3), .zero(zero3), .minus_inf(minus_inf3), .plus_inf(plus_inf3), .X(fpm_2_x_y),
    .Y(32'h3f000000));
  // Probe on fpm_3_x_y
  or or_4 (zero, zero1, zero2, zero3, zero4, zero5);
  FPAS fpas_1 (
    .X_____Y(fpas_1_x_____y), .NaN(NaN4), .plus_inf(plus_inf4), .minus_inf(minus_inf4), .zero(zero4),
    .X(32'h3fc00000), .in_3(1'b1), .Y(fpm_3_x_y));
  // Probe on Y1
  FPM fpm_4 (
    .X_Y(Out), .NaN(NaN5), .zero(zero5), .minus_inf(minus_inf5), .plus_inf(plus_inf5), .X(Y1),
    .Y(fpas_1_x_____y));
  // Probe on Out

  // Notes on the sheet:
  //   xi
  //   xi^2
  //   yxi^2
  //   0.5yxi^2
  //   1.5-0.5yxi^2
  //   yi(1.5-0.5yxi^2)
endmodule

module DIVIDE_TEST (
);

  wire clk, fpdiv_1_minus_inf, fpdiv_1_nan, fpdiv_1_plus_inf, fpdiv_1_zero;
  wire [7:0] A;
  wire [31:0] X, X_Y, Y;

  RAM #(.dataWidth(32)) ram_1 (.addr(A), .clk(clk), .dout(X));  // open: we, din
  // Probe on X
  RAM #(.dataWidth(32)) ram_2 (.addr(A), .we(1'b1), .clk(clk), .din(X_Y));  // open: dout
  Clock clock_1 (.out(clk));
  Counter #(.ongoal("stay")) counter_1 (.count(1'b1), .Q(A), .clk(clk));  // open: load, D, carry, clr
  // Probe on X_Y
  RAM #(.dataWidth(32)) ram_3 (.addr(A), .clk(clk), .dout(Y));  // open: we, din
  FPDIV fpdiv_1 (
    .zero(fpdiv_1_zero), .X_Y(X_Y), .NaN(fpdiv_1_nan), .plus_inf(fpdiv_1_plus_inf),
    .minus_inf(fpdiv_1_minus_inf), .X(X), .Y(Y));
  LED led_1 (.in(fpdiv_1_nan));
  LED led_2 (.in(fpdiv_1_plus_inf));
  LED led_3 (.in(fpdiv_1_minus_inf));
  LED led_4 (.in(fpdiv_1_zero));
  // Probe on Y

  // Notes on the sheet:
  //   input X
  //   output X/Y
  //   input Y
endmodule

module FPSQRT (
  input  [31:0] X,
  output [31:0] X_Y,
  output NaN,
  output plus_inf,
  output minus_inf,
  output zero
);

  wire minus_inf1, minus_inf2, NaN1, NaN2, plus_inf1, plus_inf2, zero1, zero2;
  wire [31:0] fisr_and_nr_1_out;

  or or_1 (NaN, NaN1, NaN2, X[31]);
  FISR_AND_NR fisr_and_nr_1 (
    .Out(fisr_and_nr_1_out), .NaN(NaN1), .plus_inf(plus_inf1), .minus_inf(minus_inf1), .zero(zero1), .X(X));
  or or_2 (plus_inf, plus_inf1, plus_inf2);
  FPM fpm_1 (
    .X_Y(X_Y), .NaN(NaN2), .zero(zero2), .minus_inf(minus_inf2), .plus_inf(plus_inf2), .X(X),
    .Y(fisr_and_nr_1_out));
  or or_3 (minus_inf, minus_inf1, minus_inf2);
  // Probe on X_Y
  or or_4 (zero, zero1, zero2);

  // Other names for the same wires on the sheet: NaN3 = X[31]

  // Notes on the sheet:
  //   test for negative input
endmodule

module SQUARE_ROOT_TEST (
);

  wire clk, fpsqrt_1_minus_inf, fpsqrt_1_nan, fpsqrt_1_plus_inf, fpsqrt_1_zero;
  wire [7:0] A;
  wire [31:0] X, X_Y_out;

  Clock clock_1 (.out(clk));
  Counter #(.ongoal("stay")) counter_1 (.count(1'b1), .Q(A), .clk(clk));  // open: load, D, carry, clr
  RAM #(.dataWidth(32)) ram_1 (.addr(A), .clk(clk), .dout(X));  // open: we, din
  RAM #(.dataWidth(32)) ram_2 (.addr(A), .we(1'b1), .clk(clk), .din(X_Y_out));  // open: dout
  // Probe on X_Y_out
  // Probe on X
  FPSQRT fpsqrt_1 (
    .NaN(fpsqrt_1_nan), .plus_inf(fpsqrt_1_plus_inf), .minus_inf(fpsqrt_1_minus_inf), .X_Y(X_Y_out),
    .zero(fpsqrt_1_zero), .X(X));
  LED led_1 (.in(fpsqrt_1_nan));
  LED led_2 (.in(fpsqrt_1_plus_inf));
  LED led_3 (.in(fpsqrt_1_minus_inf));
  LED led_4 (.in(fpsqrt_1_zero));

  // Notes on the sheet:
  //   input X
  //   output X.Y
endmodule

module FPU (
  input  [31:0] X,
  input  [31:0] Y,
  input  [2:0] Select,
  output [31:0] OUT,
  output NaN,
  output plus_inf,
  output minus_inf,
  output zero
);

  wire add, div, minus_inf1, minus_inf2, minus_inf3, minus_inf4, mult, NaN1, NaN2, NaN3, NaN4, not_1_out,
       nul, or_1_out, plus_inf1, plus_inf2, plus_inf3, plus_inf4, sqrt, sub, zero1, zero2, zero3, zero4;
  wire [31:0] SQRTX, X__Y, X_Y, X_Y_t;

  FPM fpm_1 (.X_Y(X_Y), .NaN(NaN1), .zero(zero1), .minus_inf(minus_inf1), .plus_inf(plus_inf1), .X(X), .Y(Y));
  FPSQRT fpsqrt_1 (.NaN(NaN3), .plus_inf(plus_inf3), .minus_inf(minus_inf3), .X_Y(SQRTX), .zero(zero3), .X(X));
  _3X8_DECODER u_3x8_decoder_1 (
    ._0(nul), ._1(mult), ._2(add), ._3(sub), ._4(div), ._5(sqrt), .c(Select[0]), .a(Select[2]), .b(Select[1]));  // open: _6, _7
  not not_1 (not_1_out, add);
  FPDIV fpdiv_1 (.zero(zero4), .X_Y(X_Y_t), .NaN(NaN4), .plus_inf(plus_inf4), .minus_inf(minus_inf4), .X(X), .Y(Y));
  FPAS fpas_1 (
    .X_____Y(X__Y), .NaN(NaN2), .plus_inf(plus_inf2), .minus_inf(minus_inf2), .zero(zero2), .X(X),
    .in_3(not_1_out), .Y(Y));
  assign NaN = mult ? NaN1 : 1'bz;  // Controlled_Buffer controlled_buffer_1
  assign plus_inf = mult ? plus_inf1 : 1'bz;  // Controlled_Buffer controlled_buffer_2
  assign minus_inf = mult ? minus_inf1 : 1'bz;  // Controlled_Buffer controlled_buffer_3
  assign zero = mult ? zero1 : 1'bz;  // Controlled_Buffer controlled_buffer_4
  assign NaN = or_1_out ? NaN2 : 1'bz;  // Controlled_Buffer controlled_buffer_5
  assign plus_inf = or_1_out ? plus_inf2 : 1'bz;  // Controlled_Buffer controlled_buffer_6
  assign minus_inf = or_1_out ? minus_inf2 : 1'bz;  // Controlled_Buffer controlled_buffer_7
  assign zero = or_1_out ? zero2 : 1'bz;  // Controlled_Buffer controlled_buffer_8
  or or_1 (or_1_out, add, sub);
  Multiplexer #(.enable("false"), .select(3), .width(32)) multiplexer_1 (
    .in0({32{1'b0}}), .in1(X_Y), .in2(X__Y), .in3(X__Y), .in4(X_Y_t), .in5(SQRTX), .in6({32{1'b0}}),
    .in7({32{1'b0}}), .out(OUT), .sel(Select));
  assign NaN = sqrt ? NaN3 : 1'bz;  // Controlled_Buffer controlled_buffer_9
  assign plus_inf = sqrt ? plus_inf3 : 1'bz;  // Controlled_Buffer controlled_buffer_10
  assign minus_inf = sqrt ? minus_inf3 : 1'bz;  // Controlled_Buffer controlled_buffer_11
  assign zero = sqrt ? zero3 : 1'bz;  // Controlled_Buffer controlled_buffer_12
  assign NaN = div ? NaN4 : 1'bz;  // Controlled_Buffer controlled_buffer_13
  assign plus_inf = div ? plus_inf4 : 1'bz;  // Controlled_Buffer controlled_buffer_14
  assign minus_inf = div ? minus_inf4 : 1'bz;  // Controlled_Buffer controlled_buffer_15
  assign zero = div ? zero4 : 1'bz;  // Controlled_Buffer controlled_buffer_16
  assign NaN = nul ? 1'b0 : 1'bz;  // Controlled_Buffer controlled_buffer_17
  assign plus_inf = nul ? 1'b0 : 1'bz;  // Controlled_Buffer controlled_buffer_18
  assign minus_inf = nul ? 1'b0 : 1'bz;  // Controlled_Buffer controlled_buffer_19
  assign zero = nul ? 1'b0 : 1'bz;  // Controlled_Buffer controlled_buffer_20

  // Other names for the same wires on the sheet: Sel[2:0] = Select

  // Notes on the sheet:
  //   4 DIV
  //   1 MULT
  //   2 ADD
  //   3 SUB
  //   5 SQRT
endmodule

module _3X8_DECODER (
  input  a,
  input  b,
  input  c,
  output _0,
  output _1,
  output _2,
  output _3,
  output _4,
  output _5,
  output _6,
  output _7
);

  wire not_1_out, not_2_out, not_3_out;

  not not_1 (not_1_out, c);
  not not_2 (not_2_out, b);
  not not_3 (not_3_out, a);
  and and_1 (_0, not_3_out, not_2_out, not_1_out);
  and and_2 (_1, not_3_out, not_2_out, c);
  and and_3 (_2, not_3_out, b, not_1_out);
  and and_4 (_3, not_3_out, b, c);
  and and_5 (_4, a, not_2_out, not_1_out);
  and and_6 (_5, a, not_2_out, c);
  and and_7 (_6, a, b, not_1_out);
  and and_8 (_7, a, b, c);
endmodule

module FPU_TEST (
  input  [2:0] Select1
);

  wire clk, fpu_1_minus_inf, fpu_1_nan, fpu_1_plus_inf, fpu_1_zero;
  wire [7:0] A;
  wire [31:0] out, X, Y;

  RAM #(.dataWidth(32)) ram_1 (.addr(A), .clk(clk), .dout(X));  // open: we, din
  // Probe on X
  RAM #(.dataWidth(32)) ram_2 (.addr(A), .we(1'b1), .clk(clk), .din(out));  // open: dout
  Clock clock_1 (.out(clk));
  Counter #(.ongoal("stay")) counter_1 (.count(1'b1), .Q(A), .clk(clk));  // open: load, D, carry, clr
  // Probe on out
  RAM #(.dataWidth(32)) ram_3 (.addr(A), .clk(clk), .dout(Y));  // open: we, din
  FPU fpu_1 (
    .NaN(fpu_1_nan), .plus_inf(fpu_1_plus_inf), .minus_inf(fpu_1_minus_inf), .zero(fpu_1_zero), .OUT(out),
    .Y(Y), .Select(Select1), .X(X));
  LED led_1 (.in(fpu_1_nan));
  LED led_2 (.in(fpu_1_plus_inf));
  LED led_3 (.in(fpu_1_minus_inf));
  LED led_4 (.in(fpu_1_zero));
  // Probe on Y

  // Notes on the sheet:
  //   1 MULT
  //   2 ADD
  //   3 SUB
  //   4 DIV
  //   5 SQRT
  //   input X
  //   output
  //   input Y
endmodule
