// Logisim project MULTIPLIER LOGISIM EVOLUTION.circ as structural Verilog
module main (
  input  lsbm,
  input  g,
  input  r,
  output o
);

  wire and_1_out, and_2_out;

  and and_1 (and_1_out, g, r);
  and and_2 (and_2_out, lsbm, g);
  or or_1 (o, and_1_out, and_2_out);
endmodule

module tmp (
  input  [31:0] Y,
  input  [31:0] X,
  input  inf,
  input  inf_2,
  input  zero,
  input  [31:0] X_Y,
  input  zero_2,
  input  NaN,
  input  [31:0] X_2,
  input  [31:0] Y_2,
  output [31:0] X_Y_2,
  output [31:0] \output 
);

  wire not_1_out, pass, priority_encoder_1_p1;
  wire [4:0] bit_extender_4_out;
  wire [7:0] adder_1_out, adder_2_out, adder_3_out, subtractor_1_out, subtractor_2_out;
  wire [22:0] bit_extender_3_out, bit_extender_5_out;
  wire [23:0] bit_extender_1_out, bit_extender_2_out, multiplier_1_cout, multiplier_1_out, shifter_1_out;

  // Probe on Y
  // Probe on X
  // Probe on Y[30:23]
  // Probe on X[30:23]
  assign bit_extender_1_out = {{1{1'b1}}, Y[22:0]};  // Bit_Extender bit_extender_1
  assign bit_extender_2_out = {{1{1'b1}}, X[22:0]};  // Bit_Extender bit_extender_2
  // Probe on subtractor_1_out
  Subtractor subtractor_1 (.a(Y[30:23]), .b(8'h7f), .out(subtractor_1_out));  // open: bin, bout
  // Probe on subtractor_2_out
  Subtractor subtractor_2 (.a(X[30:23]), .b(8'h7f), .out(subtractor_2_out));  // open: bin, bout
  Multiplier #(.width(24)) multiplier_1 (
    .a(bit_extender_1_out), .b(bit_extender_2_out), .out(multiplier_1_out), .cout(multiplier_1_cout));  // open: cin
  xor xor_1 (X_Y_2[31], Y[31], X[31]);
  // Probe on adder_1_out
  Adder adder_1 (.a(subtractor_1_out), .b(subtractor_2_out), .out(adder_1_out));  // open: cin, cout
  Bit_Extender #(.in_width(24), .out_width(23)) bit_extender_3 (.in(multiplier_1_cout), .out(bit_extender_3_out));
  assign bit_extender_4_out = {{4{multiplier_1_cout[23]}}, multiplier_1_cout[23]};  // Bit_Extender bit_extender_4
  // Probe on bit_extender_4_out
  // Probe on adder_2_out
  Adder adder_2 (.a(8'h7f), .b(adder_1_out), .out(adder_2_out));  // open: cin, cout
  Adder adder_3 (.a(adder_1_out), .b(8'h80), .out(adder_3_out));  // open: cin, cout
  // Probe on adder_3_out
  Shifter #(.width(24)) shifter_1 (.in(multiplier_1_cout), .\dist (bit_extender_4_out), .out(shifter_1_out));
  Multiplexer #(.width(8)) multiplexer_1 (
    .in0(adder_2_out), .in1(adder_3_out), .out(X_Y_2[30:23]), .sel(multiplier_1_cout[23]));  // open: en
  Bit_Extender #(.in_width(24), .out_width(23)) bit_extender_5 (.in(shifter_1_out), .out(bit_extender_5_out));
  // Probe on X_Y_2[30:23]
  Multiplexer #(.width(23)) multiplexer_2 (
    .in0(bit_extender_3_out), .in1(bit_extender_5_out), .out(X_Y_2[22:0]), .sel(not_1_out));  // open: en
  not not_1 (not_1_out, multiplier_1_cout[23]);
  // Probe on X_Y_2
  // Probe on X_2
  nor nor_1 (pass, inf, NaN);
  // Probe on Y_2
  Multiplexer #(.select(3), .width(32)) multiplexer_3 (
    .in0(X_Y), .in1(32'h7f800000), .in2(32'hff800000), .in3({32{1'b0}}), .in4(32'h8000000),
    .in5(32'h7fffffff), .out(\output ), .en(priority_encoder_1_p1));  // open: in6, in7, sel
  // Priority_Encoder #(.select(4)) priority_encoder_1: pin names not known; wires that end beside it: priority_encoder_1_p1, pass, inf, inf_2, zero, zero_2, NaN

  // Other names for the same wires on the sheet: minus_inf = inf_2; plus_inf = inf; zero_t = zero_2

  // Notes on the sheet:
  //   -0.7
  //   492.75
  //   492.75
  //   NaN
  //   - zero
  //   + zero
  //   - infinity
  //   +infinity
  //   -0.7
endmodule

module FPM_INPUT_X (
  input  [31:0] X,
  output Sx,
  output [22:0] Mx,
  output [8:0] Ex
);

  assign Ex = {{1{1'b0}}, X[30:23]};  // Bit_Extender bit_extender_1

  assign Mx = X[22:0];
  assign Sx = X[31];
endmodule

module FPM_INPUT_Y (
  input  [31:0] Y,
  output Sy,
  output [22:0] My,
  output [8:0] Ey
);

  assign Ey = {{1{1'b0}}, Y[30:23]};  // Bit_Extender bit_extender_1

  assign My = Y[22:0];
  assign Sy = Y[31];
endmodule

module FPM_Ex_ex (
  input  Xn,
  input  [4:0] pre_lzc,
  input  [8:0] Ex,
  input  [8:0] b,
  output [8:0] ex_2
);

  wire [8:0] adder_1_out, bit_extender_1_out, subtractor_1_out, subtractor_2_out;

  assign bit_extender_1_out = {{4{1'b0}}, pre_lzc};  // Bit_Extender bit_extender_1
  Adder #(.width(9)) adder_1 (.a(9'h7e), .b(bit_extender_1_out), .out(adder_1_out));  // open: cin, cout
  // Probe on adder_1_out
  // Probe on Ex
  // Probe on b
  Subtractor #(.width(9)) subtractor_1 (.a({9{1'b0}}), .b(adder_1_out), .out(subtractor_1_out));  // open: bin, bout
  // Probe on subtractor_1_out
  Subtractor #(.width(9)) subtractor_2 (.a(Ex), .b(b), .out(subtractor_2_out));  // open: bin, bout
  // Probe on subtractor_2_out
  Multiplexer #(.width(9)) multiplexer_1 (
    .in0(subtractor_1_out), .in1(subtractor_2_out), .out(ex_2), .sel(Xn));  // open: en
  // Probe on ex_2

  // Notes on the sheet:
  //   choose ex = Ex-127 or ex = -126 -pre_lzc
endmodule

module FPM_Ey_ey (
  input  Yn,
  input  [4:0] pre_lzc,
  input  [8:0] Ey,
  input  [8:0] b,
  output [8:0] ey_2
);

  wire [8:0] adder_1_out, bit_extender_1_out, subtractor_1_out, subtractor_2_out;

  // Probe on bit_extender_1_out
  assign bit_extender_1_out = {{4{1'b0}}, pre_lzc};  // Bit_Extender bit_extender_1
  // Probe on 9'h7e
  // Probe on adder_1_out
  Adder #(.width(9)) adder_1 (.a(9'h7e), .b(bit_extender_1_out), .out(adder_1_out));  // open: cin, cout
  Subtractor #(.width(9)) subtractor_1 (.a({9{1'b0}}), .b(adder_1_out), .out(subtractor_1_out));  // open: bin, bout
  // Probe on subtractor_1_out
  // Probe on subtractor_1_out
  Subtractor #(.width(9)) subtractor_2 (.a(Ey), .b(b), .out(subtractor_2_out));  // open: bin, bout
  Multiplexer #(.width(9)) multiplexer_1 (
    .in0(subtractor_1_out), .in1(subtractor_2_out), .out(ey_2), .sel(Yn));  // open: en

  // Notes on the sheet:
  //   choose ey = Ey-127 or ey = -126 -pre_lzc
endmodule

module FPU_ADDER (
  input  [8:0] _1,
  input  [8:0] _2,
  output [8:0] _1_2,
  output UP,
  output OP
);

  wire and_1_out, and_2_out, comparator_1_gt, comparator_2_gt, comparator_3_lt, comparator_4_lt,
       comparator_5_lt, comparator_6_gt;

  // Probe on _1
  // Probe on _2
  // Probe on _1
  // Probe on _2
  // Probe on _1_2
  Adder #(.width(9)) adder_1 (.a(_1), .b(_2), .out(_1_2));  // open: cin, cout
  Comparator #(.mode("unsigned"), .width(9)) comparator_1 (.a(_1), .b(9'hff), .gt(comparator_1_gt));  // open: eq, lt
  Comparator #(.mode("unsigned"), .width(9)) comparator_2 (.a(_2), .b(9'hff), .gt(comparator_2_gt));  // open: eq, lt
  Comparator #(.mode("unsigned"), .width(9)) comparator_3 (.a(_1), .b(9'h100), .lt(comparator_3_lt));  // open: gt, eq
  Comparator #(.mode("unsigned"), .width(9)) comparator_4 (.a(_2), .b(9'h100), .lt(comparator_4_lt));  // open: gt, eq
  // Probe on _1_2
  Comparator #(.mode("unsigned"), .width(9)) comparator_5 (.a(_1_2), .b(9'h16b), .lt(comparator_5_lt));  // open: gt, eq
  and and_1 (and_1_out, comparator_1_gt, comparator_2_gt);
  Comparator #(.mode("unsigned"), .width(9)) comparator_6 (.a(_1_2), .b(9'h80), .gt(comparator_6_gt));  // open: eq, lt
  and and_2 (and_2_out, comparator_3_lt, comparator_4_lt);
  and and_3 (UP, comparator_5_lt, and_1_out);
  and and_4 (OP, comparator_6_gt, and_2_out);

  // Notes on the sheet:
  //   adder with overflow and underflow protection
  //   2 negative inputs
  //   overflow range
  //   2 positive inputs
  //   underflow range
endmodule

module FPM_1_0_xxx (
  input  Xn,
  input  [22:0] in_2,
  output [23:0] out_3,
  output [4:0] LZCX
);

  wire [4:0] bitfinder_1_index;
  wire [23:0] bit_extender_1_out, shifter_1_out;

  assign bit_extender_1_out = {{1{Xn}}, in_2};  // Bit_Extender bit_extender_1
  BitFinder #(.\type ("high1"), .width(24)) bitfinder_1 (
    .in(bit_extender_1_out), .index(bitfinder_1_index));  // open: found
  Subtractor #(.width(5)) subtractor_1 (.a(5'b10111), .b(bitfinder_1_index), .out(LZCX));  // open: bin, bout
  Shifter #(.width(24)) shifter_1 (.in(bit_extender_1_out), .\dist (LZCX), .out(shifter_1_out));
  Multiplexer #(.width(24)) multiplexer_1 (
    .in0(shifter_1_out), .in1(bit_extender_1_out), .out(out_3), .sel(Xn));  // open: en

  // Notes on the sheet:
  //   bit extension
  //   pre normalisation of subnormal number
endmodule

module FPM_MULTIPLY (
  input  [23:0] in_1,
  input  [23:0] in_2,
  output [23:0] LSB,
  output _48,
  output [23:0] MSB
);

  Multiplier #(.mode("unsigned"), .width(24)) multiplier_1 (
    .a(in_1), .b(in_2), .out(LSB), .cout({_48, MSB[22:0]}));  // open: cin

  assign MSB[23] = _48;
endmodule

module FPM_SHIFTER (
  input  _48,
  input  [23:0] MSB,
  input  [7:0] bias,
  input  [23:0] LSB,
  output [22:0] _1,
  output [22:0] _1_2,
  output [22:0] _0
);

  wire not_1_out, not_2_out;
  wire [4:0] bit_extender_1_out, bit_extender_3_out, bit_extender_6_out;
  wire [7:0] subtractor_1_out;
  wire [22:0] adder_1_out, bit_extender_2_out, bit_extender_4_out, bit_extender_5_out, bit_extender_7_out,
       bit_extender_8_out;
  wire [23:0] shifter_1_out, shifter_2_out, shifter_3_out;

  not not_1 (not_1_out, MSB[23]);
  assign bit_extender_1_out = {{4{1'b0}}, not_1_out};  // Bit_Extender bit_extender_1
  // Probe on bias
  assign bit_extender_2_out = {{22{1'b0}}, LSB[23]};  // Bit_Extender bit_extender_2
  assign bit_extender_3_out = {{4{1'b0}}, MSB[23]};  // Bit_Extender bit_extender_3
  // Probe on subtractor_1_out
  Subtractor subtractor_1 (.a({8{1'b0}}), .b(bias), .out(subtractor_1_out));  // open: bin, bout
  Shifter #(.shift("lr"), .width(24)) shifter_1 (.in(LSB), .\dist (bit_extender_3_out), .out(shifter_1_out));
  Bit_Extender #(.in_width(24), .out_width(23), .\type ("zero")) bit_extender_4 (.in(LSB), .out(bit_extender_4_out));
  Bit_Extender #(.in_width(24), .out_width(23), .\type ("zero")) bit_extender_5 (
    .in(shifter_1_out), .out(bit_extender_5_out));
  Bit_Extender #(.out_width(5), .\type ("zero")) bit_extender_6 (.in(subtractor_1_out), .out(bit_extender_6_out));
  Shifter #(.width(24)) shifter_2 (.in(MSB), .\dist (bit_extender_1_out), .out(shifter_2_out));
  Shifter #(.shift("lr"), .width(24)) shifter_3 (.in(MSB), .\dist (bit_extender_6_out), .out(shifter_3_out));
  Multiplexer #(.width(23)) multiplexer_1 (
    .in0(bit_extender_4_out), .in1(bit_extender_5_out), .out(_0), .sel(MSB[23]));  // open: en
  Bit_Extender #(.in_width(24), .out_width(23), .\type ("zero")) bit_extender_7 (.in(MSB), .out(bit_extender_7_out));
  Bit_Extender #(.in_width(24), .out_width(23), .\type ("zero")) bit_extender_8 (
    .in(shifter_2_out), .out(bit_extender_8_out));
  Bit_Extender #(.in_width(24), .out_width(23), .\type ("zero")) bit_extender_9 (.in(shifter_3_out), .out(_1_2));
  Adder #(.width(23)) adder_1 (.a(bit_extender_8_out), .b(bit_extender_2_out), .out(adder_1_out));  // open: cin, cout
  not not_2 (not_2_out, _48);
  Multiplexer #(.width(23)) multiplexer_2 (
    .in0(bit_extender_7_out), .in1(adder_1_out), .out(_1), .sel(not_2_out));  // open: en

  // Notes on the sheet:
  //   0
  //   1
  //   left 1
  //   left 0
  //   right by bias 
  //   left xe+ye+b+1
  //   subnormal rounding injection
endmodule

module FPM_X_Y (
  input  So,
  input  [7:0] Eo,
  input  [22:0] Mo,
  output [31:0] X_Y
);


  assign X_Y = {So, Eo, Mo};
endmodule

module FPM_MULTIPLIER_NNN (
  input  [31:0] X,
  input  [31:0] Y,
  output NNS,
  output NSN,
  output NSS,
  output NNN,
  output plus_iO,
  output minus_iO,
  output not_exact,
  output plus_0U,
  output minus_0U,
  output NaN,
  output [31:0] X_Y
);

  wire _48, fpm_incrementer_1_carry, fpm_rounding_1_o, fpm_sticky_1_out_3, NE, NNN_t, NNS_t, NSN_t, NSS_t,
       OP, or_1_out, So, sub, Sx, Sy, UP, Xn, Yn;
  wire [4:0] LZCX, LZCY;
  wire [7:0] bias, fpu_adder_1_2__1_2, multiplexer_1_out, multiplexer_2_out;
  wire [8:0] Ex, ex_ey, Ey, fpm_ex_ex_1_ex_2, fpm_ey_ey_1_ey_2;
  wire [22:0] fpm_incrementer_1_out, fpm_shifter_1__0, fpm_shifter_1__1, fpm_shifter_1__1_2,
       multiplexer_3_out, Mx, My;
  wire [23:0] fpm_1_0_xxx_1_out_3, fpm_1_0_yyy_1_out_3, fpm_multiply_1_lsb, fpm_multiply_1_msb;
  wire [31:0] X_Y_t;

  FPM_INPUT_X fpm_input_x_1 (.Sx(Sx), .Mx(Mx), .Ex(Ex), .X(X));
  xor xor_1 (So, Sx, Sy);
  FPM_Ex_ex fpm_ex_ex_1 (.ex_2(fpm_ex_ex_1_ex_2), .pre_lzc(LZCX), .Xn(Xn), .Ex(Ex), .b(9'h7f));
  // Probe on fpm_ex_ex_1_ex_2
  FPU_ADDER fpu_adder_1 (._1_2(ex_ey), .UP(UP), .OP(OP), ._1(fpm_ex_ex_1_ex_2), ._2(fpm_ey_ey_1_ey_2));
  FPU_ADDER_1 fpu_adder_1_1 (._1_2(bias), ._1(9'h7f), ._2(ex_ey));
  Multiplexer #(.width(8)) multiplexer_1 (
    .in0(bias), .in1(fpu_adder_1_2__1_2), .out(multiplexer_1_out), .sel(or_1_out));  // open: en
  // Probe on multiplexer_1_out
  FPM_INPUT_Y fpm_input_y_1 (.Sy(Sy), .My(My), .Ey(Ey), .Y(Y));
  // Probe on fpm_ey_ey_1_ey_2
  FPU_ADDER_1 fpu_adder_1_2 (._1_2(fpu_adder_1_2__1_2), ._1(ex_ey), ._2(9'h80));
  Multiplexer #(.width(8)) multiplexer_2 (
    .in0(multiplexer_1_out), .in1({8{1'b0}}), .out(multiplexer_2_out), .sel(sub));  // open: en
  FPM_Ey_ey fpm_ey_ey_1 (.ey_2(fpm_ey_ey_1_ey_2), .pre_lzc(LZCY), .Yn(Yn), .Ey(Ey), .b(9'h7f));
  or or_1 (or_1_out, _48, fpm_incrementer_1_carry);
  FPM_1_0_xxx fpm_1_0_xxx_1 (.out_3(fpm_1_0_xxx_1_out_3), .LZCX(LZCX), .in_2(Mx), .Xn(Xn));
  FPM_SHIFTER fpm_shifter_1 (
    ._1(fpm_shifter_1__1), ._1_2(fpm_shifter_1__1_2), ._0(fpm_shifter_1__0), .MSB(fpm_multiply_1_msb),
    .LSB(fpm_multiply_1_lsb), .bias(bias), ._48(_48));
  Multiplexer #(.width(23)) multiplexer_3 (
    .in0(fpm_shifter_1__1), .in1(fpm_shifter_1__1_2), .out(multiplexer_3_out), .sel(sub));  // open: en
  FPM_1_0_yyy fpm_1_0_yyy_1 (.out_3(fpm_1_0_yyy_1_out_3), .LZCY(LZCY), .in_2(My), .Yn(Yn));
  FPM_STICKY fpm_sticky_1 (.NE(NE), .out_3(fpm_sticky_1_out_3), .in_1(fpm_shifter_1__0));
  FPM_ROUNDING fpm_rounding_1 (
    .O(fpm_rounding_1_o), .Bit_23(multiplexer_3_out), .Bit_24(fpm_shifter_1__0),
    .sticky_bit(fpm_sticky_1_out_3));
  FPM_INCREMENTER fpm_incrementer_1 (
    .out(fpm_incrementer_1_out), .carry(fpm_incrementer_1_carry), .inc(fpm_rounding_1_o),
    .mantissa(multiplexer_3_out));
  FPM_MULTIPLY fpm_multiply_1 (
    .MSB(fpm_multiply_1_msb), .LSB(fpm_multiply_1_lsb), ._48(_48), .in_1(fpm_1_0_xxx_1_out_3),
    .in_2(fpm_1_0_yyy_1_out_3));
  FPM_SPECIAL_CASES fpm_special_cases_1 (
    .NaN(NaN), .not_exact(not_exact), .NNN(NNN), .NSS(NSS), .NSN(NSN), .NNS(NNS), .plus_iO(plus_iO),
    .minus_iO(minus_iO), .plus_0U(plus_0U), .minus_0U(minus_0U), .X_Y_out(X_Y), .Y(Y), .Sx(Sx), .Sy(Sy),
    .OP(OP), .UP(UP), .So(So), .NE(NE), .X(X), .OP_2(NNN_t), .UP_2(NSS_t), .So_2(NSN_t), .NE_2(NNS_t),
    .X_Y(X_Y_t));
  FPM_TEST_TYPE fpm_test_type_1 (
    .Xn(Xn), .Yn(Yn), .sub(sub), .NNN(NNN_t), .NSS(NSS_t), .NSN(NSN_t), .NNS(NNS_t), .ex_ey(ex_ey), .Y(Ey),
    .X(Ex));
  FPM_X_Y fpm_x_y_1 (.X_Y(X_Y_t), .So(So), .Eo(multiplexer_2_out), .Mo(fpm_incrementer_1_out));

  // Other names for the same wires on the sheet: X_Yo[31:0] = X_Y

  // Notes on the sheet:
  //   sx
  //   sy
  //   EXOR
  //   b
  //   ex
  //   ex+ey+b
  //   eo+b
  //   ey
  //   b+1
  //   ex+ey+b+1
  //   OR
  //   1.mx
  //   1.my
endmodule

module FPM_MULTIPLIER_NNN_TEST (
);

  wire clk, NaN, NNN, NNS, not_exact, NSN, NSS, overflow__inf, overflow__inf_t, underflow___zero,
       underflow___zero_t;
  wire [7:0] A;
  wire [31:0] X, X_Y_out, Y;

  RAM #(.dataWidth(32)) ram_1 (.addr(A), .clk(clk), .dout(X));  // open: we, din
  LED led_1 (.in(NNN));
  LED led_2 (.in(NSS));
  LED led_3 (.in(NSN));
  LED led_4 (.in(NNS));
  // Probe on X
  RAM #(.dataWidth(32)) ram_2 (.addr(A), .we(1'b1), .clk(clk), .din(X_Y_out));  // open: dout
  Clock clock_1 (.out(clk));
  Counter #(.ongoal("stay")) counter_1 (.count(1'b1), .Q(A), .clk(clk));  // open: load, D, carry, clr
  FPM_MULTIPLIER_NNN fpm_multiplier_nnn_1 (
    .minus_0U(underflow___zero_t), .plus_iO(overflow__inf), .minus_iO(overflow__inf_t),
    .plus_0U(underflow___zero), .NNS(NNS), .NSN(NSN), .NSS(NSS), .NNN(NNN), .NaN(NaN), .X_Y(X_Y_out),
    .not_exact(not_exact), .X(X), .Y(Y));
  // Probe on X_Y_out
  RAM #(.dataWidth(32)) ram_3 (.addr(A), .clk(clk), .dout(Y));  // open: we, din
  // Probe on Y
  LED led_5 (.in(not_exact));
  LED led_6 (.in(NaN));
  LED led_7 (.in(overflow__inf));
  LED led_8 (.in(overflow__inf_t));
  LED led_9 (.in(underflow___zero));
  LED led_10 (.in(underflow___zero_t));

  // Notes on the sheet:
  //   input X
  //   output X.Y
  //   input Y
  //   flags
endmodule

module FPM_INCREMENTER (
  input  [22:0] mantissa,
  input  inc,
  output [22:0] out,
  output carry
);

  wire [22:0] bit_extender_1_out;

  assign bit_extender_1_out = {{22{1'b0}}, inc};  // Bit_Extender bit_extender_1
  Adder #(.width(23)) adder_1 (.a(mantissa), .b(bit_extender_1_out), .out(out), .cout(carry));  // open: cin
endmodule

module FPM_STICKY (
  input  [22:0] in_1,
  output NE,
  output out_3
);

  or or_1 (NE, in_1[22], out_3);
  or or_2 (out_3, in_1[21], in_1[20], in_1[19], in_1[18], in_1[17], in_1[16], in_1[15], in_1[14], in_1[13], in_1[12], in_1[11], in_1[10], in_1[9], in_1[8], in_1[7], in_1[6], in_1[5], in_1[4], in_1[3], in_1[2], in_1[1], in_1[0]);

  // Notes on the sheet:
  //   not exact
  //   sticky
endmodule

module FPM_ROUNDING (
  input  sticky_bit,
  input  [22:0] Bit_23,
  input  [22:0] Bit_24,
  output O
);

  wire and_1_out, and_2_out;

  and and_1 (and_1_out, Bit_24[22], sticky_bit);
  and and_2 (and_2_out, Bit_23[0], Bit_24[22]);
  or or_1 (O, and_1_out, and_2_out);

  // Notes on the sheet:
  //   LSM mantissa
  //   Guard Bit
  //   g
  //   r
  //   lsbm
  //   O
  //   0   0   0   0
  //   0   0   1   0
  //   tie
  //   0   1   0   0
  //   0   1   1   1
  //   1   0   0   0
  //   1   0   1   0
  //   1   1   0   1
  //   tie
  //   1   1   1   1
endmodule

module FPM_SPECIAL_CASES (
  input  [31:0] X,
  input  [31:0] Y,
  input  Sx,
  input  Sy,
  input  OP,
  input  OP_2,
  input  [31:0] X_Y,
  input  UP,
  input  UP_2,
  input  So,
  input  So_2,
  input  NE,
  input  NE_2,
  output NaN,
  output [31:0] X_Y_out,
  output NNN,
  output NSS,
  output NSN,
  output NNS,
  output plus_iO,
  output minus_iO,
  output not_exact,
  output plus_0U,
  output minus_0U
);

  wire fpm_comparators_1_minus_inf_x, fpm_comparators_1_minus_inf_y, fpm_comparators_1_minus_x,
       fpm_comparators_1_minus_y, fpm_comparators_1_minus_zero_x, fpm_comparators_1_minus_zero_y,
       fpm_comparators_1_nanx, fpm_comparators_1_nany, fpm_comparators_1_plus_inf_x,
       fpm_comparators_1_plus_inf_y, fpm_comparators_1_plus_x, fpm_comparators_1_plus_y,
       fpm_comparators_1_plus_zero_x, fpm_comparators_1_plus_zero_y, fpm_special_test_1_minus_infinity,
       fpm_special_test_1_minus_zero, fpm_special_test_1_plus_inf, fpm_special_test_1_plus_zero;

  FPM_COMPARATORS fpm_comparators_1 (
    .plus_x(fpm_comparators_1_plus_x), .minus_x(fpm_comparators_1_minus_x),
    .minus_inf_x(fpm_comparators_1_minus_inf_x), .plus_inf_x(fpm_comparators_1_plus_inf_x),
    .plus_zero_x(fpm_comparators_1_plus_zero_x), .minus_zero_x(fpm_comparators_1_minus_zero_x),
    .minus_inf_y(fpm_comparators_1_minus_inf_y), .plus_y(fpm_comparators_1_plus_y),
    .minus_y(fpm_comparators_1_minus_y), .plus_inf_y(fpm_comparators_1_plus_inf_y),
    .plus_zero_y(fpm_comparators_1_plus_zero_y), .minus_zero_y(fpm_comparators_1_minus_zero_y),
    .NaNy(fpm_comparators_1_nany), .NaNx(fpm_comparators_1_nanx), .Y(Y), .X(X), .Sx(Sx), .Sy(Sy));
  FPM_SPECIAL_TEST fpm_special_test_1 (
    .plus_zero(fpm_special_test_1_plus_zero), .minus_zero(fpm_special_test_1_minus_zero), .NaN(NaN),
    .plus_inf(fpm_special_test_1_plus_inf), .minus_infinity(fpm_special_test_1_minus_infinity),
    .plus_inf_x(fpm_comparators_1_plus_inf_x), .minus_inf_x(fpm_comparators_1_minus_inf_x),
    .plus_inf_y(fpm_comparators_1_plus_inf_y), .minus_inf_y(fpm_comparators_1_minus_inf_y),
    .plus_zero_x(fpm_comparators_1_plus_zero_x), .minus_zero_x(fpm_comparators_1_minus_zero_x),
    .plus_zero_y(fpm_comparators_1_plus_zero_y), .minus_zero_y(fpm_comparators_1_minus_zero_y),
    .Nay(fpm_comparators_1_nany), .plus_x(fpm_comparators_1_plus_x), .plus_y(fpm_comparators_1_plus_y),
    .minus_x(fpm_comparators_1_minus_x), .minus_y(fpm_comparators_1_minus_y), .NaNx(fpm_comparators_1_nanx));
  FPM_MULTIPLEX fpm_multiplex_1 (
    .X_Y_out(X_Y_out), .NNNo(NNN), .NSSo(NSS), .NSNo(NSN), .NNSo(NNS), .overlow___inf_out(plus_iO),
    .underflow____zero_out(plus_0U), .overflow___inf_out(minus_iO), .underflow___zero_out(minus_0U),
    .not_exact(not_exact), .X_Y(X_Y), .UP(UP), .plus_inf(fpm_special_test_1_plus_inf),
    .plus_zero(fpm_special_test_1_plus_zero), .minus_inf(fpm_special_test_1_minus_infinity),
    .minus_zero(fpm_special_test_1_minus_zero), .NaN(NaN), .OP(OP), .So(So), .NE(NE), .NNN(OP_2), .NSS(UP_2),
    .NSN(So_2), .NNS(NE_2));

  // Other names for the same wires on the sheet: NNN_t = OP_2; NNS_t = NE_2; NSN_t = So_2; NSS_t = UP_2
endmodule

module FPM_TEST_TYPE (
  input  [8:0] X,
  input  [8:0] Y,
  input  [8:0] ex_ey,
  output NNN,
  output NSS,
  output Xn,
  output Yn,
  output NSN,
  output NNS,
  output sub
);

  wire and_3_out, and_4_out, and_5_out, and_6_out, comparator_1_lt, comparator_2_gt, not_1_out, not_2_out,
       not_3_out, not_4_out, not_5_out, not_6_out, not_7_out;

  or or_1 (Xn, X[7], X[6], X[5], X[4], X[3], X[2], X[1], X[0]);
  // Probe on ex_ey
  or or_2 (Yn, Y[7], Y[6], Y[5], Y[4], Y[3], Y[2], Y[1], Y[0]);
  Comparator #(.mode("unsigned"), .width(9)) comparator_1 (
    .a(ex_ey), .b(9'h181), .lt(comparator_1_lt));  // open: gt, eq
  Comparator #(.mode("unsigned"), .width(9)) comparator_2 (
    .a(ex_ey), .b(9'h16a), .gt(comparator_2_gt));  // open: eq, lt
  and and_1 (sub, comparator_1_lt, comparator_2_gt);
  not not_1 (not_1_out, sub);
  not not_2 (not_2_out, Xn);
  not not_3 (not_3_out, Yn);
  not not_4 (not_4_out, Xn);
  not not_5 (not_5_out, sub);
  not not_6 (not_6_out, Yn);
  not not_7 (not_7_out, sub);
  and and_2 (NNN, Xn, Yn, not_1_out);
  and and_3 (and_3_out, not_2_out, Yn, sub);
  and and_4 (and_4_out, Xn, not_3_out, sub);
  and and_5 (and_5_out, not_4_out, Yn, not_5_out);
  and and_6 (and_6_out, Xn, not_6_out, not_7_out);
  and and_7 (NNS, Xn, Yn, sub);
  or or_3 (NSS, and_3_out, and_4_out);
  or or_4 (NSN, and_5_out, and_6_out);

  // Notes on the sheet:
  //   subnormal = 1
  //   normal =0
  //   test for normal or subnormal inputs
  //   normal = 1 
  //   subnormal =0
  //   test for normal or subnormal outputs
  //   182 hex is 386 decimal = -126 in signed decimal for 9 bits
  //   16a hex is 362 decimal = -150 in signed decimal for 9 bits
  //   test number types
  //   Xn
  //   Yn
  //   sub
  //    0     0     0     S     S     X
  //   0     0     1     S     S     X
  //   0     1     0     S     N     N
  //   0     1     1     S     N     S
  //   1     0     0     N     S     N
  //   1     0     1     N     S     S
  //   1     1     0     N     N     N
  //   1     1     1     N     N     S
endmodule

module FPM_PRE_LZC (
  input  [23:0] Ym,
  input  [23:0] Xm,
  output [4:0] LZC_Y,
  output [4:0] LZC_X
);

  wire [4:0] bitfinder_1_index, bitfinder_2_index;

  BitFinder #(.\type ("high1"), .width(24)) bitfinder_1 (.in(Ym), .index(bitfinder_1_index));  // open: found
  BitFinder #(.\type ("high1"), .width(24)) bitfinder_2 (.in(Xm), .index(bitfinder_2_index));  // open: found
  Subtractor #(.width(5)) subtractor_1 (.a(5'b10111), .b(bitfinder_1_index), .out(LZC_Y));  // open: bin, bout
  Subtractor #(.width(5)) subtractor_2 (.a(5'b10111), .b(bitfinder_2_index), .out(LZC_X));  // open: bin, bout
endmodule

module FPU_ADDER_1 (
  input  [8:0] _1,
  input  [8:0] _2,
  output [7:0] _1_2
);

  wire [8:0] adder_1_out;

  Adder #(.width(9)) adder_1 (.a(_1), .b(_2), .out(adder_1_out));  // open: cin, cout
  Bit_Extender #(.in_width(9), .out_width(8), .\type ("zero")) bit_extender_1 (.in(adder_1_out), .out(_1_2));
endmodule

module FPM_1_0_yyy (
  input  Yn,
  input  [22:0] in_2,
  output [23:0] out_3,
  output [4:0] LZCY
);

  wire [4:0] bitfinder_1_index;
  wire [23:0] bit_extender_1_out, shifter_1_out;

  assign bit_extender_1_out = {{1{Yn}}, in_2};  // Bit_Extender bit_extender_1
  BitFinder #(.\type ("high1"), .width(24)) bitfinder_1 (
    .in(bit_extender_1_out), .index(bitfinder_1_index));  // open: found
  Subtractor #(.width(5)) subtractor_1 (.a(5'b10111), .b(bitfinder_1_index), .out(LZCY));  // open: bin, bout
  Shifter #(.width(24)) shifter_1 (.in(bit_extender_1_out), .\dist (LZCY), .out(shifter_1_out));
  Multiplexer #(.width(24)) multiplexer_1 (
    .in0(shifter_1_out), .in1(bit_extender_1_out), .out(out_3), .sel(Yn));  // open: en
endmodule

module FPM_INFINITY (
  input  [31:0] X,
  input  [31:0] Y,
  input  Sx,
  input  Sy,
  output [31:0] \output 
);

  wire and_1_out, and_2_out, and_3_out, and_4_out, and_5_out, and_6_out, and_7_out, and_8_out, and_9_out,
       and_10_out, and_11_out, and_12_out, comparator_5_eq, comparator_6_eq, comparator_7_eq,
       comparator_8_eq, comparator_9_eq, comparator_10_eq, comparator_11_eq, comparator_12_eq,
       comparator_13_eq, comparator_14_eq, comparator_15_eq, comparator_16_eq, comparator_17_eq,
       comparator_18_eq, comparator_19_eq, comparator_20_eq, comparator_21_eq, comparator_22_eq,
       comparator_23_eq, comparator_24_eq, minus_X, minus_Y, plus_X, plus_Y;

  Comparator #(.mode("unsigned"), .width(1)) comparator_1 (.a(Sx), .b(1'b0), .eq(plus_X));  // open: gt, lt
  Comparator #(.mode("unsigned"), .width(1)) comparator_2 (.a(Sx), .b(1'b1), .eq(minus_X));  // open: gt, lt
  Comparator #(.mode("unsigned"), .width(1)) comparator_3 (.a(Sy), .b(1'b0), .eq(plus_Y));  // open: gt, lt
  Comparator #(.mode("unsigned"), .width(1)) comparator_4 (.a(Sy), .b(1'b1), .eq(minus_Y));  // open: gt, lt
  Comparator #(.mode("unsigned"), .width(32)) comparator_5 (
    .a(X), .b(32'h7f800000), .eq(comparator_5_eq));  // open: gt, lt
  Comparator #(.mode("unsigned"), .width(32)) comparator_6 (
    .a(Y), .b(32'h7f800000), .eq(comparator_6_eq));  // open: gt, lt
  Comparator #(.mode("unsigned"), .width(32)) comparator_7 (
    .a(X), .b(32'hff800000), .eq(comparator_7_eq));  // open: gt, lt
  Comparator #(.mode("unsigned"), .width(32)) comparator_8 (
    .a(Y), .b(32'h7f800000), .eq(comparator_8_eq));  // open: gt, lt
  Comparator #(.mode("unsigned"), .width(32)) comparator_9 (
    .a(X), .b(32'h7f800000), .eq(comparator_9_eq));  // open: gt, lt
  Comparator #(.mode("unsigned"), .width(32)) comparator_10 (
    .a(Y), .b(32'hff800000), .eq(comparator_10_eq));  // open: gt, lt
  Comparator #(.mode("unsigned"), .width(32)) comparator_11 (
    .a(X), .b(32'hff800000), .eq(comparator_11_eq));  // open: gt, lt
  Comparator #(.mode("unsigned"), .width(32)) comparator_12 (
    .a(Y), .b(32'hff800000), .eq(comparator_12_eq));  // open: gt, lt
  Comparator #(.mode("unsigned"), .width(32)) comparator_13 (
    .a(X), .b(32'h7f800000), .eq(comparator_13_eq));  // open: gt, lt
  Comparator #(.mode("unsigned"), .width(32)) comparator_14 (
    .a(Y), .b(32'h7fffffff), .eq(comparator_14_eq));  // open: gt, lt
  Comparator #(.mode("unsigned"), .width(32)) comparator_15 (
    .a(Y), .b(32'h7f800000), .eq(comparator_15_eq));  // open: gt, lt
  Comparator #(.mode("unsigned"), .width(32)) comparator_16 (
    .a(X), .b(32'h7fffffff), .eq(comparator_16_eq));  // open: gt, lt
  Comparator #(.mode("unsigned"), .width(32)) comparator_17 (
    .a(X), .b(32'hff800000), .eq(comparator_17_eq));  // open: gt, lt
  Comparator #(.mode("unsigned"), .width(32)) comparator_18 (
    .a(Y), .b(32'h7fffffff), .eq(comparator_18_eq));  // open: gt, lt
  Comparator #(.mode("unsigned"), .width(32)) comparator_19 (
    .a(Y), .b(32'h7f800000), .eq(comparator_19_eq));  // open: gt, lt
  Comparator #(.mode("unsigned"), .width(32)) comparator_20 (
    .a(X), .b(32'h7fffffff), .eq(comparator_20_eq));  // open: gt, lt
  and and_1 (and_1_out, comparator_5_eq, comparator_6_eq);
  and and_2 (and_2_out, comparator_7_eq, comparator_8_eq);
  and and_3 (and_3_out, comparator_9_eq, comparator_10_eq);
  and and_4 (and_4_out, comparator_11_eq, comparator_12_eq);
  and and_5 (and_5_out, comparator_13_eq, comparator_14_eq);
  and and_6 (and_6_out, comparator_15_eq, comparator_16_eq);
  and and_7 (and_7_out, comparator_17_eq, comparator_18_eq);
  and and_8 (and_8_out, comparator_19_eq, comparator_20_eq);
  Comparator #(.mode("unsigned"), .width(32)) comparator_21 (
    .a(X), .b(32'h7f800000), .eq(comparator_21_eq));  // open: gt, lt
  Comparator #(.mode("unsigned"), .width(32)) comparator_22 (
    .a(Y), .b(32'h7f800000), .eq(comparator_22_eq));  // open: gt, lt
  Comparator #(.mode("unsigned"), .width(32)) comparator_23 (
    .a(X), .b(32'h7f800000), .eq(comparator_23_eq));  // open: gt, lt
  Comparator #(.mode("unsigned"), .width(32)) comparator_24 (
    .a(Y), .b(32'h7f800000), .eq(comparator_24_eq));  // open: gt, lt
  and and_9 (and_9_out, comparator_21_eq, comparator_22_eq);
  and and_10 (and_10_out, comparator_23_eq, comparator_24_eq);
  and and_11 (and_11_out, and_9_out, plus_Y);
  and and_12 (and_12_out, and_10_out, minus_Y);

  // Notes on the sheet:
  //   1
  //   2
  //   3
  //   4
  //   5
  //   6
  //   7
  //   8
  //   (+infinity) x (NaN) = Nan
  //   (-infinity) x (NaN) = Nan
  //   (+infinity)  x (+infinity)  = +infinity
  //   (+infinity)  x (-infinity)  = -infinity
  //   (-infinity)  x (+infinity)  = -infinity
  //   (-infinity)  x (-infinity)  = +infinity
  //   (+infinity) x (NaN) = Nan
  //   (-infinity) x (NaN) = Nan
  //   11
  //   12
  //   13
  //   14
  //   15
  //   16
  //   9
  //   10
  //   (+infinity) x  +Y = +infinity
  //   (+infinity) x  -Y = -infinity
endmodule

module FPM_SPECIAL_TEST (
  input  plus_inf_x,
  input  plus_zero_x,
  input  plus_x,
  input  minus_inf_x,
  input  minus_zero_x,
  input  plus_y,
  input  plus_inf_y,
  input  plus_zero_y,
  input  minus_x,
  input  minus_inf_y,
  input  minus_zero_y,
  input  minus_y,
  input  NaNx,
  input  Nay,
  output NaN,
  output plus_zero,
  output plus_inf,
  output minus_infinity,
  output minus_zero
);

  wire and_1_out, and_2_out, and_3_out, and_4_out, and_5_out, and_6_out, and_7_out, and_8_out, and_9_out,
       and_10_out, and_11_out, and_12_out, and_13_out, and_14_out, and_15_out, and_16_out, and_17_out,
       and_18_out, and_19_out, and_20_out, and_21_out, and_22_out, and_23_out, and_24_out, and_25_out,
       and_26_out, and_27_out, and_28_out, and_29_out, and_30_out, and_31_out, and_32_out, or_5_out, or_6_out;

  and and_1 (and_1_out, plus_inf_x, plus_inf_y);
  and and_2 (and_2_out, plus_inf_x, plus_y);
  and and_3 (and_3_out, minus_inf_x, minus_inf_y);
  and and_4 (and_4_out, minus_inf_x, minus_y);
  and and_5 (and_5_out, plus_x, plus_inf_y);
  and and_6 (and_6_out, minus_x, minus_inf_y);
  and and_7 (and_7_out, plus_inf_x, minus_inf_y);
  and and_8 (and_8_out, plus_inf_x, minus_y);
  and and_9 (and_9_out, minus_inf_x, plus_inf_y);
  and and_10 (and_10_out, minus_inf_x, plus_y);
  and and_11 (and_11_out, plus_x, minus_inf_y);
  and and_12 (and_12_out, minus_x, plus_inf_y);
  or or_1 (plus_inf, and_1_out, and_2_out, and_3_out, and_4_out, and_5_out, and_6_out);
  or or_2 (minus_infinity, and_7_out, and_8_out, and_9_out, and_10_out, and_11_out, and_12_out);
  and and_13 (and_13_out, plus_zero_x, plus_zero_y);
  and and_14 (and_14_out, plus_zero_x, plus_y);
  and and_15 (and_15_out, minus_zero_x, minus_zero_y);
  and and_16 (and_16_out, minus_zero_x, minus_y);
  and and_17 (and_17_out, plus_x, plus_zero_y);
  and and_18 (and_18_out, minus_x, minus_zero_y);
  and and_19 (and_19_out, plus_zero_x, minus_zero_y);
  and and_20 (and_20_out, plus_zero_x, minus_y);
  and and_21 (and_21_out, minus_zero_x, plus_zero_y);
  and and_22 (and_22_out, minus_zero_x, plus_y);
  and and_23 (and_23_out, plus_x, minus_zero_y);
  and and_24 (and_24_out, minus_x, plus_zero_y);
  or or_3 (plus_zero, and_13_out, and_14_out, and_15_out, and_16_out, and_17_out, and_18_out);
  or or_4 (minus_zero, and_19_out, and_20_out, and_21_out, and_22_out, and_23_out, and_24_out);
  or or_5 (or_5_out, NaNx, Nay);
  and and_25 (and_25_out, plus_inf_x, plus_zero_y);
  and and_26 (and_26_out, plus_inf_x, minus_zero_y);
  and and_27 (and_27_out, minus_inf_x, plus_zero_y);
  and and_28 (and_28_out, minus_inf_x, minus_zero_y);
  and and_29 (and_29_out, plus_zero_x, plus_inf_y);
  and and_30 (and_30_out, plus_zero_x, minus_inf_y);
  and and_31 (and_31_out, minus_zero_x, plus_inf_y);
  and and_32 (and_32_out, minus_zero_x, minus_inf_y);
  or or_6 (or_6_out, and_25_out, and_26_out, and_27_out, and_28_out, and_29_out, and_30_out, and_31_out, and_32_out);
  or or_7 (NaN, or_5_out, or_6_out);

  // Other names for the same wires on the sheet: NaNy = Nay

  // Notes on the sheet:
  //   plus infinity
  //   minus infinity
  //   plus zero
  //   minus zero
endmodule

module FPM_COMPARATORS (
  input  [31:0] X,
  input  [31:0] Y,
  input  Sx,
  input  Sy,
  output plus_inf_x,
  output plus_inf_y,
  output NaNx,
  output plus_zero_x,
  output plus_zero_y,
  output NaNy,
  output minus_inf_x,
  output minus_inf_y,
  output minus_zero_x,
  output minus_zero_y,
  output plus_x,
  output plus_y,
  output minus_y,
  output minus_x
);

  wire nor_1_out, nor_2_out, nor_3_out, nor_4_out, not_1_out, not_2_out, not_3_out, not_4_out, not_5_out,
       not_6_out, not_7_out, not_8_out, NZNIX, NZNIY;

  not not_1 (not_1_out, NZNIX);
  not not_2 (not_2_out, Sx);
  not not_3 (not_3_out, NZNIX);
  nor nor_1 (nor_1_out, Sx, not_1_out);
  nor nor_2 (nor_2_out, not_2_out, not_3_out);
  not not_4 (not_4_out, nor_1_out);
  Comparator #(.mode("unsigned"), .width(1)) comparator_1 (.a(not_4_out), .b(1'b0), .eq(plus_x));  // open: gt, lt
  Comparator #(.mode("unsigned"), .width(1)) comparator_2 (.a(nor_2_out), .b(1'b1), .eq(minus_x));  // open: gt, lt
  Comparator #(.mode("unsigned"), .width(32)) comparator_3 (.a(X), .b(32'h7f800000), .eq(plus_inf_x));  // open: gt, lt
  Comparator #(.mode("unsigned"), .width(32)) comparator_4 (.a(X), .b({32{1'b0}}), .eq(plus_zero_x));  // open: gt, lt
  Comparator #(.mode("unsigned"), .width(32)) comparator_5 (.a(X), .b(32'hff800000), .eq(minus_inf_x));  // open: gt, lt
  Comparator #(.mode("unsigned"), .width(32)) comparator_6 (
    .a(X), .b(32'h80000000), .eq(minus_zero_x));  // open: gt, lt
  not not_5 (not_5_out, NZNIY);
  not not_6 (not_6_out, Sy);
  not not_7 (not_7_out, NZNIY);
  nor nor_3 (nor_3_out, Sy, not_5_out);
  not not_8 (not_8_out, nor_3_out);
  nor nor_4 (nor_4_out, not_6_out, not_7_out);
  Comparator #(.mode("unsigned"), .width(32)) comparator_7 (.a(Y), .b(32'h7f800000), .eq(plus_inf_y));  // open: gt, lt
  Comparator #(.mode("unsigned"), .width(32)) comparator_8 (.a(Y), .b({32{1'b0}}), .eq(plus_zero_y));  // open: gt, lt
  Comparator #(.mode("unsigned"), .width(32)) comparator_9 (.a(Y), .b(32'hff800000), .eq(minus_inf_y));  // open: gt, lt
  Comparator #(.mode("unsigned"), .width(32)) comparator_10 (
    .a(Y), .b(32'h80000000), .eq(minus_zero_y));  // open: gt, lt
  Comparator #(.mode("unsigned"), .width(1)) comparator_11 (.a(not_8_out), .b(1'b0), .eq(plus_y));  // open: gt, lt
  Comparator #(.mode("unsigned"), .width(1)) comparator_12 (.a(nor_4_out), .b(1'b1), .eq(minus_y));  // open: gt, lt
  Comparator #(.mode("unsigned"), .width(32)) comparator_13 (.a(X), .b(32'h7fffffff), .eq(NaNx));  // open: gt, lt
  Comparator #(.mode("unsigned"), .width(32)) comparator_14 (.a(Y), .b(32'h7fffffff), .eq(NaNy));  // open: gt, lt
  nor nor_5 (NZNIX, plus_zero_x, minus_zero_x);
  nor nor_6 (NZNIY, plus_inf_y, minus_zero_y);

  // Notes on the sheet:
  //   plus x but not zero not inf
  //   minus x but not - zero
  //   plus infinity x
  //   plus zero x
  //   minus infinity x
  //   minus zero x
  //   minus y but not - zero
  //   plus infinity y
  //   plus zero y
  //   minus infinity y
  //   minus zero y
  //   plus y but not zero
  //   NaNx
  //   NaNy
endmodule

module FPM_MULTIPLEX (
  input  [31:0] X_Y,
  input  plus_inf,
  input  plus_zero,
  input  minus_inf,
  input  minus_zero,
  input  OP,
  input  UP,
  input  NaN,
  input  So,
  input  NE,
  input  NNN,
  input  NSS,
  input  NSN,
  input  NNS,
  output [31:0] X_Y_out,
  output overlow___inf_out,
  output underflow____zero_out,
  output overflow___inf_out,
  output underflow___zero_out,
  output not_exact,
  output NNNo,
  output NSSo,
  output NSNo,
  output NNSo
);

  wire and_1_out, and_2_out, and_3_out, and_4_out, and_5_out, nor_1_out, nor_2_out, OP_minus, OP_plus,
       or_1_out, or_2_out, or_3_out, or_4_out, UP_minus, UP_plus;
  wire [2:0] priority_encoder_1_out;

  Demultiplexer demultiplexer_1 (.out0(OP_plus), .out1(OP_minus), .in(OP), .sel(So));  // open: en
  Demultiplexer demultiplexer_2 (.out0(UP_plus), .out1(UP_minus), .in(UP), .sel(So));  // open: en
  nor nor_1 (nor_1_out, plus_inf, minus_zero);
  and and_1 (and_1_out, nor_1_out, OP_plus);
  and and_2 (and_2_out, nor_1_out, UP_plus);
  and and_3 (and_3_out, nor_1_out, OP_minus);
  and and_4 (and_4_out, nor_1_out, UP_minus);
  and and_5 (and_5_out, nor_1_out, NE);
  and and_6 (NNNo, nor_1_out, NNN);
  and and_7 (NSSo, nor_1_out, NSS);
  and and_8 (NSNo, nor_1_out, NSN);
  and and_9 (NNSo, nor_1_out, NNS);
  or or_1 (or_1_out, plus_inf, and_1_out);
  or or_2 (or_2_out, plus_zero, and_2_out);
  or or_3 (or_3_out, minus_inf, and_3_out);
  or or_4 (or_4_out, minus_zero, and_4_out);
  nor nor_2 (nor_2_out, OP_plus, UP_plus, OP_minus, UP_minus);
  Multiplexer #(.select(3), .width(32)) multiplexer_1 (
    .in0(X_Y), .in1(32'h7f800000), .in2({32{1'b0}}), .in3(32'h7fffffff), .in4(32'hff800000),
    .in5(32'h80000000), .out(X_Y_out), .sel(priority_encoder_1_out));  // open: in6, in7, en
  Priority_Encoder priority_encoder_1 (
    .in0(nor_1_out), .in1(or_1_out), .in2(or_2_out), .in3(NaN), .in4(or_3_out), .in5(or_4_out),
    .out(priority_encoder_1_out));  // open: in6, in7, en_in, gs, en_out
  or or_5 (overlow___inf_out, plus_inf, and_1_out);
  or or_6 (underflow____zero_out, plus_zero, and_2_out);
  or or_7 (overflow___inf_out, minus_inf, and_3_out);
  or or_8 (underflow___zero_out, minus_zero, and_4_out);
  and and_10 (not_exact, and_5_out, nor_2_out);
endmodule
