// Logisim project AdderSubtractor.circ as structural Verilog: 12 circuits, main circuit Tester
module Tester (
  input  SUB
);

  wire CLK_out, comparator_1_eq, comparator_2_eq, comparator_4_eq, DONE, ERR, INF, NaN, OK, OVF, RESET_out;
  wire [7:0] counter_1_q;
  wire [15:0] adder_subractor_1_x___y, rom_1_data, rom_2_data, rom_3_data;

  Clock CLK (.out(CLK_out));
  Button RESET (.out(RESET_out));
  LED u_DONE (.in(DONE));
  LED ERROR (.in(ERR));
  Counter counter_1 (.count(OK), .Q(counter_1_q), .clk(CLK_out), .clr(RESET_out));  // open: load, D, carry
  LED u_OVF (.in(OVF));
  ROM #(.dataWidth(16)) rom_1 (.addr(counter_1_q), .data(rom_1_data));
  LED u_INF (.in(INF));
  LED u_NaN (.in(NaN));
  // Probe on rom_1_data
  ROM #(.dataWidth(16)) rom_2 (.addr(counter_1_q), .data(rom_2_data));
  Comparator #(.mode("unsigned"), .width(16)) comparator_1 (
    .a(rom_1_data), .b({16{1'b1}}), .eq(comparator_1_eq));  // open: gt, lt
  // Probe on rom_2_data
  ROM #(.dataWidth(16)) rom_3 (.addr(counter_1_q), .data(rom_3_data));
  Adder_Subractor adder_subractor_1 (
    .ovf(OVF), .inf(INF), .NaN(NaN), .X___Y(adder_subractor_1_x___y), .sub(SUB), .X(rom_1_data),
    .Y(rom_2_data));
  Comparator #(.mode("unsigned"), .width(16)) comparator_2 (
    .a(rom_2_data), .b({16{1'b1}}), .eq(comparator_2_eq));  // open: gt, lt
  // Probe on adder_subractor_1_x___y
  Comparator #(.mode("unsigned"), .width(16)) comparator_3 (
    .a(adder_subractor_1_x___y), .b(rom_3_data), .eq(OK));  // open: gt, lt
  Comparator #(.mode("unsigned"), .width(16)) comparator_4 (
    .a(rom_3_data), .b({16{1'b0}}), .eq(comparator_4_eq));  // open: gt, lt
  and and_1 (DONE, comparator_1_eq, comparator_2_eq, comparator_4_eq);
  nor nor_1 (ERR, DONE, OK);

  // Notes on the sheet:
  //   contents of rom_1 (hex, n*v repeats v):
  //   5493 55b3 b008 f5cd 4800 c800 c800 c800 2001 402 4bb 836b 4c8 81c9 2b4 8197 7b 2b3 8002 8004 57ce
  //   8042 79a6 7bff fb38 fbff 7bff fbff 7e00 8166 7e00 0 7c00 fc00 fc00 f64d 7c00 fc00 d044 0 8000 0 0
  //   ffff
  //   contents of rom_2 (hex, n*v repeats v):
  //   640b b8fc 4b99 ec16 482d 482d c783 4783 a000 8400 50 bf1f 8387 418 29c 833a 11 800d 57 8046 d7ce 42
  //   76ca 5000 f71f d000 4800 c800 7046 7e00 7c00 7e00 5475 8009 0 7c00 7c00 7c00 0 e 5433 0 8000 ffff
  //   contents of rom_3 (hex, n*v repeats v):
  //   6454 55a9 4b89 f6d2 4c16 35a0 cbc2 b7d0 80 2 50b bf1f 141 24f 550 84d1 8c 2a6 55 804a 0 0 7c00 7c00
  //   fc00 fc00 7bff fbff 4*7e00 7c00 fc00 fc00 7c00 7c00 7e00 d044 e 5433
endmodule

module Adder_Subractor (
  input  [15:0] X,
  input  sub,
  input  [15:0] Y,
  output [15:0] X___Y,
  output ovf,
  output inf,
  output NaN
);

  wire add_sub_1_carry, and_1_out, comparator_1_lt, lzc_shift_1_zero, multiplexer_4_out, mx_my_1_mx_my,
       not_1_out, X0, X2norm, Xinf, XNaN, Xnorm, xor_2_out, Xsign, Xsubn, Y0, Y2norm, Yinf, YNaN, Ynorm,
       Ysign, Ysubn;
  wire [3:0] bit_extender_1_out;
  wire [4:0] exp_diff_swap_1_diff, lzc_shift_1_eout, normalise_1_eout;
  wire [9:0] lzc_shift_1_mout_hi, normalise_1_mout_hi;
  wire [10:0] add_sub_1_z_hi, add_sub_1_z_lo, bit_extender_2_out, bit_extender_3_out, lzc_shift_1_mout_lo,
       multiplexer_3_out, mx_my_1_mz_hi, mx_my_1_mz_lo, normalise_1_mout_lo, shifter_1_out_hi,
       shifter_1_out_lo;
  wire [14:0] exp_diff_swap_1_xout, exp_diff_swap_1_yout;
  wire [15:0] multiplexer_2_out, round_1_out;
  wire [15:15] multiplexer_1_out, xor_1_out;

  // Probe on X
  // Probe on Y
  Classifier classifier_1 (
    .inf(Xinf), .norm(Xnorm), .subnorm(Xsubn), ._0(X0), .NaN(XNaN), .exp(X[14:10]), .mant(X[9:0]));
  xor xor_1 (xor_1_out[15], sub, Y[15]);
  Classifier classifier_2 (
    .inf(Yinf), .norm(Ynorm), .subnorm(Ysubn), ._0(Y0), .NaN(YNaN), .exp(Y[14:10]), .mant(Y[9:0]));
  xor xor_2 (xor_2_out, X[15], xor_1_out[15]);
  Exp_Diff_Swap exp_diff_swap_1 (
    .diff(exp_diff_swap_1_diff), .Yout({Ysign, exp_diff_swap_1_yout}), .Xout({Xsign, exp_diff_swap_1_xout}),
    .XoutN(X2norm), .YoutN(Y2norm), .XinN(Xnorm), .YinN(Ynorm), .Xin(X), .Yin({xor_1_out[15], Y[14:0]}));
  Bit_Extender #(.in_width(5), .out_width(4), .\type ("zero")) bit_extender_1 (
    .in(exp_diff_swap_1_diff), .out(bit_extender_1_out));
  assign bit_extender_2_out = {{1{Y2norm}}, exp_diff_swap_1_yout[9:0]};  // Bit_Extender bit_extender_2
  assign bit_extender_3_out = {{1{X2norm}}, exp_diff_swap_1_xout[9:0]};  // Bit_Extender bit_extender_3
  Comparator #(.mode("unsigned"), .width(4)) comparator_1 (
    .a(bit_extender_1_out), .b(4'b0010), .lt(comparator_1_lt));  // open: gt, eq
  Shifter shifter_1 (
    .out_lo(shifter_1_out_lo), .out_hi(shifter_1_out_hi), .shift(bit_extender_1_out), .in(bit_extender_2_out));
  Add_Sub add_sub_1 (
    .Z_lo(add_sub_1_z_lo), .Z_hi(add_sub_1_z_hi), .carry(add_sub_1_carry), .Y_hi(shifter_1_out_hi),
    .Y_lo(shifter_1_out_lo), .X_hi(bit_extender_3_out), .sub(xor_2_out));
  mx_my mx_my_1 (
    .mz_hi(mx_my_1_mz_hi), .mz_lo(mx_my_1_mz_lo), .mx_my(mx_my_1_mx_my), .mx_hi(bit_extender_3_out),
    .my_hi(shifter_1_out_hi), .my_lo(shifter_1_out_lo));
  Normalise normalise_1 (
    .mout_hi(normalise_1_mout_hi), .eout(normalise_1_eout), .mout_lo(normalise_1_mout_lo),
    .min_hi(add_sub_1_z_hi), .ein(exp_diff_swap_1_xout[14:10]), .min_lo(add_sub_1_z_lo), .Xnorm(X2norm),
    .Ynorm(Y2norm), .sub(xor_2_out), .carry(add_sub_1_carry));
  and and_1 (and_1_out, xor_2_out, comparator_1_lt);
  LZC_Shift lzc_shift_1 (
    .mout_hi(lzc_shift_1_mout_hi), .mout_lo(lzc_shift_1_mout_lo), .eout(lzc_shift_1_eout),
    .zero(lzc_shift_1_zero), .diff(bit_extender_1_out), .ein(exp_diff_swap_1_xout[14:10]),
    .min_hi(mx_my_1_mz_hi), .min_lo(mx_my_1_mz_lo), .Xnorm(X2norm), .Ynorm(Y2norm));
  not not_1 (not_1_out, Xsign);
  Multiplexer #(.enable("false")) multiplexer_1 (
    .in0(not_1_out), .in1(Xsign), .out(multiplexer_1_out[15]), .sel(mx_my_1_mx_my));
  Multiplexer #(.enable("false"), .width(16)) multiplexer_2 (
    .in0({Xsign, normalise_1_eout, normalise_1_mout_hi}),
    .in1({multiplexer_1_out[15], lzc_shift_1_eout, lzc_shift_1_mout_hi}), .out(multiplexer_2_out),
    .sel(and_1_out));
  Multiplexer #(.enable("false"), .width(11)) multiplexer_3 (
    .in0(normalise_1_mout_lo), .in1(lzc_shift_1_mout_lo), .out(multiplexer_3_out), .sel(and_1_out));
  Multiplexer #(.enable("false")) multiplexer_4 (
    .in0(1'b0), .in1(lzc_shift_1_zero), .out(multiplexer_4_out), .sel(and_1_out));
  Round round_1 (.out(round_1_out), .zero(multiplexer_4_out), .in_lo(multiplexer_3_out), .in_hi(multiplexer_2_out));
  Selector selector_1 (
    .out(X___Y), .ovf(ovf), .inf(inf), .NaN(NaN), .X0(X0), .Y0(Y0), .Xsubn(Xsubn), .Ysubn(Ysubn),
    .Xnorm(Xnorm), .Ynorm(Ynorm), .Xinf(Xinf), .Yinf(Yinf), .Xsign(Xsign), .Ysign(Ysign), .XNaN(XNaN),
    .YNaN(YNaN), .in(round_1_out));
  // Probe on X___Y
endmodule

module Exp_Diff_Swap (
  input  XinN,
  input  [15:0] Xin,
  input  YinN,
  input  [15:0] Yin,
  output [15:0] Xout,
  output XoutN,
  output [4:0] diff,
  output YoutN,
  output [15:0] Yout
);

  wire comparator_1_lt, comparator_2_gt;
  wire [4:0] multiplexer_1_out, subtractor_1_out, subtractor_2_out, subtractor_3_out, subtractor_4_out;

  Subtractor #(.width(5)) subtractor_1 (
    .a(Xin[14:10]), .b(5'b01110), .out(subtractor_1_out), .bin(XinN));  // open: bout
  Comparator #(.mode("unsigned"), .width(5)) comparator_1 (
    .a(Xin[14:10]), .b(Yin[14:10]), .lt(comparator_1_lt));  // open: gt, eq
  Subtractor #(.width(5)) subtractor_2 (
    .a(Yin[14:10]), .b(5'b01110), .out(subtractor_2_out), .bin(YinN));  // open: bout
  Subtractor #(.width(5)) subtractor_3 (
    .a(subtractor_1_out), .b(subtractor_2_out), .out(subtractor_3_out));  // open: bin, bout
  Subtractor #(.width(5)) subtractor_4 (
    .a(subtractor_2_out), .b(subtractor_1_out), .out(subtractor_4_out));  // open: bin, bout
  Multiplexer #(.enable("false"), .width(5)) multiplexer_1 (
    .in0(subtractor_3_out), .in1(subtractor_4_out), .out(multiplexer_1_out), .sel(comparator_1_lt));
  Multiplexer #(.enable("false"), .width(16)) multiplexer_2 (.in0(Xin), .in1(Yin), .out(Xout), .sel(comparator_1_lt));
  Multiplexer #(.enable("false")) multiplexer_3 (.in0(XinN), .in1(YinN), .out(XoutN), .sel(comparator_1_lt));
  Multiplexer #(.enable("false")) multiplexer_4 (.in0(YinN), .in1(XinN), .out(YoutN), .sel(comparator_1_lt));
  Multiplexer #(.enable("false"), .width(16)) multiplexer_5 (.in0(Yin), .in1(Xin), .out(Yout), .sel(comparator_1_lt));
  Comparator #(.mode("unsigned"), .width(5)) comparator_2 (
    .a(multiplexer_1_out), .b(5'b01011), .gt(comparator_2_gt));  // open: eq, lt
  Multiplexer #(.enable("false"), .width(5)) multiplexer_6 (
    .in0(multiplexer_1_out), .in1(5'b01100), .out(diff), .sel(comparator_2_gt));
endmodule

module Add_Sub (
  input  [10:0] X_hi,
  input  [10:0] Y_hi,
  input  sub,
  input  [10:0] Y_lo,
  output [10:0] Z_hi,
  output carry,
  output [10:0] Z_lo
);

  wire adder_3_cout, adder_4_cout, C_LO;
  wire [10:0] adder_1_out, adder_2_out, adder_3_out, adder_4_out, adder_5_out, not_1_out, not_2_out;

  assign not_1_out = ~Y_hi;  // NOT_Gate not_1, 11 bits wide
  assign not_2_out = ~Y_lo;  // NOT_Gate not_2, 11 bits wide
  Adder #(.width(11)) adder_1 (.a(not_1_out), .b({11{1'b0}}), .out(adder_1_out), .cin(C_LO));  // open: cout
  Adder #(.width(11)) adder_2 (.a(not_2_out), .b(11'h1), .out(adder_2_out), .cout(C_LO));  // open: cin
  Adder #(.width(11)) adder_3 (.a(X_hi), .b(Y_hi), .out(adder_3_out), .cout(adder_3_cout));  // open: cin
  Adder #(.width(11)) adder_4 (.a(adder_1_out), .b(X_hi), .out(adder_4_out), .cout(adder_4_cout));  // open: cin
  Adder #(.width(11)) adder_5 (.a({11{1'b0}}), .b(Y_lo), .out(adder_5_out));  // open: cin, cout
  Multiplexer #(.enable("false"), .width(11)) multiplexer_1 (
    .in0(adder_3_out), .in1(adder_4_out), .out(Z_hi), .sel(sub));
  Multiplexer #(.enable("false"), .width(11)) multiplexer_2 (
    .in0(adder_5_out), .in1(adder_2_out), .out(Z_lo), .sel(sub));
  Multiplexer #(.enable("false")) multiplexer_3 (.in0(adder_3_cout), .in1(adder_4_cout), .out(carry), .sel(sub));
endmodule

module Normalise (
  input  [4:0] ein,
  input  Xnorm,
  input  Ynorm,
  input  sub,
  input  carry,
  input  [10:0] min_hi,
  input  [10:0] min_lo,
  output [4:0] eout,
  output [9:0] mout_hi,
  output [10:0] mout_lo
);

  wire and_1_out, and_2_out, and_3_out, nor_1_out, not_1_out, not_2_out, or_1_out;
  wire [4:0] adder_1_out, multiplexer_1_out, subtractor_1_out;
  wire [10:0] bit_extender_1_out, bit_extender_2_out, multiplexer_2_out, multiplexer_3_out,
       multiplexer_5_out, or_2_out, or_3_out, shifter_1_out, shifter_2_out, shifter_3_out, shifter_4_out,
       shifter_5_out;

  nor nor_1 (nor_1_out, Xnorm, Ynorm);
  not not_1 (not_1_out, sub);
  not not_2 (not_2_out, min_hi[10]);
  assign bit_extender_1_out = {{10{1'b0}}, min_hi[0]};  // Bit_Extender bit_extender_1
  assign bit_extender_2_out = {{10{1'b0}}, min_lo[10]};  // Bit_Extender bit_extender_2
  Adder #(.width(5)) adder_1 (.a(ein), .b(5'b00001), .out(adder_1_out));  // open: cin, cout
  Subtractor #(.width(5)) subtractor_1 (.a(ein), .b(5'b00001), .out(subtractor_1_out));  // open: bin, bout
  and and_1 (and_1_out, not_1_out, carry);
  and and_2 (and_2_out, nor_1_out, min_hi[10]);
  Shifter_part #(.shift("lr"), .width(11)) shifter_1 (.in(min_hi), .\dist (4'b0001), .out(shifter_1_out));
  Shifter_part #(.width(11)) shifter_2 (.in(min_hi), .\dist (4'b0001), .out(shifter_2_out));
  Shifter_part #(.shift("rr"), .width(11)) shifter_3 (.in(bit_extender_1_out), .\dist (4'b0001), .out(shifter_3_out));
  Shifter_part #(.shift("lr"), .width(11)) shifter_4 (.in(min_lo), .\dist (4'b0001), .out(shifter_4_out));
  Shifter_part #(.width(11)) shifter_5 (.in(min_lo), .\dist (4'b0001), .out(shifter_5_out));
  Multiplexer #(.enable("false"), .width(5)) multiplexer_1 (
    .in0(ein), .in1(adder_1_out), .out(multiplexer_1_out), .sel(or_1_out));
  or or_1 (or_1_out, and_1_out, and_2_out);
  Multiplexer #(.enable("false"), .width(11)) multiplexer_2 (
    .in0(min_hi), .in1(shifter_1_out), .out(multiplexer_2_out), .sel(and_1_out));
  assign or_2_out = shifter_3_out | shifter_4_out;  // OR_Gate or_2, 11 bits wide
  and and_3 (and_3_out, not_2_out, sub);
  assign or_3_out = shifter_2_out | bit_extender_2_out;  // OR_Gate or_3, 11 bits wide
  Multiplexer #(.enable("false"), .width(11)) multiplexer_3 (
    .in0(min_lo), .in1(or_2_out), .out(multiplexer_3_out), .sel(and_1_out));
  Multiplexer #(.enable("false"), .width(5)) multiplexer_4 (
    .in0(multiplexer_1_out), .in1(subtractor_1_out), .out(eout), .sel(and_3_out));
  Multiplexer #(.enable("false"), .width(11)) multiplexer_5 (
    .in0(multiplexer_2_out), .in1(or_3_out), .out(multiplexer_5_out), .sel(and_3_out));
  Multiplexer #(.enable("false"), .width(11)) multiplexer_6 (
    .in0(multiplexer_3_out), .in1(shifter_5_out), .out(mout_lo), .sel(and_3_out));
  Bit_Extender #(.in_width(11), .out_width(10), .\type ("zero")) bit_extender_3 (.in(multiplexer_5_out), .out(mout_hi));
endmodule

module mx_my (
  input  [10:0] mx_hi,
  input  [10:0] my_hi,
  input  [10:0] my_lo,
  output [10:0] mz_hi,
  output mx_my,
  output [10:0] mz_lo
);

  wire C_LO, not_1_out, not_2_out;
  wire [10:0] adder_1_out, adder_2_out, multiplexer_1_out, multiplexer_2_out, multiplexer_3_out,
       multiplexer_4_out, not_3_out, not_4_out;

  Comparator #(.mode("unsigned"), .width(11)) comparator_1 (.a(mx_hi), .b(my_hi), .gt(mx_my));  // open: eq, lt
  Multiplexer #(.enable("false"), .width(11)) multiplexer_1 (
    .in0(mx_hi), .in1(my_hi), .out(multiplexer_1_out), .sel(mx_my));
  not not_1 (not_1_out, mx_my);
  Multiplexer #(.enable("false"), .width(11)) multiplexer_2 (
    .in0({11{1'b0}}), .in1(my_lo), .out(multiplexer_2_out), .sel(mx_my));
  not not_2 (not_2_out, mx_my);
  assign not_3_out = ~multiplexer_1_out;  // NOT_Gate not_3, 11 bits wide
  Multiplexer #(.enable("false"), .width(11)) multiplexer_3 (
    .in0(mx_hi), .in1(my_hi), .out(multiplexer_3_out), .sel(not_1_out));
  assign not_4_out = ~multiplexer_2_out;  // NOT_Gate not_4, 11 bits wide
  Multiplexer #(.enable("false"), .width(11)) multiplexer_4 (
    .in0({11{1'b0}}), .in1(my_lo), .out(multiplexer_4_out), .sel(not_2_out));
  Adder #(.width(11)) adder_1 (.a(not_3_out), .b({11{1'b0}}), .out(adder_1_out), .cin(C_LO));  // open: cout
  Adder #(.width(11)) adder_2 (.a(not_4_out), .b(11'h1), .out(adder_2_out), .cout(C_LO));  // open: cin
  Adder #(.width(11)) adder_3 (.a(adder_1_out), .b(multiplexer_3_out), .out(mz_hi));  // open: cin, cout
  Adder #(.width(11)) adder_4 (.a(adder_2_out), .b(multiplexer_4_out), .out(mz_lo));  // open: cin, cout
endmodule

module LZC_Shift (
  input  Xnorm,
  input  Ynorm,
  input  [4:0] ein,
  input  [10:0] min_hi,
  input  [10:0] min_lo,
  input  [3:0] diff,
  output [4:0] eout,
  output [9:0] mout_hi,
  output [10:0] mout_lo,
  output zero
);

  wire and_1_out, and_2_out, and_4_out, comparator_1_eq, comparator_2_eq, comparator_3_eq, comparator_4_eq,
       comparator_4_lt, comparator_5_eq, not_1_out, or_2_out;
  wire [3:0] bit_extender_3_out, bitfinder_1_index, multiplexer_1_out, subtractor_1_out, subtractor_2_out;
  wire [4:0] bit_extender_4_out, multiplexer_6_out, subtractor_4_out;
  wire [5:0] bit_extender_1_out, bit_extender_2_out, multiplexer_2_out, subtractor_3_out;
  wire [10:0] multiplexer_3_out, multiplexer_4_out, multiplexer_5_out, multiplexer_7_out, or_1_out, or_3_out,
       shifter_1_out, shifter_2_out, shifter_3_out, shifter_4_out, shifter_5_out, shifter_6_out;

  not not_1 (not_1_out, Ynorm);
  and and_1 (and_1_out, Xnorm, not_1_out);
  assign bit_extender_1_out = {{1{1'b0}}, ein};  // Bit_Extender bit_extender_1
  BitFinder #(.\type ("high1"), .width(11)) bitfinder_1 (.in(min_hi), .index(bitfinder_1_index));  // open: found
  and and_2 (and_2_out, Xnorm, Ynorm);
  Subtractor #(.width(4)) subtractor_1 (.a(4'b1010), .b(bitfinder_1_index), .out(subtractor_1_out));  // open: bin, bout
  Comparator #(.mode("unsigned"), .width(11)) comparator_1 (
    .a(min_lo), .b({11{1'b0}}), .eq(comparator_1_eq));  // open: gt, lt
  Comparator #(.mode("unsigned"), .width(11)) comparator_2 (
    .a(min_hi), .b({11{1'b0}}), .eq(comparator_2_eq));  // open: gt, lt
  Comparator #(.mode("unsigned"), .width(4)) comparator_3 (
    .a(diff), .b(4'b0000), .eq(comparator_3_eq));  // open: gt, lt
  Multiplexer #(.enable("false"), .width(4)) multiplexer_1 (
    .in0(subtractor_1_out), .in1(4'b0000), .out(multiplexer_1_out), .sel(and_1_out));
  assign bit_extender_2_out = {{2{1'b0}}, subtractor_1_out};  // Bit_Extender bit_extender_2
  Shifter_part #(.width(11)) shifter_1 (.in(min_hi), .\dist (multiplexer_1_out), .out(shifter_1_out));
  Subtractor #(.width(4)) subtractor_2 (.a(4'b1011), .b(multiplexer_1_out), .out(subtractor_2_out));  // open: bin, bout
  Shifter_part #(.width(11)) shifter_2 (.in(min_lo), .\dist (multiplexer_1_out), .out(shifter_2_out));
  Subtractor #(.width(6)) subtractor_3 (
    .a(bit_extender_1_out), .b(bit_extender_2_out), .out(subtractor_3_out));  // open: bin, bout
  Shifter_part #(.shift("lr"), .width(11)) shifter_3 (.in(min_lo), .\dist (subtractor_2_out), .out(shifter_3_out));
  and and_3 (zero, comparator_1_eq, comparator_2_eq, comparator_3_eq);
  Comparator #(.width(6)) comparator_4 (
    .a(subtractor_3_out), .b({6{1'b0}}), .eq(comparator_4_eq), .lt(comparator_4_lt));  // open: gt
  assign or_1_out = shifter_1_out | shifter_3_out;  // OR_Gate or_1, 11 bits wide
  Subtractor #(.width(5)) subtractor_4 (.a(ein), .b(5'b00001), .out(subtractor_4_out));  // open: bin, bout
  or or_2 (or_2_out, zero, comparator_4_eq, comparator_4_lt);
  Multiplexer #(.enable("false"), .width(6)) multiplexer_2 (
    .in0(subtractor_3_out), .in1({6{1'b0}}), .out(multiplexer_2_out), .sel(or_2_out));
  Multiplexer #(.enable("false"), .width(11)) multiplexer_3 (
    .in0(or_1_out), .in1(min_hi), .out(multiplexer_3_out), .sel(or_2_out));
  Bit_Extender #(.in_width(5), .out_width(4), .\type ("zero")) bit_extender_3 (
    .in(subtractor_4_out), .out(bit_extender_3_out));
  Bit_Extender #(.in_width(6), .out_width(5), .\type ("zero")) bit_extender_4 (
    .in(multiplexer_2_out), .out(bit_extender_4_out));
  Shifter_part #(.width(11)) shifter_4 (.in(multiplexer_3_out), .\dist (bit_extender_3_out), .out(shifter_4_out));
  Shifter_part #(.shift("lr"), .width(11)) shifter_5 (.in(shifter_2_out), .\dist (4'b1010), .out(shifter_5_out));
  Shifter_part #(.width(11)) shifter_6 (.in(shifter_2_out), .\dist (bit_extender_3_out), .out(shifter_6_out));
  Comparator #(.width(5)) comparator_5 (.a(bit_extender_4_out), .b({5{1'b0}}), .eq(comparator_5_eq));  // open: gt, lt
  assign or_3_out = shifter_4_out | shifter_5_out;  // OR_Gate or_3, 11 bits wide
  and and_4 (and_4_out, comparator_5_eq, and_2_out);
  Multiplexer #(.enable("false"), .width(11)) multiplexer_4 (
    .in0(multiplexer_3_out), .in1(or_3_out), .out(multiplexer_4_out), .sel(and_4_out));
  Multiplexer #(.enable("false"), .width(11)) multiplexer_5 (
    .in0(shifter_2_out), .in1(shifter_6_out), .out(multiplexer_5_out), .sel(and_4_out));
  Multiplexer #(.enable("false"), .width(5)) multiplexer_6 (
    .in0({5{1'b0}}), .in1(5'b00001), .out(multiplexer_6_out), .sel(comparator_2_eq));
  Multiplexer #(.enable("false"), .width(11)) multiplexer_7 (
    .in0(multiplexer_4_out), .in1({11{1'b0}}), .out(multiplexer_7_out), .sel(comparator_2_eq));
  Multiplexer #(.enable("false"), .width(11)) multiplexer_8 (
    .in0(multiplexer_5_out), .in1(min_lo), .out(mout_lo), .sel(comparator_2_eq));
  Subtractor #(.width(5)) subtractor_5 (.a(bit_extender_4_out), .b(multiplexer_6_out), .out(eout));  // open: bin, bout
  Bit_Extender #(.in_width(11), .out_width(10), .\type ("zero")) bit_extender_5 (.in(multiplexer_7_out), .out(mout_hi));

  // Other names for the same wires on the sheet: EXP_IN[4:0] = ein
endmodule

module Round (
  input  [15:0] in_hi,
  input  [10:0] in_lo,
  input  zero,
  output [15:0] out
);

  wire and_1_out, and_2_out, or_1_out, sticky_1_sb;
  wire [14:0] adder_1_out, bit_extender_1_out;

  and and_1 (and_1_out, in_hi[0], in_lo[10]);
  and and_2 (and_2_out, in_lo[10], sticky_1_sb);
  or or_1 (or_1_out, and_1_out, and_2_out);
  Sticky sticky_1 (.sb(sticky_1_sb), .in(in_lo[9:0]));
  assign bit_extender_1_out = {{14{1'b0}}, or_1_out};  // Bit_Extender bit_extender_1
  Adder #(.width(15)) adder_1 (.a(in_hi[14:0]), .b(bit_extender_1_out), .out(adder_1_out));  // open: cin, cout
  Multiplexer #(.enable("false"), .width(16)) multiplexer_1 (
    .in0({in_hi[15], adder_1_out}), .in1({16{1'b0}}), .out(out), .sel(zero));
endmodule

module Shifter (
  input  [10:0] in,
  input  [3:0] shift,
  output [10:0] out_hi,
  output [10:0] out_lo
);

  wire [3:0] subtractor_1_out;

  Subtractor #(.width(4)) subtractor_1 (.a(4'b1011), .b(shift), .out(subtractor_1_out));  // open: bin, bout
  Shifter_part #(.shift("lr"), .width(11)) shifter_1 (.in(in), .\dist (shift), .out(out_hi));
  Shifter_part #(.width(11)) shifter_2 (.in(in), .\dist (subtractor_1_out), .out(out_lo));
endmodule

module Classifier (
  input  [4:0] exp,
  input  [9:0] mant,
  output NaN,
  output inf,
  output norm,
  output subnorm,
  output _0
);

  wire comparator_1_eq, comparator_1_gt, comparator_2_eq, comparator_3_eq, comparator_4_eq, comparator_4_gt;

  Comparator #(.mode("unsigned"), .width(10)) comparator_1 (
    .a(mant), .b({10{1'b0}}), .gt(comparator_1_gt), .eq(comparator_1_eq));  // open: lt
  Comparator #(.mode("unsigned"), .width(5)) comparator_2 (
    .a(exp), .b({5{1'b1}}), .eq(comparator_2_eq));  // open: gt, lt
  Comparator #(.mode("unsigned"), .width(5)) comparator_3 (
    .a(exp), .b({5{1'b0}}), .eq(comparator_3_eq));  // open: gt, lt
  Comparator #(.mode("unsigned"), .width(10)) comparator_4 (
    .a(mant), .b({10{1'b0}}), .gt(comparator_4_gt), .eq(comparator_4_eq));  // open: lt
  and and_1 (NaN, comparator_1_gt, comparator_2_eq);
  and and_2 (inf, comparator_1_eq, comparator_2_eq);
  nor nor_1 (norm, comparator_2_eq, comparator_3_eq);
  and and_3 (subnorm, comparator_3_eq, comparator_4_gt);
  and and_4 (_0, comparator_3_eq, comparator_4_eq);
endmodule

module Selector (
  input  [15:0] in,
  input  X0,
  input  Y0,
  input  Xsubn,
  input  Ysubn,
  input  Xnorm,
  input  Ynorm,
  input  Xinf,
  input  Yinf,
  input  Xsign,
  input  Ysign,
  input  XNaN,
  input  YNaN,
  output [15:0] out,
  output ovf,
  output inf,
  output NaN
);

  wire and_1_out, and_2_out, and_4_out, comparator_1_eq, nor_1_out, not_1_out, or_1_out, or_2_out, or_3_out,
       xor_1_out;
  wire [1:0] priority_encoder_1_out;

  and and_1 (and_1_out, Yinf, Xinf);
  xor xor_1 (xor_1_out, Xsign, Ysign);
  Comparator #(.mode("unsigned"), .width(5)) comparator_1 (
    .a(in[14:10]), .b({5{1'b1}}), .eq(comparator_1_eq));  // open: gt, lt
  or or_1 (or_1_out, X0, Y0, Xsubn, Ysubn, Xnorm, Ynorm);
  or or_2 (or_2_out, Xinf, Yinf);
  Multiplexer #(.enable("false")) multiplexer_1 (.in0(in[15]), .in1(1'b0), .out(out[15]), .sel(NaN));
  or or_3 (or_3_out, comparator_1_eq, or_2_out);
  and and_2 (and_2_out, and_1_out, xor_1_out);
  or or_4 (NaN, XNaN, and_2_out, YNaN);
  Priority_Encoder #(.select(2)) priority_encoder_1 (
    .in0(or_1_out), .in1(or_3_out), .in2(NaN), .out(priority_encoder_1_out));  // open: in3, gs, en_out, en_in
  nor nor_1 (nor_1_out, NaN, or_2_out);
  Multiplexer #(.enable("false"), .select(2), .width(15)) multiplexer_2 (
    .in0(in[14:0]), .in1(15'h7c00), .in2(15'h7e00), .out(out[14:0]), .sel(priority_encoder_1_out));  // open: in3
  and and_3 (ovf, nor_1_out, or_3_out);
  and and_4 (and_4_out, or_2_out, not_1_out);
  not not_1 (not_1_out, NaN);
  or or_5 (inf, ovf, and_4_out);
endmodule

module Sticky (
  input  [9:0] in,
  output sb
);

  or or_1 (sb, in[0], in[1], in[2], in[3], in[4], in[5], in[6], in[7], in[8], in[9]);
endmodule
