// Logisim project CORDIC.circ as structural Verilog: 6 circuits, main circuit Tester
module Tester (
);

  wire and_1_out, and_2_out, and_3_out, and_4_out, CLK_out, comparator_1_eq, comparator_1_gt,
       comparator_2_gt, comparator_2_lt, comparator_3_eq, comparator_4_eq, comparator_5_eq, comparator_6_eq,
       comparator_7_eq, comparator_8_eq, comparator_9_eq, cordic_1_done, DONE, ERR, INF, NaN, nand_1_out,
       nor_1_out, not_1_out, not_2_out, OK, or_1_out, register_1_q, register_2_q, register_3_q, RESET_out;
  wire [5:0] counter_2_q;
  wire [7:0] counter_1_q;
  wire [15:0] cordic_1_cos, cordic_1_sin, cordic_1_tan, rom_1_data, rom_2_data, rom_3_data, rom_4_data;

  Clock CLK (.out(CLK_out));
  not not_1 (not_1_out, DONE);
  not not_2 (not_2_out, OK);
  nand nand_1 (nand_1_out, not_2_out, comparator_1_eq);
  Button RESET (.out(RESET_out));
  and and_1 (and_1_out, CLK_out, not_1_out, nand_1_out);
  Counter counter_1 (
    .count(nand_1_out), .Q(counter_1_q), .clk(comparator_2_lt), .clr(RESET_out));  // open: load, D, carry
  LED u_DONE (.in(DONE));
  Counter #(.max('h2a), .width(6)) counter_2 (
    .Q(counter_2_q), .clk(and_1_out), .clr(RESET_out));  // open: load, D, count, carry
  LED ERROR (.in(ERR));
  ROM #(.dataWidth(16)) rom_1 (.addr(counter_1_q), .data(rom_1_data));
  LED u_INF (.in(INF));
  Comparator #(.mode("unsigned"), .width(6)) comparator_1 (
    .a(counter_2_q), .b(6'b100111), .gt(comparator_1_gt), .eq(comparator_1_eq));  // open: lt
  Comparator #(.mode("unsigned"), .width(6)) comparator_2 (
    .a(counter_2_q), .b(6'b000001), .gt(comparator_2_gt), .lt(comparator_2_lt));  // open: eq
  LED u_NaN (.in(NaN));
  // Probe on rom_1_data
  or or_1 (or_1_out, comparator_1_gt, RESET_out);
  ROM #(.dataWidth(16)) rom_2 (.addr(counter_1_q), .data(rom_2_data));
  CORDIC cordic_1 (
    .sin(cordic_1_sin), .NaN(NaN), .cos(cordic_1_cos), .tan(cordic_1_tan), .inf(INF), .done(cordic_1_done),
    .clk(and_1_out), .en(comparator_2_gt), .clear(or_1_out), .getTan(1'b1), .X(rom_1_data));
  Comparator #(.mode("unsigned"), .width(16)) comparator_3 (
    .a(rom_1_data), .b({16{1'b1}}), .eq(comparator_3_eq));  // open: gt, lt
  // Probe on cordic_1_sin
  // Probe on cordic_1_tan
  ROM #(.dataWidth(16)) rom_3 (.addr(counter_1_q), .data(rom_3_data));
  Comparator #(.mode("unsigned"), .width(16)) comparator_4 (
    .a(cordic_1_sin), .b(rom_2_data), .eq(comparator_4_eq));  // open: gt, lt
  Comparator #(.mode("unsigned"), .width(16)) comparator_5 (
    .a(rom_2_data), .b({16{1'b0}}), .eq(comparator_5_eq));  // open: gt, lt
  and and_2 (and_2_out, comparator_4_eq, cordic_1_done);
  // Probe on cordic_1_cos
  Comparator #(.mode("unsigned"), .width(16)) comparator_6 (
    .a(cordic_1_cos), .b(rom_3_data), .eq(comparator_6_eq));  // open: gt, lt
  ROM #(.dataWidth(16)) rom_4 (.addr(counter_1_q), .data(rom_4_data));
  Comparator #(.mode("unsigned"), .width(16)) comparator_7 (
    .a(rom_3_data), .b({16{1'b0}}), .eq(comparator_7_eq));  // open: gt, lt
  and and_3 (and_3_out, comparator_6_eq, cordic_1_done);
  Comparator #(.mode("unsigned"), .width(16)) comparator_8 (
    .a(cordic_1_tan), .b(rom_4_data), .eq(comparator_8_eq));  // open: gt, lt
  Comparator #(.mode("unsigned"), .width(16)) comparator_9 (
    .a(rom_4_data), .b({16{1'b0}}), .eq(comparator_9_eq));  // open: gt, lt
  and and_4 (and_4_out, comparator_8_eq, cordic_1_done);
  Register #(.width(1)) register_1 (.D(and_2_out), .Q(register_1_q), .clk(comparator_1_eq));  // open: en, clr
  Register #(.width(1)) register_2 (.D(and_3_out), .Q(register_2_q), .clk(comparator_1_eq));  // open: en, clr
  Register #(.width(1)) register_3 (.D(and_4_out), .Q(register_3_q), .clk(comparator_1_eq));  // open: en, clr
  and and_5 (OK, register_1_q, register_2_q, register_3_q);
  and and_6 (DONE, comparator_3_eq, comparator_5_eq, comparator_7_eq, comparator_9_eq);
  nor nor_1 (nor_1_out, OK, DONE);
  and and_7 (ERR, nor_1_out, comparator_1_eq);

  // Notes on the sheet:
  //   contents of rom_1 (hex, n*v repeats v):
  //   0 4500 4900 4b80 4d00 4e40 4f80 5060 5100 51a0 5240 52e0 5380 5410 5460 54b0 5500 5550 55a0 3e00
  //   5568 55f0 c900 7c00 7e00 ffff
  //   contents of rom_2 (hex, n*v repeats v):
  //   0 2d92 318f 3425 3578 36c3 37fb 3896 3925 39a8 3a22 3a8f 3aed 3b41 3b86 3bbb 3be2 3bf9 3c00 26b4
  //   3c00 4*7e00
  //   contents of rom_3 (hex, n*v repeats v):
  //   3c00 3bf9 3be2 3bbb 3b85 3b41 3aed 3a8d 3a20 39a8 3923 3894 37fd 36bd 3570 3425 318b 2d82 0 3c00
  //   2bc0 4*7e00
  //   contents of rom_4 (hex, n*v repeats v):
  //   0 2d97 31a4 344a 35d1 3775 389c 399a 3ab8 3c00 3cc7 3dbb 3ef0 404e 4189 4376 45b0 49ca 7c00 26b4
  //   4c21 4*7e00
endmodule

module CORDIC (
  input  [15:0] X,
  input  clk,
  input  en,
  input  clear,
  input  getTan,
  output [15:0] sin,
  output NaN,
  output [15:0] cos,
  output [15:0] tan,
  output inf,
  output done
);

  wire _0, _5, _5_85, _85, _90, and_1_out, divider_1_done, divider_1_inf, inf_t, invalid, NaN_t, not_1_out,
       trig_calc_1_done;
  wire [2:0] priority_encoder_1_out;
  wire [15:0] adder_subractor_1_x___y, divider_1_x_y, multiplexer_1_out, multiplexer_2_out, multiplier_1_x_y,
       trig_calc_1_cos, trig_calc_1_sin;

  Classifier classifier_1 (
    .inf(inf_t), .invalid(invalid), ._90(_90), ._85(_85), ._5_85(_5_85), ._5(_5), ._0(_0), .NaN(NaN_t),
    .val(X));
  Multiplier multiplier_1 (.X_Y(multiplier_1_x_y), .Y(16'h2478), .X(X));  // open: NaN, INF, UNF, OVF
  Trig_Calc trig_calc_1 (
    .done(trig_calc_1_done), .cos(trig_calc_1_cos), .sin(trig_calc_1_sin), .clear(clear), .clk(clk), .en(en),
    .X(X));
  not not_1 (not_1_out, getTan);
  and and_1 (and_1_out, trig_calc_1_done, not_1_out);
  or or_1 (done, and_1_out, divider_1_done);
  Adder_Subractor adder_subractor_1 (
    .X___Y(adder_subractor_1_x___y), .sub(1'b1), .X(16'h3e48), .Y(multiplier_1_x_y));  // open: ovf, inf, NaN
  Multiplexer #(.enable("false"), .select(3), .width(16)) multiplexer_1 (
    .in0({16{1'b0}}), .in1(multiplier_1_x_y), .in2(trig_calc_1_sin), .in3(16'h3c00), .in4(16'h3c00),
    .in5(16'h7e00), .out(multiplexer_1_out), .sel(priority_encoder_1_out));  // open: in6, in7
  Priority_Encoder priority_encoder_1 (
    .in0(_0), .in1(_5), .in2(_5_85), .in3(_85), .in4(_90), .in5(invalid), .out(priority_encoder_1_out));  // open: in6, in7, en_in, gs, en_out
  Multiplexer #(.enable("false"), .select(3), .width(16)) multiplexer_2 (
    .in0(16'h3c00), .in1(16'h3c00), .in2(trig_calc_1_cos), .in3(adder_subractor_1_x___y), .in4({16{1'b0}}),
    .in5(16'h7e00), .out(multiplexer_2_out), .sel(priority_encoder_1_out));  // open: in6, in7
  Divider divider_1 (
    .X_Y(divider_1_x_y), .INF(divider_1_inf), .done(divider_1_done), .Y(multiplexer_2_out),
    .X(multiplexer_1_out), .clk(clk), .en(trig_calc_1_done), .clear(clear));  // open: OVF, NaN, UNF
  Pull_Resistor pull_resistor_1 (.node(divider_1_inf));
  Selector selector_1 (.res(sin), .invalid(invalid), .inf(inf_t), .NaN(NaN_t), .in(multiplexer_1_out));
  or or_2 (NaN, NaN_t, inf_t, invalid);
  Selector selector_2 (.res(cos), .invalid(invalid), .inf(inf_t), .NaN(NaN_t), .in(multiplexer_2_out));
  Selector selector_3 (.res(tan), .invalid(invalid), .inf(inf_t), .NaN(NaN_t), .in(divider_1_x_y));
  and and_2 (inf, divider_1_inf, getTan);
endmodule

module Classifier (
  input  [15:0] val,
  output NaN,
  output inf,
  output invalid,
  output _90,
  output _85,
  output _5_85,
  output _5,
  output _0
);

  wire and_2_out, comparator_2_gt, comparator_2_lt, comparator_3_eq, comparator_3_gt, comparator_3_lt,
       comparator_4_eq, comparator_4_gt, comparator_4_lt, comparator_5_gt;

  Comparator #(.mode("unsigned"), .width(15)) comparator_1 (
    .a(val[14:0]), .b(15'h7c00), .gt(NaN), .eq(inf));  // open: lt
  Comparator #(.mode("unsigned"), .width(15)) comparator_2 (
    .a(val[14:0]), .b(15'h55a0), .gt(comparator_2_gt), .eq(_90), .lt(comparator_2_lt));
  Comparator #(.mode("unsigned"), .width(15)) comparator_3 (
    .a(val[14:0]), .b(15'h5550), .gt(comparator_3_gt), .eq(comparator_3_eq), .lt(comparator_3_lt));
  Comparator #(.mode("unsigned"), .width(15)) comparator_4 (
    .a(val[14:0]), .b(15'h4500), .gt(comparator_4_gt), .eq(comparator_4_eq), .lt(comparator_4_lt));
  Comparator #(.mode("unsigned"), .width(15)) comparator_5 (
    .a(val[14:0]), .b({15{1'b0}}), .gt(comparator_5_gt), .eq(_0));  // open: lt
  and and_1 (_85, comparator_2_lt, comparator_3_gt);
  and and_2 (and_2_out, comparator_3_lt, comparator_4_gt);
  and and_3 (_5, comparator_4_lt, comparator_5_gt);
  or or_1 (invalid, val[15], comparator_2_gt);
  or or_2 (_5_85, comparator_3_eq, and_2_out, comparator_4_eq);
endmodule

module Trig_Calc (
  input  [15:0] X,
  input  clear,
  input  clk,
  input  en,
  output [15:0] cos,
  output [15:0] sin,
  output done
);

  wire and_1_out, comparator_1_eq, comparator_1_gt, comparator_2_lt, nor_1_out, not_1_out, not_2_out;
  wire [3:0] counter_1_q;
  wire [15:0] adder_subractor_1_x___y, multiplexer_1_out, multiplexer_2_out, multiplexer_3_out, register_1_q,
       register_2_q, register_3_q, rom_1_data;
  wire [15:15] nextxy_2_c;

  not not_1 (not_1_out, done);
  Multiplexer #(.enable("false"), .width(16)) multiplexer_1 (
    .in0(cos), .in1(16'h38dc), .out(multiplexer_1_out), .sel(comparator_2_lt));
  Multiplexer #(.enable("false"), .width(16)) multiplexer_2 (
    .in0({nextxy_2_c[15], sin[14:0]}), .in1({16{1'b0}}), .out(multiplexer_2_out), .sel(comparator_2_lt));
  Multiplexer #(.enable("false"), .width(16)) multiplexer_3 (
    .in0(adder_subractor_1_x___y), .in1({16{1'b0}}), .out(multiplexer_3_out), .sel(comparator_2_lt));
  and and_1 (and_1_out, clk, not_1_out, en);
  Register #(.width(16)) register_1 (
    .D(multiplexer_1_out), .Q(register_1_q), .clk(and_1_out), .clr(clear));  // open: en
  Register #(.width(16)) register_2 (
    .D(multiplexer_2_out), .Q(register_2_q), .clk(and_1_out), .clr(clear));  // open: en
  Register #(.width(16)) register_3 (
    .D(multiplexer_3_out), .Q(register_3_q), .clk(and_1_out), .clr(clear));  // open: en
  Counter #(.max('hd), .ongoal("stay"), .width(4)) counter_1 (
    .Q(counter_1_q), .clk(and_1_out), .clr(clear));  // open: load, D, count, carry
  Comparator #(.mode("unsigned"), .width(16)) comparator_1 (
    .a(X), .b(register_3_q), .gt(comparator_1_gt), .eq(comparator_1_eq));  // open: lt
  nor nor_1 (nor_1_out, comparator_1_gt, comparator_1_eq);
  Comparator #(.mode("unsigned"), .width(4)) comparator_2 (
    .a(counter_1_q), .b(4'b0001), .lt(comparator_2_lt));  // open: gt, eq
  Comparator #(.mode("unsigned"), .width(4)) comparator_3 (.a(counter_1_q), .b(4'b1101), .eq(done));  // open: gt, lt
  not not_2 (not_2_out, nor_1_out);
  ROM #(.addrWidth(4), .dataWidth(16)) rom_1 (.addr(counter_1_q), .data(rom_1_data));
  NextXY nextxy_1 (.c(cos), .b(register_2_q), .sub(nor_1_out), .a(register_1_q), .n(counter_1_q));
  NextXY nextxy_2 (
    .c({nextxy_2_c[15], sin[14:0]}), .b(register_1_q), .sub(not_2_out), .a(register_2_q), .n(counter_1_q));
  Adder_Subractor adder_subractor_1 (
    .X___Y(adder_subractor_1_x___y), .sub(nor_1_out), .X(register_3_q), .Y(rom_1_data));  // open: ovf, inf, NaN
  not not_3 (sin[15], nextxy_2_c[15]);

  // Notes on the sheet:
  //   contents of rom_1 (hex, n*v repeats v):
  //   0 51a0 4ea4 4b05 4720 4327 3f29 3b29 3729 3329 2f29 2b29 2729
endmodule

module Selector (
  input  [15:0] in,
  input  invalid,
  input  inf,
  input  NaN,
  output [15:0] res
);

  wire or_1_out;

  or or_1 (or_1_out, invalid, inf, NaN);
  Multiplexer #(.enable("false"), .width(16)) multiplexer_1 (.in0(in), .in1(16'h7e00), .out(res), .sel(or_1_out));
endmodule

module NextXY (
  input  [15:0] a,
  input  [15:0] b,
  input  [3:0] n,
  input  sub,
  output [15:0] c
);

  wire comparator_1_lt, comparator_2_eq, or_1_out;
  wire [4:0] bit_extender_1_out, subtractor_1_out, subtractor_2_out;
  wire [15:0] multiplexer_1_out;

  assign bit_extender_1_out = {{1{1'b0}}, n};  // Bit_Extender bit_extender_1
  Subtractor #(.width(5)) subtractor_1 (
    .a(bit_extender_1_out), .b(5'b00001), .out(subtractor_1_out));  // open: bin, bout
  Subtractor #(.width(5)) subtractor_2 (.a(b[14:10]), .b(subtractor_1_out), .out(subtractor_2_out));  // open: bin, bout
  Comparator #(.width(5)) comparator_1 (.a(subtractor_2_out), .b({5{1'b0}}), .lt(comparator_1_lt));  // open: gt, eq
  Multiplexer #(.enable("false"), .width(16)) multiplexer_1 (
    .in0({b[15], subtractor_2_out, b[9:0]}), .in1({16{1'b0}}), .out(multiplexer_1_out), .sel(or_1_out));
  or or_1 (or_1_out, comparator_1_lt, comparator_2_eq);
  Comparator #(.mode("unsigned"), .width(16)) comparator_2 (
    .a(b), .b({16{1'b0}}), .eq(comparator_2_eq));  // open: gt, lt
  Adder_Subractor adder_subractor_1 (.X___Y(c), .sub(sub), .X(a), .Y(multiplexer_1_out));  // open: ovf, inf, NaN
endmodule
