// Logisim project Multiplier.circ as structural Verilog: 11 circuits, main circuit Multiplier
module Multiplier (
  input  [15:0] X,
  input  [15:0] Y,
  output [15:0] X_Y,
  output NaN,
  output INF,
  output UNF,
  output OVF
);

  wire adder_3_cout, adder_with_ovf_unf_1_minus_0, adder_with_ovf_unf_1_minus_inf,
       adder_with_ovf_unf_1_plus_0, adder_with_ovf_unf_1_plus_inf, nor_1_out, normal_1_norm, normal_2_norm,
       or_1_out, or_2_out, or_3_out, rounder_1_round, SUB, X0, Xinf, XNaN, Xnum, xor_1_out, Y0, Yinf, YNaN,
       Ynum;
  wire [0:0] shifter_1_mant_hi;
  wire [3:0] normaliser_1_lzc, normaliser_2_lzc;
  wire [4:0] bit_extender_2_out;
  wire [5:0] adder_2_out, adder_with_ovf_unf_1_sum, adjust_exponent_1_out, adjust_exponent_2_out, BIAS,
       multiplexer_1_out, multiplexer_2_out;
  wire [8:0] shifter_1_mant_hi_2;
  wire [9:0] adder_3_out, bit_extender_1_out;
  wire [10:0] multiplier_1_cout, multiplier_1_out, normaliser_1_out, normaliser_2_out, shifter_1_mant_lo;
  wire [14:0] bit_extender_3_out;

  Classifier classifier_1 (.inf(Xinf), .num(Xnum), ._0(X0), .NaN(XNaN), .val(X));
  Classifier classifier_2 (.inf(Yinf), .num(Ynum), ._0(Y0), .NaN(YNaN), .val(Y));
  xor xor_1 (xor_1_out, X[15], Y[15]);
  Normal normal_1 (.norm(normal_1_norm), .in(X[14:10]));
  Normal normal_2 (.norm(normal_2_norm), .in(Y[14:10]));
  Normaliser normaliser_1 (.out(normaliser_1_out), .lzc(normaliser_1_lzc), .in(X[9:0]), .norm(normal_1_norm));
  Normaliser normaliser_2 (.out(normaliser_2_out), .lzc(normaliser_2_lzc), .in(Y[9:0]), .norm(normal_2_norm));
  Multiplier_part #(.mode("unsigned"), .width(11)) multiplier_1 (
    .a(normaliser_1_out), .b(normaliser_2_out), .out(multiplier_1_out), .cout(multiplier_1_cout));  // open: cin
  Adjust_Exponent adjust_exponent_1 (
    .out(adjust_exponent_1_out), .lzc(normaliser_1_lzc), .in(X[14:10]), .norm(normal_1_norm));
  Adjust_Exponent adjust_exponent_2 (
    .out(adjust_exponent_2_out), .lzc(normaliser_2_lzc), .in(Y[14:10]), .norm(normal_2_norm));
  nor nor_1 (nor_1_out, X0, Y0);
  or or_1 (or_1_out, adder_with_ovf_unf_1_plus_0, adder_with_ovf_unf_1_minus_0);
  and and_1 (UNF, nor_1_out, or_1_out);
  Adder_With_OVF_UNF adder_with_ovf_unf_1 (
    .sum(adder_with_ovf_unf_1_sum), .plus_0(adder_with_ovf_unf_1_plus_0),
    .minus_0(adder_with_ovf_unf_1_minus_0), .plus_inf(adder_with_ovf_unf_1_plus_inf),
    .minus_inf(adder_with_ovf_unf_1_minus_inf), .b(adjust_exponent_2_out), .a(adjust_exponent_1_out),
    .sign(xor_1_out));
  Shifter shifter_1 (
    .Mant_Hi({shifter_1_mant_hi_2, shifter_1_mant_hi[0]}), .Mant_Lo(shifter_1_mant_lo),
    .Mult_Hi(multiplier_1_cout), .Bias(BIAS), .Mult_Lo(multiplier_1_out), .Sub(SUB));
  or or_2 (or_2_out, adder_with_ovf_unf_1_minus_inf, adder_with_ovf_unf_1_plus_inf);
  and and_2 (OVF, Ynum, Xnum, or_2_out);
  Adder #(.width(6)) adder_1 (.a(adder_with_ovf_unf_1_sum), .b(6'b001111), .out(BIAS));  // open: cin, cout
  Adder #(.width(6)) adder_2 (.a(adder_with_ovf_unf_1_sum), .b(6'b010000), .out(adder_2_out));  // open: cin, cout
  Subnormal subnormal_1 (.sub(SUB), .exp(adder_with_ovf_unf_1_sum));
  or or_3 (or_3_out, multiplier_1_cout[10], adder_3_cout);
  Multiplexer #(.enable("false"), .width(6)) multiplexer_1 (
    .in0(BIAS), .in1(adder_2_out), .out(multiplexer_1_out), .sel(or_3_out));
  Rounder rounder_1 (.Round(rounder_1_round), .Mant_Lo(shifter_1_mant_lo), .Mant_10(shifter_1_mant_hi[0]));
  Multiplexer #(.enable("false"), .width(6)) multiplexer_2 (
    .in0(multiplexer_1_out), .in1({6{1'b0}}), .out(multiplexer_2_out), .sel(SUB));
  assign bit_extender_1_out = {{9{1'b0}}, rounder_1_round};  // Bit_Extender bit_extender_1
  Bit_Extender #(.in_width(6), .out_width(5), .\type ("zero")) bit_extender_2 (
    .in(multiplexer_2_out), .out(bit_extender_2_out));
  Adder #(.width(10)) adder_3 (
    .a({shifter_1_mant_hi_2, shifter_1_mant_hi[0]}), .b(bit_extender_1_out), .out(adder_3_out),
    .cout(adder_3_cout));  // open: cin
  Selector selector_1 (
    .res(X_Y), .Xnum(Xnum), .X0(X0), .unf(UNF), .ovf(OVF), .Xinf(Xinf), .Yinf(Yinf), .Ynum(Ynum),
    .XNaN(XNaN), .YNaN(YNaN), .Y0(Y0), .sign(xor_1_out), .exp(bit_extender_2_out), .mant(adder_3_out));
  Bit_Extender #(.in_width(16), .out_width(15), .\type ("zero")) bit_extender_3 (.in(X_Y), .out(bit_extender_3_out));
  Comparator #(.mode("unsigned"), .width(15)) comparator_1 (
    .a(bit_extender_3_out), .b(15'h7c00), .gt(NaN), .eq(INF));  // open: lt
endmodule

module Classifier (
  input  [15:0] val,
  output NaN,
  output inf,
  output num,
  output _0
);

  wire comparator_1_eq, comparator_1_gt, comparator_1_lt, comparator_2_eq, comparator_2_gt;

  Comparator #(.mode("unsigned"), .width(15)) comparator_1 (
    .a(val[14:0]), .b(15'h7c00), .gt(comparator_1_gt), .eq(comparator_1_eq), .lt(comparator_1_lt));
  Comparator #(.mode("unsigned"), .width(15)) comparator_2 (
    .a(val[14:0]), .b({15{1'b0}}), .gt(comparator_2_gt), .eq(comparator_2_eq));  // open: lt
  Multiplexer #(.enable("false")) multiplexer_1 (.in0(comparator_1_gt), .in1(1'b0), .out(NaN), .sel(comparator_1_lt));
  Multiplexer #(.enable("false")) multiplexer_2 (.in0(comparator_1_eq), .in1(1'b0), .out(inf), .sel(comparator_1_lt));
  Multiplexer #(.enable("false")) multiplexer_3 (.in0(1'b0), .in1(comparator_2_gt), .out(num), .sel(comparator_1_lt));
  Multiplexer #(.enable("false")) multiplexer_4 (.in0(1'b0), .in1(comparator_2_eq), .out(_0), .sel(comparator_1_lt));
endmodule

module Adjust_Exponent (
  input  norm,
  input  [3:0] lzc,
  input  [4:0] in,
  output [5:0] out
);

  wire [5:0] adder_1_out, bit_extender_1_out, bit_extender_2_out, subtractor_1_out, subtractor_2_out;

  assign bit_extender_1_out = {{2{1'b0}}, lzc};  // Bit_Extender bit_extender_1
  assign bit_extender_2_out = {{1{1'b0}}, in};  // Bit_Extender bit_extender_2
  Adder #(.width(6)) adder_1 (.a(bit_extender_1_out), .b(6'b001110), .out(adder_1_out));  // open: cin, cout
  Subtractor #(.width(6)) subtractor_1 (.a({6{1'b0}}), .b(adder_1_out), .out(subtractor_1_out));  // open: bin, bout
  Subtractor #(.width(6)) subtractor_2 (
    .a(bit_extender_2_out), .b(6'b001111), .out(subtractor_2_out));  // open: bin, bout
  Multiplexer #(.width(6)) multiplexer_1 (
    .in0(subtractor_1_out), .in1(subtractor_2_out), .out(out), .sel(norm));  // open: en
endmodule

module Normaliser (
  input  norm,
  input  [9:0] in,
  output [10:0] out,
  output [3:0] lzc
);

  wire [3:0] bitfinder_1_index;
  wire [10:0] bit_extender_1_out, shifter_1_out;

  assign bit_extender_1_out = {{1{norm}}, in};  // Bit_Extender bit_extender_1
  BitFinder #(.\type ("high1"), .width(11)) bitfinder_1 (
    .in(bit_extender_1_out), .index(bitfinder_1_index));  // open: found
  Subtractor #(.width(4)) subtractor_1 (.a(4'b1010), .b(bitfinder_1_index), .out(lzc));  // open: bin, bout
  Shifter_part #(.width(11)) shifter_1 (.in(bit_extender_1_out), .\dist (lzc), .out(shifter_1_out));
  Multiplexer #(.width(11)) multiplexer_1 (
    .in0(shifter_1_out), .in1(bit_extender_1_out), .out(out), .sel(norm));  // open: en
endmodule

module Adder_With_OVF_UNF (
  input  [5:0] a,
  input  [5:0] b,
  input  sign,
  output [5:0] sum,
  output plus_0,
  output minus_0,
  output plus_inf,
  output minus_inf
);

  wire and_1_out, and_2_out, and_3_out, and_4_out, comparator_1_gt, comparator_2_gt, comparator_3_lt,
       comparator_4_lt, comparator_5_lt, comparator_6_gt;

  Adder #(.width(6)) adder_1 (.a(a), .b(b), .out(sum));  // open: cin, cout
  Comparator #(.mode("unsigned"), .width(6)) comparator_1 (.a(a), .b(6'b011111), .gt(comparator_1_gt));  // open: eq, lt
  Comparator #(.mode("unsigned"), .width(6)) comparator_2 (.a(b), .b(6'b011111), .gt(comparator_2_gt));  // open: eq, lt
  Comparator #(.mode("unsigned"), .width(6)) comparator_3 (.a(a), .b(6'b100000), .lt(comparator_3_lt));  // open: gt, eq
  Comparator #(.mode("unsigned"), .width(6)) comparator_4 (.a(b), .b(6'b100000), .lt(comparator_4_lt));  // open: gt, eq
  and and_1 (and_1_out, comparator_1_gt, comparator_2_gt);
  and and_2 (and_2_out, comparator_3_lt, comparator_4_lt);
  Comparator #(.mode("unsigned"), .width(6)) comparator_5 (
    .a(sum), .b(6'b101000), .lt(comparator_5_lt));  // open: gt, eq
  Comparator #(.mode("unsigned"), .width(6)) comparator_6 (
    .a(sum), .b(6'b001111), .gt(comparator_6_gt));  // open: eq, lt
  and and_3 (and_3_out, comparator_5_lt, and_1_out);
  and and_4 (and_4_out, comparator_6_gt, and_2_out);
  Demultiplexer demultiplexer_1 (.out0(plus_0), .out1(minus_0), .in(and_3_out), .sel(sign));  // open: en
  Demultiplexer demultiplexer_2 (.out0(plus_inf), .out1(minus_inf), .in(and_4_out), .sel(sign));  // open: en
endmodule

module Selector (
  input  sign,
  input  [4:0] exp,
  input  [9:0] mant,
  input  Xnum,
  input  X0,
  input  unf,
  input  ovf,
  input  Xinf,
  input  Yinf,
  input  Ynum,
  input  XNaN,
  input  YNaN,
  input  Y0,
  output [15:0] res
);

  wire and_1_out, and_2_out, and_3_out, or_1_out, or_2_out, or_3_out;
  wire [1:0] priority_encoder_1_out;

  and and_1 (and_1_out, Xnum, Ynum);
  or or_1 (or_1_out, X0, unf, Y0);
  or or_2 (or_2_out, Xinf, ovf, Yinf);
  and and_2 (and_2_out, Xinf, Y0);
  and and_3 (and_3_out, Yinf, X0);
  Multiplexer #(.enable("false")) multiplexer_1 (.in0(sign), .in1(1'b0), .out(res[15]), .sel(or_3_out));
  or or_3 (or_3_out, XNaN, YNaN, and_2_out, and_3_out);
  Priority_Encoder #(.select(2)) priority_encoder_1 (
    .in0(and_1_out), .in1(or_1_out), .in2(or_2_out), .in3(or_3_out), .out(priority_encoder_1_out));  // open: gs, en_out, en_in
  Multiplexer #(.enable("false"), .select(2), .width(15)) multiplexer_2 (
    .in0({exp, mant}), .in1({15{1'b0}}), .in2(15'h7c00), .in3(15'h7e00), .out(res[14:0]),
    .sel(priority_encoder_1_out));
endmodule

module Shifter (
  input  Sub,
  input  [10:0] Mult_Hi,
  input  [5:0] Bias,
  input  [10:0] Mult_Lo,
  output [9:0] Mant_Hi,
  output [10:0] Mant_Lo
);

  wire B21, not_2_out;
  wire [3:0] bit_extender_2_out, bit_extender_3_out;
  wire [5:0] subtractor_1_out, subtractor_2_out;
  wire [10:0] bit_extender_1_out, multiplexer_1_out, multiplexer_2_out, multiplexer_3_out, or_1_out,
       or_2_out, shifter_1_out, shifter_2_out, shifter_3_out, shifter_4_out, shifter_5_out;

  Subtractor #(.width(6)) subtractor_1 (.a({6{1'b0}}), .b(Bias), .out(subtractor_1_out));  // open: bin, bout
  Shifter_part #(.width(11)) shifter_1 (.in(Mult_Hi), .\dist (4'b0001), .out(shifter_1_out));
  assign bit_extender_1_out = {{10{1'b0}}, Mult_Lo[10]};  // Bit_Extender bit_extender_1
  Bit_Extender #(.in_width(6), .out_width(4), .\type ("zero")) bit_extender_2 (
    .in(subtractor_1_out), .out(bit_extender_2_out));
  not not_1 (B21, Mult_Hi[10]);
  assign or_1_out = shifter_1_out | bit_extender_1_out;  // OR_Gate or_1, 11 bits wide
  Subtractor #(.width(6)) subtractor_2 (
    .a(6'b001011), .b(subtractor_1_out), .out(subtractor_2_out));  // open: bin, bout
  Multiplexer #(.enable("false"), .width(11)) multiplexer_1 (
    .in0(Mult_Hi), .in1(or_1_out), .out(multiplexer_1_out), .sel(B21));
  Shifter_part #(.shift("lr"), .width(11)) shifter_2 (.in(Mult_Hi), .\dist (bit_extender_2_out), .out(shifter_2_out));
  Bit_Extender #(.in_width(6), .out_width(4), .\type ("zero")) bit_extender_3 (
    .in(subtractor_2_out), .out(bit_extender_3_out));
  Shifter_part #(.shift("lr"), .width(11)) shifter_3 (.in(Mult_Lo), .\dist (bit_extender_2_out), .out(shifter_3_out));
  Shifter_part #(.width(11)) shifter_4 (.in(Mult_Lo), .\dist (4'b0001), .out(shifter_4_out));
  Multiplexer #(.enable("false"), .width(11)) multiplexer_2 (
    .in0(multiplexer_1_out), .in1(shifter_2_out), .out(multiplexer_2_out), .sel(Sub));
  Shifter_part #(.width(11)) shifter_5 (.in(Mult_Hi), .\dist (bit_extender_3_out), .out(shifter_5_out));
  Multiplexer #(.enable("false"), .width(11)) multiplexer_3 (
    .in0(Mult_Lo), .in1(shifter_4_out), .out(multiplexer_3_out), .sel(B21));
  Bit_Extender #(.in_width(11), .out_width(10), .\type ("zero")) bit_extender_4 (.in(multiplexer_2_out), .out(Mant_Hi));
  assign or_2_out = shifter_5_out | shifter_3_out;  // OR_Gate or_2, 11 bits wide
  not not_2 (not_2_out, Sub);
  Multiplexer #(.enable("false"), .width(11)) multiplexer_4 (
    .in0(or_2_out), .in1(multiplexer_3_out), .out(Mant_Lo), .sel(not_2_out));
endmodule

module Rounder (
  input  Mant_10,
  input  [10:0] Mant_Lo,
  output Round
);

  wire or_1_out, sticky_1_out;

  Sticky sticky_1 (.out(sticky_1_out), .in(Mant_Lo[9:0]));
  or or_1 (or_1_out, Mant_10, sticky_1_out);
  and and_1 (Round, or_1_out, Mant_Lo[10]);
endmodule

module Normal (
  input  [4:0] in,
  output norm
);

  or or_1 (norm, in[0], in[1], in[2], in[3], in[4]);
endmodule

module Subnormal (
  input  [5:0] exp,
  output sub
);

  wire comparator_1_lt, comparator_2_gt;

  Comparator #(.mode("unsigned"), .width(6)) comparator_1 (
    .a(exp), .b(6'b110010), .lt(comparator_1_lt));  // open: gt, eq
  Comparator #(.mode("unsigned"), .width(6)) comparator_2 (
    .a(exp), .b(6'b100111), .gt(comparator_2_gt));  // open: eq, lt
  and and_1 (sub, comparator_1_lt, comparator_2_gt);
endmodule

module Sticky (
  input  [9:0] in,
  output out
);

  or or_1 (out, in[0], in[1], in[2], in[3], in[4], in[5], in[6], in[7], in[8], in[9]);
endmodule
