// Logisim project SAL-16V-D.circ as structural Verilog
module User_Panel (
  input  [15:0] IN
);

  wire CLK, DONE, ENTER, ERR, KBD_C, RESET, TTY_C, WAIT;
  wire [6:0] KBD_D, TTY_D;
  wire [15:0] FP, IDX, IR, LR, OUT, PC, R0, R1, R2, R3, R4, SP;

  Hex_Digit_Display hex_digit_display_1 (.value(R0[15:12]));  // open: dp
  Hex_Digit_Display hex_digit_display_2 (.value(IDX[15:12]));  // open: dp
  TTY #(.rows(10)) tty_1 (.data(TTY_D), .clk(TTY_C), .we(1'b1), .clr(RESET));
  Keyboard keyboard_1 (.clk(KBD_C), .re(1'b1), .clr(RESET), .data(KBD_D));  // open: avail
  Hex_Digit_Display hex_digit_display_3 (.value(R0[11:8]));  // open: dp
  Hex_Digit_Display hex_digit_display_4 (.value(R0[7:4]));  // open: dp
  Hex_Digit_Display hex_digit_display_5 (.value(IDX[11:8]));  // open: dp
  Hex_Digit_Display hex_digit_display_6 (.value(IDX[7:4]));  // open: dp
  Hex_Digit_Display hex_digit_display_7 (.value(IN[15:12]));  // open: dp
  Hex_Digit_Display hex_digit_display_8 (.value(R0[3:0]));  // open: dp
  Hex_Digit_Display hex_digit_display_9 (.value(IDX[3:0]));  // open: dp
  Hex_Digit_Display hex_digit_display_10 (.value(IN[11:8]));  // open: dp
  Hex_Digit_Display hex_digit_display_11 (.value(IN[7:4]));  // open: dp
  Hex_Digit_Display hex_digit_display_12 (.value(R1[15:12]));  // open: dp
  Hex_Digit_Display hex_digit_display_13 (.value(R1[11:8]));  // open: dp
  Hex_Digit_Display hex_digit_display_14 (.value(FP[15:12]));  // open: dp
  Hex_Digit_Display hex_digit_display_15 (.value(FP[11:8]));  // open: dp
  LED u_WAIT (.in(WAIT));
  Hex_Digit_Display hex_digit_display_16 (.value(IN[3:0]));  // open: dp
  Hex_Digit_Display hex_digit_display_17 (.value(R1[7:4]));  // open: dp
  Hex_Digit_Display hex_digit_display_18 (.value(R1[3:0]));  // open: dp
  Hex_Digit_Display hex_digit_display_19 (.value(FP[7:4]));  // open: dp
  Hex_Digit_Display hex_digit_display_20 (.value(FP[3:0]));  // open: dp
  Button u_ENTER (.out(ENTER));
  Hex_Digit_Display hex_digit_display_21 (.value(R2[15:12]));  // open: dp
  Hex_Digit_Display hex_digit_display_22 (.value(LR[15:12]));  // open: dp
  Button u_RESET (.out(RESET));
  Hex_Digit_Display hex_digit_display_23 (.value(R2[11:8]));  // open: dp
  Hex_Digit_Display hex_digit_display_24 (.value(R2[7:4]));  // open: dp
  Hex_Digit_Display hex_digit_display_25 (.value(LR[11:8]));  // open: dp
  Hex_Digit_Display hex_digit_display_26 (.value(LR[7:4]));  // open: dp
  LED u_DONE (.in(DONE));
  Hex_Digit_Display hex_digit_display_27 (.value(OUT[15:12]));  // open: dp
  Hex_Digit_Display hex_digit_display_28 (.value(R2[3:0]));  // open: dp
  Hex_Digit_Display hex_digit_display_29 (.value(LR[3:0]));  // open: dp
  LED u_ERR (.in(ERR));
  Hex_Digit_Display hex_digit_display_30 (.value(OUT[11:8]));  // open: dp
  Hex_Digit_Display hex_digit_display_31 (.value(OUT[7:4]));  // open: dp
  Hex_Digit_Display hex_digit_display_32 (.value(R3[15:12]));  // open: dp
  Hex_Digit_Display hex_digit_display_33 (.value(R3[11:8]));  // open: dp
  Hex_Digit_Display hex_digit_display_34 (.value(SP[15:12]));  // open: dp
  Hex_Digit_Display hex_digit_display_35 (.value(SP[11:8]));  // open: dp
  LED u_CLK (.in(CLK));
  Logo logo_1 ();
  Hex_Digit_Display hex_digit_display_36 (.value(OUT[3:0]));  // open: dp
  Hex_Digit_Display hex_digit_display_37 (.value(R3[7:4]));  // open: dp
  Hex_Digit_Display hex_digit_display_38 (.value(R3[3:0]));  // open: dp
  Hex_Digit_Display hex_digit_display_39 (.value(SP[7:4]));  // open: dp
  Hex_Digit_Display hex_digit_display_40 (.value(SP[3:0]));  // open: dp
  Hex_Digit_Display hex_digit_display_41 (.value(R4[15:12]));  // open: dp
  Hex_Digit_Display hex_digit_display_42 (.value(R4[11:8]));  // open: dp
  Hex_Digit_Display hex_digit_display_43 (.value(PC[15:12]));  // open: dp
  Hex_Digit_Display hex_digit_display_44 (.value(PC[11:8]));  // open: dp
  Hex_Digit_Display hex_digit_display_45 (.value(R4[7:4]));  // open: dp
  Hex_Digit_Display hex_digit_display_46 (.value(R4[3:0]));  // open: dp
  Hex_Digit_Display hex_digit_display_47 (.value(PC[7:4]));  // open: dp
  Hex_Digit_Display hex_digit_display_48 (.value(PC[3:0]));  // open: dp
  Hex_Digit_Display hex_digit_display_49 (.value(IR[15:12]));  // open: dp
  Hex_Digit_Display hex_digit_display_50 (.value(IR[11:8]));  // open: dp
  Hex_Digit_Display hex_digit_display_51 (.value(IR[7:4]));  // open: dp
  Hex_Digit_Display hex_digit_display_52 (.value(IR[3:0]));  // open: dp
  Computer computer_1 (
    .OUT(OUT), .R0(R0), .R1(R1), .R2(R2), .R3(R3), .R4(R4), .IDX(IDX), .WAIT(WAIT), .SP(SP), .PC(PC),
    .IR(IR), .FP(FP), .LR(LR), .END(DONE), .TTY_DATA(TTY_D), .KBD_CLK(KBD_C), .TTY_CLK(TTY_C), .IN(IN),
    .RESET(RESET), .KBD_DATA(KBD_D), .ENTER(ENTER), .CLK(CLK), .ERR(ERR));

  // Notes on the sheet:
  //   DISPLAY
  //   KEYBOARD
  //   INPUTS
  //   REGISTERS
  //   i
  //   GENERAL PURPOSE REGISTERS
  //   DEDICATED REGISTERS
  //   CONTROLS & INDICATORS
  //   OUTPUTS
  //   (or Error Code)
  //   NOTES & COMPUTER
  //   g
  //   then set up IN_x and press ENTER_x.
  //   NOTES
  //   1. Ensure that MicrocodeLUT.uc is in the control unit's LUT.
  //   2. Ensure that Microcode.uc is in the control unit's ROM.
  //   3. Ensure that TimmiOS.mc is in the computer's ROM.
  //   4. Ensure that the program is in the computer's RAM.
  //   5. Press the RESET button to initilaise the computer.
  //   6. Set 'Auto-Tick Frequency' to 8MHz, then select 'Auto-Tick Enabled'.
  //   7. If any IN_x input is required the WAIT_x led will turn red,
  //   8. The Program has completed when END turns green.
  //   9. Press the RESET button to re-run the program.
  //   COMPUTER
endmodule

module Computer (
  input  RESET,
  input  ENTER,
  input  [6:0] KBD_DATA,
  input  [15:0] IN,
  output END,
  output CLK,
  output [15:0] R0,
  output [15:0] R1,
  output [15:0] SP,
  output [15:0] R2,
  output [15:0] R3,
  output KBD_CLK,
  output [15:0] PC,
  output [15:0] R4,
  output [15:0] IR,
  output [15:0] IDX,
  output [15:0] FP,
  output [15:0] LR,
  output [6:0] TTY_DATA,
  output TTY_CLK,
  output [15:0] OUT,
  output WAIT,
  output ERR
);

  wire address_decoder_1_i_o, address_decoder_1_ram, address_decoder_1_rom, and_1_out, and_2_out,
       cpu_1_ld_gr, cpu_1_mem_e, cpu_1_mem_s, not_1_out;
  wire [0:0] register_1_q;
  wire [14:0] output_device_2_data, output_device_3_data;
  wire [15:0] cpu_1_bus_out, cpu_1_mem_addr, kbd_controller_1_bus_out, ram_1_dout, rom_1_data;

  Clock_part CLK_IN (.out(CLK));
  CPU cpu_1 (
    .out_5(R0), .out_6(R1), .out_7(R2), .out_22(PC), .out_8(R3), .out_9(R4), .out_23(IR), .out_10(IDX),
    .out_11(FP), .ld_gr(cpu_1_ld_gr), .mem_s(cpu_1_mem_s), .mem_e(cpu_1_mem_e), .\end (END), .out_21(SP),
    .out_12(LR), .mem_addr(cpu_1_mem_addr), .bus_out(cpu_1_bus_out), .bus_in(kbd_controller_1_bus_out),
    .reset(RESET), .clkin(CLK));  // open: clk, clks, clke
  Address_Decoder address_decoder_1 (
    .i_o(address_decoder_1_i_o), .ram(address_decoder_1_ram), .rom(address_decoder_1_rom),
    .ld_gr(cpu_1_ld_gr), .addr(cpu_1_mem_addr));
  ROM #(.addrWidth(15), .dataWidth(16)) rom_1 (.addr(cpu_1_mem_addr[14:0]), .data(rom_1_data));
  RAM #(.addrWidth(15), .dataWidth(16)) ram_1 (
    .addr(cpu_1_mem_addr[14:0]), .we(address_decoder_1_ram), .clk(cpu_1_mem_s), .din(cpu_1_bus_out),
    .dout(ram_1_dout));
  KBD_Controller kbd_controller_1 (
    .bus_out(kbd_controller_1_bus_out), .kbd_clk(KBD_CLK), .id(4'b0001), .addr(cpu_1_mem_addr[3:0]),
    .data(KBD_DATA), .reset(RESET), .clk_e(cpu_1_mem_e), .en(address_decoder_1_i_o));
  TTY_Controller tty_controller_1 (
    .data(TTY_DATA), .clk(TTY_CLK), .id(4'b0010), .addr(cpu_1_mem_addr[3:0]), .bus_in(cpu_1_bus_out),
    .clk_s(cpu_1_mem_s), .en(address_decoder_1_i_o));
  assign kbd_controller_1_bus_out = and_1_out ? rom_1_data : 16'bz;  // Controlled_Buffer controlled_buffer_1
  and and_1 (and_1_out, address_decoder_1_rom, cpu_1_mem_e);
  assign kbd_controller_1_bus_out = and_2_out ? ram_1_dout : 16'bz;  // Controlled_Buffer controlled_buffer_2
  and and_2 (and_2_out, address_decoder_1_ram, cpu_1_mem_e);
  Graphics_Unit graphics_unit_1 (
    .clk(CLK), .en_ld(cpu_1_ld_gr), .set(cpu_1_mem_s), .reset(RESET), .pos(cpu_1_mem_addr),
    .col(cpu_1_bus_out));
  Input_Device input_device_1 (
    .bus_out(kbd_controller_1_bus_out), .id(4'b0011), .addr(cpu_1_mem_addr[3:0]), .data(IN), .reset(RESET),
    .clk_e(cpu_1_mem_e), .en(address_decoder_1_i_o));
  Output_Device output_device_1 (
    .data(OUT), .id(4'b0110), .addr(cpu_1_mem_addr[3:0]), .bus_in(cpu_1_bus_out), .reset(RESET),
    .clk_s(cpu_1_mem_s), .en(address_decoder_1_i_o));
  Input_Device input_device_2 (
    .bus_out(kbd_controller_1_bus_out), .id(4'b0101), .addr(cpu_1_mem_addr[3:0]),
    .data({{15{1'b0}}, register_1_q[0]}), .reset(RESET), .clk_e(cpu_1_mem_e), .en(address_decoder_1_i_o));
  Output_Device output_device_2 (
    .data({output_device_2_data, WAIT}), .id(4'b0100), .addr(cpu_1_mem_addr[3:0]), .bus_in(cpu_1_bus_out),
    .reset(RESET), .clk_s(cpu_1_mem_s), .en(address_decoder_1_i_o));
  Register #(.width(1)) register_1 (.D(1'b1), .Q(register_1_q[0]), .clk(ENTER), .clr(not_1_out));  // open: en
  not not_1 (not_1_out, WAIT);
  Output_Device output_device_3 (
    .data({output_device_3_data, ERR}), .id(4'b0000), .addr(cpu_1_mem_addr[3:0]), .bus_in(cpu_1_bus_out),
    .reset(RESET), .clk_s(cpu_1_mem_s), .en(address_decoder_1_i_o));

  // Notes on the sheet:
  //   contents of rom_1 (hex, n*v repeats v):
  //   compressed eJy9WkmihCgM3ecUrP8KEBWPo6j3P0InTAIGy1/9uzdVKpjxZQCxUgor8UcKTRdiH+l6gnSt9Q/O
  //   MDRtoB9NPwp/DJznaYQV+DcKR38DvqkETjOgtcL3pcUHVk5C78IRRRoTmgjNFmfhj6Urhz84f55x
  //   QA8/iQPRnMC/Q9Pj+PRzk8WSLCoIoYVbNDKhwV1qLwCxIzou0rnYEsVB/ZQ6acFynIjPGO0ABW+y
  //   nqE3rFijCIDKBIn2zQh37FZo4+VxUR53wi5NvNk34YUb7GrEOgaiNMWtxophXb008ia8VXSrLAQx
  //   7U8hYempIFOQZZsczlyt2PUU2SuUdtAysPaOV4HFnZnnM//gLLoqbMIAhIQnQ8hgBSSP7IJZkLUE
  //   d54OLXIkKYY96O5w4i4nCeHxtMXXyC945QhMaVwJNeK4Q9jtY6CEj2Z8hMMikUXLSnHIoO9G45CQ
  //   MfvZh9aLsKsk6jOy8sYh+ot///SEHGqymyzurGHT+MZKChvNukd6swH5iK4i3rxXL93IazMZ/tGa
  //   HmaolTcEkkONPM6tTRBXjqjJFdQ6o7XRSgN5dqMXV/82OgECSBWaw8ziUGbEKyKzOBwjRjgwiHWX
  //   yVhblHXdkQCYYGwPx4RmtLgbxD4cyWVuEmQsdJcsKbkjgGsLg2G8BjbUlhON5fT4zljewgZWjyXl
  //   mSkToKdsMKFHnx69GsmnWg4eWf4OtFoD4o6Yxjah1SIu5OAdeOQoEp/GPISuu0ASPHweERKj+NJz
  //   iXpyIdbmngYGejbRUR4k5O/a10C+Fpyv9bgHoceUwbQHjQcM+R0av2tMJuT3yHk6hYOb3/U8B6rT
  //   KCTwfv8QMWqq7ZEMACH50mSUUwt9rJTugmpaAT5U9DDZx4gh3I7oRHBBhGB+wwNO1bmOiUnPnUgF
  //   YTzR7hWqFqWMt0G+eJtqIgatonTseZDgaTTB+ITBbjbdFBTiH/1AMi5hQJWwPWNu9pC8SHscXRUT
  //   kweJG+ULrDClRL5Bi2DgQpY9z9aMiFUqutQgscODo6R1QGWoRtOsHXjtlIzaDXqK4a8LQ9y1G5fL
  //   +lDwODge3gtQeUFmUWU2RQSXDxm8wlGJQNKLH2xoU6fUOJ11dTQJKTqoKULph8XqXCfHJ6wGw3zC
  //   qhhqF2jW/p+w6hWAR6yWRqiwOmzy8mbhgNabuwqYY7E6JFBi7LFYHRgRb1gNc3pYveGIxSo2qhVW
  //   jxarwaKNdkYtjfUZPNVYLYBfYTVHM8geVmnwCasx6J6xih6Z4A1WfV6FbsPzK8D+9bx7ALTJ+nMA
  //   yAwtI3qxVGTqB1KQQXglneSeKzSYjI9WXAZgcNZGkVk3KDESZAwYgYARrJz0zAW0DPYyF0xmYwvS
  //   YzVCptv6phqZXdfV6Mq1Xkpv4lI27S7ZBMpWa1bFbydtXEEQjL9njmMTMbTWCC84EStaerAB77HP
  //   ZRpblDeGGX3vA5LJWjHsSbo2m7lSyxNYydq0dUmm5zdpaxz2e/mHW0r1xsryxcy2iaYzsL0qUlu2
  //   Y81JjOM7a86ysGbgtopbJwNVUvVzihdyW6Mq4WtrExoXqdM7U5hCK2XwMDuusTmMFU/GtnFaSg4L
  //   9MzT6ZrQPIt90zVdMT4XBa+DGVwuFJhZDw4zngEU9kcDJ5sVoIS2/tRJBEZc0HxOcDDue47ytrfc
  //   CoWYWlqWuR1ymRuPvU4VkSL4GHuszsENTC8x3yhN7ynNVwme9FnJVnYnfdmg1fa490xws9srSvtd
  //   y5LS+J7SzPRehYBckoYUKL9vwZerBR8tUpzZlkb9pqWhYpSrTlvKyOttKat6t6Iupxdi7YNcl8u+
  //   NxZyYF7Ihbyuj8VKhq38ubqOP9x6PezhXsvm3tZF3d7VtbhdYOXG1/A4oXSTO+vplG/SzYwrqlpv
  //   SHpLzlAQXSEZFMFT1ohtoA/LI5pu4mE01TsON9zElXdZP8o9jjWIojr7GQ1IeWhG4FDVX/wmdW4F
  //   F2XM1aRC2lVpBbg2VIDV0dbw+IyM37fsRf+Tq2RRmPPsb9rwo11P5VILLDQ5Gvs9rfKRei3L2t0K
  //   trB72aG/HM98geF7pRQo+eqvtXStpYry09NS/4GWmS8wfDtaylrLpjHuNJZg6fvC59ZjNQe7OnqR
  //   O9o9lHplXoh330ChANPtBgpHJTdw3eWInQemgS6m+i9L6bvMhHpQfznF/pLuXvSXdhm5on5Gt5Gz
  //   5uHSIOdUu5nWgzirbeZ6UX3r5vOyL0DdlJ6LWJ2nLAa7wqtWCxyAcuttnXmzOLfuyLlPRDTV2Qf4
  //   SGHbxHYjt+w2OztXHBnHJzEaAd3dXkqtz2OEf9pW3HNI6I7ZX0WWKyNr7+QK6GTi/8fytSFuvTDj
  //   A7hpcO+F28r1TR3s6dLPnQxBeNalXEz1tit7gdemRh9mV0gtiyq+3naT0mocU3wfA+Vh6fOquv2H
  //   ju6Gx7e+/qob4IPtXdvzn1r+dV/xkC7urQXjg2/Cg/UBPOpS9OnPeIIHXeLaZwnFx+pdLPyuvv7b
  //   r6XcPFWua2W7D3ZtKUIz+3d+Ptr+sYeaV59rd+itF95vOjl4jh2R9gVs9lu1fdB+d+YVYVlvfDO9
  //   /eslwwe4b/fFAzB8vyoF9e7wpuY3nxmd5cK32kZ6yETnvcVM+6dcQ11sU2yDa9cYqfdkm/iSULVz
  //   vxlusVKYJDfx0S7j5pt4yHePnWo4/rNN9b5j6QcDbBPv88pmj9aDd9O+/NhWN/EZMMlz9yb+2mz6
  //   4tQBmmZpt7fZVmJbr00Nuvj7Ruz7DQn362aOJbO9qPEpiLlU9ZuO/oNV/kKUx3xSiNK0lg4TSm4t
  //   HxLKfDDroS7mXi+J3vZ8H5ZE/ZLxicb2YllF06Bjeg/DP1gl/ms5PMzkjGmL3631B/V0BoAy8Viq
  //   W+OhN/psFw+YHrSXOvtTjr5bkp3zup4UZeJwZFfTqeC0lYKj7gzQSgeFwbm5d7ywOrL7fL5UTArw
  //   HX9eEi3pDy2X/F1M77vcvZ4kDUF+LbZ58A4OZbHpWlZZnmQ+GtmgPeJ5HWAOJ5bNCesSsisdLR3E
  //   aq87FanN/pTmTxNWdBR4jGd2yY2jBKoj3tHxBDoNwj+pHO0v
endmodule

module CPU (
  input  [15:0] bus_in,
  input  reset,
  input  clkin,
  output [15:0] bus_out,
  output [15:0] out_5,
  output [15:0] out_6,
  output [15:0] out_7,
  output [15:0] out_8,
  output [15:0] out_9,
  output [15:0] out_10,
  output [15:0] out_11,
  output [15:0] out_12,
  output [15:0] mem_addr,
  output clk,
  output clks,
  output clke,
  output ld_gr,
  output mem_s,
  output mem_e,
  output \end ,
  output [15:0] out_21,
  output [15:0] out_22,
  output [15:0] out_23
);

  wire and_1_out, ASR, control_1_acc_e, control_1_acc_s, control_1_flags_s, control_1_fp_e, control_1_fp_s,
       control_1_idx_e, control_1_idx_s, control_1_ir_s, control_1_lr_e, control_1_lr_id, control_1_lr_s,
       control_1_mar_s, control_1_math_e, control_1_op0, control_1_op1, control_1_op2, control_1_pc_e,
       control_1_pc_s, control_1_plus1_e, control_1_r0_e, control_1_r0_s, control_1_r1_e, control_1_r1_s,
       control_1_r2_e, control_1_r2_s, control_1_r3_e, control_1_r3_s, control_1_r4_e, control_1_r4_s,
       control_1_sp_e, control_1_sp_id, control_1_sp_s, control_1_tmp_s, not_1_out;
  wire [1:0] n16_bit_register_9_dout;
  wire [5:0] alu_1_v, maths_unit_1_v, multiplexer_1_out, n6_bit_register_1_dout;
  wire [13:0] n16_bit_register_9_dout_2;
  wire [15:0] alu_1_c, maths_unit_1_c, multiplexer_2_out, n16_bit_register_1_dout, set_to_one_1_b;

  Set_To_One set_to_one_1 (.B(set_to_one_1_b), .A(n16_bit_register_1_dout), .S(control_1_plus1_e));
  _16_Bit_Register u_16_bit_register_1 (
    .Dout(n16_bit_register_1_dout), .Din(bus_in), .R(1'b1), .W(control_1_tmp_s), .Reset(reset));  // open: Cont
  ALU alu_1 (
    .C(alu_1_c), .EQ(alu_1_v[3]), .Z(alu_1_v[2]), .N(alu_1_v[1]), .Co(alu_1_v[5]), .GT(alu_1_v[4]),
    .asr(ASR), .lr_id(control_1_lr_id), .Op2(control_1_op2), .Op1(control_1_op1), .Op0(control_1_op0),
    .B(set_to_one_1_b), .A(bus_in), .V(alu_1_v[0]), .fcmp(1'b0));
  Maths_Unit maths_unit_1 (
    .C(maths_unit_1_c), .Z(maths_unit_1_v[2]), .N(maths_unit_1_v[1]), .Co(maths_unit_1_v[5]),
    .B(n16_bit_register_1_dout), .A(bus_in), .op(n16_bit_register_9_dout), .V(maths_unit_1_v[0]));
  not not_1 (not_1_out, \end );
  and and_1 (and_1_out, not_1_out, clkin);
  Multiplexer #(.enable("false"), .width(6)) multiplexer_1 (
    .in0(alu_1_v), .in1({maths_unit_1_v[5], alu_1_v[4:3], maths_unit_1_v[2:0]}), .out(multiplexer_1_out),
    .sel(control_1_math_e));
  Multiplexer #(.enable("false"), .width(16)) multiplexer_2 (
    .in0(alu_1_c), .in1(maths_unit_1_c), .out(multiplexer_2_out), .sel(control_1_math_e));
  Clock clock_1 (.clkin(and_1_out), .reset(reset), .clk(clk), .clke(clke), .clks(clks), .init(clkin));
  _6_Bit_Register u_6_bit_register_1 (
    .Dout(n6_bit_register_1_dout), .Din(multiplexer_1_out), .R(1'b1), .W(control_1_flags_s), .Reset(reset));  // open: Cont
  _16_Bit_Register u_16_bit_register_2 (
    .Dout(bus_in), .Cont(out_5), .Din(bus_in), .R(control_1_r0_e), .W(control_1_r0_s), .Reset(reset));
  _16_Bit_Register u_16_bit_register_3 (
    .Dout(bus_in), .Cont(out_6), .Din(bus_in), .R(control_1_r1_e), .W(control_1_r1_s), .Reset(reset));
  _16_Bit_Register u_16_bit_register_4 (
    .Dout(bus_in), .Din(multiplexer_2_out), .R(control_1_acc_e), .W(control_1_acc_s), .Reset(reset));  // open: Cont
  _16_Bit_Register u_16_bit_register_5 (
    .Dout(bus_in), .Cont(out_7), .Din(bus_in), .R(control_1_r2_e), .W(control_1_r2_s), .Reset(reset));
  _16_Bit_Register u_16_bit_register_6 (
    .Dout(bus_in), .Cont(out_8), .Din(bus_in), .R(control_1_r3_e), .W(control_1_r3_s), .Reset(reset));
  _16_Bit_Register u_16_bit_register_7 (
    .Dout(bus_in), .Cont(out_22), .Din(bus_in), .R(control_1_pc_e), .W(control_1_pc_s), .Reset(reset));
  _16_Bit_Register u_16_bit_register_8 (
    .Dout(bus_in), .Cont(out_9), .Din(bus_in), .R(control_1_r4_e), .W(control_1_r4_s), .Reset(reset));
  _16_Bit_Register u_16_bit_register_9 (
    .Dout({n16_bit_register_9_dout_2, n16_bit_register_9_dout}), .Cont(out_23), .Din(bus_in), .R(1'b1),
    .W(control_1_ir_s), .Reset(reset));
  _16_Bit_Register u_16_bit_register_10 (
    .Dout(bus_in), .Cont(out_10), .Din(bus_in), .R(control_1_idx_e), .W(control_1_idx_s), .Reset(reset));
  Control control_1 (
    .r3_s(control_1_r3_s), .r4_s(control_1_r4_s), .idx_s(control_1_idx_s), .fp_s(control_1_fp_s),
    .lr_s(control_1_lr_s), .sp_id(control_1_sp_id), .ld_gr(ld_gr), .\end (\end ), .ir_s(control_1_ir_s),
    .mar_s(control_1_mar_s), .pc_s(control_1_pc_s), .acc_s(control_1_acc_s), .mem_s(mem_s),
    .tmp_s(control_1_tmp_s), .flags_s(control_1_flags_s), .sp_s(control_1_sp_s), .r0_s(control_1_r0_s),
    .r1_s(control_1_r1_s), .r2_s(control_1_r2_s), .asr(ASR), .lr_e(control_1_lr_e), .lr_id(control_1_lr_id),
    .op0(control_1_op0), .op1(control_1_op1), .op2(control_1_op2), .plus1_e(control_1_plus1_e),
    .pc_e(control_1_pc_e), .mem_e(mem_e), .acc_e(control_1_acc_e), .sp_e(control_1_sp_e),
    .r0_e(control_1_r0_e), .r1_e(control_1_r1_e), .r2_e(control_1_r2_e), .r3_e(control_1_r3_e),
    .r4_e(control_1_r4_e), .idx_e(control_1_idx_e), .fp_e(control_1_fp_e), .clks(clks), .clk(clk),
    .clke(clke), .reset(reset), .ir({n16_bit_register_9_dout_2, n16_bit_register_9_dout}),
    .c(n6_bit_register_1_dout[5]), .a(n6_bit_register_1_dout[4]), .e(n6_bit_register_1_dout[3]),
    .z(n6_bit_register_1_dout[2]), .n(n6_bit_register_1_dout[1]), .v(n6_bit_register_1_dout[0]),
    .math_e(control_1_math_e));
  _16_Bit_Register u_16_bit_register_11 (
    .Dout(bus_in), .Cont(out_11), .Din(bus_in), .R(control_1_fp_e), .W(control_1_fp_s), .Reset(reset));
  Stack_Pointer stack_pointer_1 (
    .cont(out_21), .sp(bus_in), .read(control_1_sp_e), .set(control_1_sp_s), .reset(reset),
    .i_d(control_1_sp_id), .set_hp(1'b0), .top_hp(bus_in));  // open: err
  _16_Bit_Register u_16_bit_register_12 (
    .Dout(bus_in), .Cont(out_12), .Din(bus_in), .R(control_1_lr_e), .W(control_1_lr_s), .Reset(reset));
  _16_Bit_Register u_16_bit_register_13 (
    .Dout(mem_addr), .Din(bus_in), .R(1'b1), .W(control_1_mar_s), .Reset(reset));  // open: Cont

  assign bus_out = bus_in;

  // Notes on the sheet:
  //   TMP
  //   FLAGS
  //   R0
  //   R1
  //   ACC
  //   R2
  //   R3
  //   PC
  //   R4
  //   IR
  //   IDX
  //   FP
  //   LR
  //   MAR
endmodule

module Maths_Unit (
  input  [15:0] A,
  input  [15:0] B,
  input  [1:0] op,
  output [15:0] C,
  output Z,
  output N,
  output Co,
  output V
);

  wire and_1_out, and_2_out, and_3_out, and_4_out, and_5_out, nor_1_out, not_1_out, not_2_out, not_3_out,
       not_4_out, not_5_out, not_6_out, or_1_out, or_2_out, subtractor_1_bout, xor_1_out, zero_1_z, zero_2_z,
       zero_3_z;
  wire [15:0] divider_1_out, divider_2_out, multiplier_1_cout, multiplier_1_out, subtractor_1_out;

  Subtractor #(.width(16)) subtractor_1 (.a(A), .b(B), .out(subtractor_1_out), .bout(subtractor_1_bout));  // open: bin
  Multiplier #(.width(16)) multiplier_1 (.a(A), .b(B), .out(multiplier_1_out), .cout(multiplier_1_cout));  // open: cin
  Divider #(.width(16)) divider_1 (.a(A), .b(B), .out(divider_1_out));  // open: upper, rem
  Divider #(.mode("unsigned"), .width(16)) divider_2 (.a(A), .b(B), .out(divider_2_out));  // open: upper, rem
  Zero zero_1 (.Z(zero_1_z), .A(A));
  Zero zero_2 (.Z(zero_2_z), .A(B));
  xor xor_1 (xor_1_out, A[15], B[15]);
  nor nor_1 (nor_1_out, zero_1_z, zero_2_z);
  not not_1 (not_1_out, zero_3_z);
  Zero zero_3 (.Z(zero_3_z), .A(multiplier_1_cout));
  not not_2 (not_2_out, A[15]);
  not not_3 (not_3_out, xor_1_out);
  Multiplexer #(.enable("false"), .select(2), .width(16)) multiplexer_1 (
    .in0(subtractor_1_out), .in1(multiplier_1_out), .in2(divider_1_out), .in3(divider_2_out), .out(C),
    .sel(op));
  not not_4 (not_4_out, B[15]);
  not not_5 (not_5_out, C[15]);
  not not_6 (not_6_out, C[15]);
  Zero zero_4 (.Z(Z), .A(C));
  Multiplexer #(.enable("false"), .select(2)) multiplexer_2 (
    .in0(subtractor_1_bout), .in1(not_1_out), .in2(1'b0), .in3(1'b0), .out(Co), .sel(op));
  and and_1 (and_1_out, not_2_out, B[15], C[15]);
  and and_2 (and_2_out, not_5_out, not_4_out, A[15]);
  and and_3 (and_3_out, not_3_out, C[15]);
  and and_4 (and_4_out, not_6_out, xor_1_out);
  or or_1 (or_1_out, and_1_out, and_2_out);
  and and_5 (and_5_out, or_2_out, nor_1_out);
  or or_2 (or_2_out, and_3_out, and_4_out);
  Multiplexer #(.enable("false"), .select(2)) multiplexer_3 (
    .in0(or_1_out), .in1(and_5_out), .in2(1'b0), .in3(1'b0), .out(V), .sel(op));

  assign N = C[15];
endmodule

module Graphics_Unit (
  input  clk,
  input  en_ld,
  input  set,
  input  [15:0] pos,
  input  [15:0] col,
  input  reset
);

  Graphics_Foreground graphics_foreground_1 (
    .set(set), .pos(pos), .col(col), .reset(reset), .en_ld(en_ld), .clk(clk));  // open: data, Y, X, scr_en, scr_clk
  ROM #(.addrWidth(16), .dataWidth(16)) rom_1 ();  // open: addr, data

  // Notes on the sheet:
  //   contents of rom_1 (hex, n*v repeats v):
  //   65536*ffd7
endmodule

module Control (
  input  clk,
  input  clke,
  input  reset,
  input  clks,
  input  c,
  input  a,
  input  e,
  input  z,
  input  n,
  input  v,
  input  [15:0] ir,
  output plus1_e,
  output ir_s,
  output pc_e,
  output mar_s,
  output mem_e,
  output pc_s,
  output acc_e,
  output acc_s,
  output sp_e,
  output mem_s,
  output r0_e,
  output tmp_s,
  output r1_e,
  output flags_s,
  output r2_e,
  output sp_s,
  output r3_e,
  output r0_s,
  output r4_e,
  output r1_s,
  output idx_e,
  output r2_s,
  output fp_e,
  output r3_s,
  output lr_e,
  output r4_s,
  output idx_s,
  output lr_id,
  output op0,
  output fp_s,
  output op1,
  output lr_s,
  output op2,
  output math_e,
  output sp_id,
  output ld_gr,
  output \end ,
  output asr
);

  wire and_13_out, and_15_out, and_17_out, jump_decoder_1_jmp, nor_1_out, not_1_out, not_2_out, not_3_out,
       not_4_out, not_5_out, not_6_out, or_1_out, or_3_out, or_4_out, or_5_out, or_6_out, or_7_out, or_8_out,
       S6;
  wire [2:0] counter_1_q, counter_2_q;
  wire [3:0] n3_8_demux_2_out, n3_8_demux_2_out_2;
  wire [6:0] adder_1_out, rom_1_data;
  wire [7:0] and_16_out, bit_extender_1_out, n3_8_demux_1_out, n3_8_demux_3_out, n3_8_demux_4_out,
       n3_8_demux_5_out, REG_E, REG_S;
  wire [29:0] rom_2_data;
  wire [29:2] multiplexer_1_out;

  and and_1 (pc_e, clke, or_3_out);
  and and_2 (mem_e, clke, or_4_out);
  and and_3 (acc_e, clke, or_5_out);
  and and_4 (sp_e, clke, multiplexer_1_out[16]);
  and and_5 (r0_e, clke, REG_E[0]);
  and and_6 (r1_e, clke, REG_E[1]);
  and and_7 (r2_e, clke, REG_E[2]);
  and and_8 (r3_e, clke, REG_E[3]);
  and and_9 (r4_e, clke, REG_E[4]);
  and and_10 (idx_e, clke, REG_E[5]);
  and and_11 (fp_e, clke, REG_E[6]);
  and and_12 (lr_e, clke, REG_E[7]);
  Jump_Decoder jump_decoder_1 (
    .jmp(jump_decoder_1_jmp), .e(e), .z(z), .c(c), .a(a), .c3(ir[3]), .c2(ir[2]), .c1(ir[1]), .c0(ir[0]),
    .n(n), .v(v));
  and and_13 (and_13_out, not_2_out, not_3_out, not_4_out, ir[12], ir[11]);
  and and_14 (asr, ir[15], not_5_out, not_6_out, ir[12], ir[11], ir[0]);
  or or_1 (or_1_out, reset, and_15_out);
  and and_15 (and_15_out, multiplexer_1_out[29], nor_1_out, not_1_out);
  not not_1 (not_1_out, n3_8_demux_2_out[3]);
  or or_2 (plus1_e, n3_8_demux_2_out[0], multiplexer_1_out[22]);
  or or_3 (or_3_out, n3_8_demux_2_out[0], multiplexer_1_out[21]);
  or or_4 (or_4_out, n3_8_demux_2_out[1], multiplexer_1_out[20]);
  or or_5 (or_5_out, n3_8_demux_2_out[2], multiplexer_1_out[17]);
  ROM #(.addrWidth(5), .dataWidth(7)) rom_1 (.addr(ir[15:11]), .data(rom_1_data));
  ROM #(.addrWidth(7), .dataWidth(30)) rom_2 (.addr(adder_1_out), .data(rom_2_data));
  not not_2 (not_2_out, ir[15]);
  not not_3 (not_3_out, ir[14]);
  not not_4 (not_4_out, ir[13]);
  not not_5 (not_5_out, ir[14]);
  not not_6 (not_6_out, ir[13]);
  Counter #(.max('h4), .ongoal("stay"), .trigger("falling"), .width(3)) counter_1 (
    .count(1'b1), .Q(counter_1_q), .up(1'b1), .clk(clk), .clr(or_1_out));  // open: load, D, carry
  assign bit_extender_1_out = {{7{nor_1_out}}, nor_1_out};  // Bit_Extender bit_extender_1
  _3_8_Demux u_3_8_demux_1 (.Out(n3_8_demux_1_out), .C(counter_2_q[0]), .A(counter_2_q[2]), .B(counter_2_q[1]));
  Adder_part #(.width(7)) adder_1 (
    .a({4'b0000, counter_2_q}), .b(rom_1_data), .out(adder_1_out), .cin(1'b0));  // open: cout
  _3_8_Demux u_3_8_demux_2 (
    .Out({n3_8_demux_2_out_2, n3_8_demux_2_out}), .C(counter_1_q[0]), .A(counter_1_q[2]), .B(counter_1_q[1]));
  assign {and_16_out[7:3], S6, and_16_out[1:0]} = bit_extender_1_out & n3_8_demux_1_out;  // AND_Gate and_16, 8 bits wide
  Counter #(.max('h7), .trigger("falling"), .width(3)) counter_2 (
    .load(n3_8_demux_2_out[2]), .D(3'b000), .count(1'b1), .Q(counter_2_q), .up(1'b1), .clk(clk), .clr(reset));  // open: carry
  nor nor_1 (nor_1_out, n3_8_demux_2_out[0], n3_8_demux_2_out[1], n3_8_demux_2_out[2]);
  and and_17 (and_17_out, jump_decoder_1_jmp, S6, and_13_out);
  Multiplexer #(.enable("false"), .width(30)) multiplexer_1 (
    .in0({30{1'b0}}), .in1(rom_2_data),
    .out({multiplexer_1_out[29], ld_gr, multiplexer_1_out[27:25], math_e, multiplexer_1_out[23:16], lr_id, op0, op1, op2, multiplexer_1_out[11:2], sp_id, \end }),
    .sel(nor_1_out));
  _3_8_Demux u_3_8_demux_3 (.Out(n3_8_demux_3_out), .C(ir[8]), .A(ir[10]), .B(ir[9]));
  _3_8_Demux u_3_8_demux_4 (.Out(n3_8_demux_4_out), .C(ir[5]), .A(ir[7]), .B(ir[6]));
  _3_8_Demux u_3_8_demux_5 (.Out(n3_8_demux_5_out), .C(ir[2]), .A(ir[4]), .B(ir[3]));
  Multiplexer #(.enable("false"), .select(2), .width(8)) multiplexer_2 (
    .in0({8{1'b0}}), .in1(n3_8_demux_3_out), .in2(n3_8_demux_4_out), .in3(n3_8_demux_5_out), .out(REG_E),
    .sel(multiplexer_1_out[19:18]));
  Multiplexer #(.enable("false"), .select(2), .width(8)) multiplexer_3 (
    .in0({8{1'b0}}), .in1(n3_8_demux_3_out), .in2(n3_8_demux_4_out), .in3(n3_8_demux_5_out), .out(REG_S),
    .sel(multiplexer_1_out[5:4]));
  or or_6 (or_6_out, n3_8_demux_2_out[0], multiplexer_1_out[10]);
  or or_7 (or_7_out, n3_8_demux_2_out[2], and_17_out, multiplexer_1_out[9]);
  or or_8 (or_8_out, n3_8_demux_2_out[0], multiplexer_1_out[8]);
  and and_18 (ir_s, clks, n3_8_demux_2_out[1]);
  and and_19 (mar_s, clks, or_6_out);
  and and_20 (pc_s, clks, or_7_out);
  and and_21 (acc_s, clks, or_8_out);
  and and_22 (mem_s, clks, multiplexer_1_out[7]);
  and and_23 (tmp_s, clks, multiplexer_1_out[6]);
  and and_24 (flags_s, clks, multiplexer_1_out[3]);
  and and_25 (sp_s, clks, multiplexer_1_out[2]);
  and and_26 (r0_s, clks, REG_S[0]);
  and and_27 (r1_s, clks, REG_S[1]);
  and and_28 (r2_s, clks, REG_S[2]);
  and and_29 (r3_s, clks, REG_S[3]);
  and and_30 (r4_s, clks, REG_S[4]);
  and and_31 (idx_s, clks, REG_S[5]);
  and and_32 (fp_s, clks, REG_S[6]);
  and and_33 (lr_s, clks, REG_S[7]);

  // Notes on the sheet:
  //   contents of rom_1 (hex, n*v repeats v):
  //   0 4 7 b f 12 17 1a 1f 21 23 26 2c 2d 2f 31 35 39 3d 41 45 48 4b 4e 52 56 5a 5d 5f 63 67 6a
  //   contents of rom_2 (hex, n*v repeats v):
  //   600500 100030 20200 20000000 200400 100200 20000000 600500 100200 20030 20000000 600500 20200 100000
  //   20000000 40400 100030 20000000 80040 40100 20400 100030 20000000 c0400 40080 20000000 80040 c0100
  //   20400 40080 20000000 40030 20000000 10030 20000000 40400 10080080 20000000 0 40040 7080100 20400
  //   108c0080 20000000 20000000 8000000 20000000 40200 20000000 4 10400 100030 20000000 10400 40080 6
  //   20000000 80040 40108 20030 20000000 80040 44108 20030 20000000 80040 4c108 20030 20000000 42108
  //   20010 20000000 4a108 20010 20000000 46108 20030 20000000 80040 41108 20030 20000000 80040 45108
  //   20030 20000000 80040 43108 20030 20000000 80040 47108 20000000 1 20000000 80040 1040108 20030
  //   20000000 80040 2040100 20030 20000000 2840100 20030 20000000 800001
  //   Fetch Counter
  //   uCode LUT
  //   uCode ROM
  //   Execute Counter
endmodule

module ALU (
  input  fcmp,
  input  [15:0] A,
  input  [15:0] B,
  input  asr,
  input  lr_id,
  input  Op2,
  input  Op1,
  input  Op0,
  output GT,
  output EQ,
  output [15:0] C,
  output Z,
  output N,
  output Co,
  output V
);

  wire adder_1_co, adder_2_co, and_2_out, and_3_out, and_4_out, multiplexer_3_out, multiplexer_4_out,
       nor_1_out, nor_2_out, not_2_out, not_3_out, not_4_out, or_2_out, shift_left_1_so, shift_right_1_so,
       xor_1_out, xor_cmp_1_gt;
  wire [15:0] adder_1_s, adder_2_s, and_1_out, multiplexer_1_out, multiplexer_2_out, not_1_out, or_1_out,
       shift_left_1_b, shift_right_1_b, xor_cmp_1_c;

  xor xor_1 (xor_1_out, A[15], B[15]);
  XOR_CMP xor_cmp_1 (.EQ(EQ), .GT(xor_cmp_1_gt), .C(xor_cmp_1_c), .A(A), .B(B));
  assign or_1_out = A | B;  // OR_Gate or_1, 16 bits wide
  assign and_1_out = A & B;  // AND_Gate and_1, 16 bits wide
  assign not_1_out = ~A;  // NOT_Gate not_1, 16 bits wide
  Multiplexer #(.width(16)) multiplexer_1 (
    .in0(16'h1), .in1({16{1'b1}}), .out(multiplexer_1_out), .sel(lr_id), .en(1'b1));
  Shift_Left shift_left_1 (.B(shift_left_1_b), .So(shift_left_1_so), .n(B), .A(A));
  Shift_Right shift_right_1 (.B(shift_right_1_b), .So(shift_right_1_so), .asr(asr), .n(B), .A(A));
  Adder adder_1 (.S(adder_1_s), .Co(adder_1_co), .Ci(1'b0), .X(A), .Y(B));
  not not_2 (not_2_out, xor_1_out);
  and and_2 (and_2_out, xor_1_out, B[15]);
  Adder adder_2 (.S(adder_2_s), .Co(adder_2_co), .Ci(1'b0), .X(A), .Y(multiplexer_1_out));
  Multiplexer #(.width(16)) multiplexer_2 (
    .in0(shift_left_1_b), .in1(shift_right_1_b), .out(multiplexer_2_out), .sel(lr_id), .en(1'b1));
  Multiplexer multiplexer_3 (
    .in0(shift_left_1_so), .in1(shift_right_1_so), .out(multiplexer_3_out), .sel(lr_id), .en(1'b1));
  nor nor_1 (nor_1_out, Op0, Op1, Op2);
  Multiplexer #(.enable("false")) multiplexer_4 (
    .in0(and_2_out), .in1(xor_cmp_1_gt), .out(multiplexer_4_out), .sel(not_2_out));
  not not_3 (not_3_out, adder_1_s[15]);
  and and_3 (and_3_out, fcmp, B[15], A[15]);
  Multiplexer #(.enable("false")) multiplexer_5 (.in0(multiplexer_4_out), .in1(not_4_out), .out(GT), .sel(and_3_out));
  not not_4 (not_4_out, multiplexer_4_out);
  and and_4 (and_4_out, B[15], A[15], not_3_out);
  Multiplexer #(.enable("false"), .select(3), .width(16)) multiplexer_6 (
    .in0(adder_1_s), .in1(multiplexer_2_out), .in2(adder_2_s), .in3(not_1_out), .in4(and_1_out),
    .in5(or_1_out), .in6(xor_cmp_1_c), .in7(16'h1), .out(C), .sel({Op2, Op1, Op0}));
  Multiplexer #(.enable("false"), .select(3)) multiplexer_7 (
    .in0(adder_1_co), .in1(multiplexer_3_out), .in2(adder_2_co), .in3(1'b0), .in4(1'b0), .in5(1'b0),
    .in6(1'b0), .in7(1'b0), .out(Co), .sel({Op2, Op1, Op0}));
  or or_2 (or_2_out, and_4_out, nor_2_out);
  nor nor_2 (nor_2_out, not_3_out, B[15], A[15]);
  Zero zero_1 (.Z(Z), .A(C));
  and and_5 (V, nor_1_out, or_2_out);

  assign N = C[15];
endmodule

module Clock (
  input  clkin,
  input  reset,
  input  init,
  output clk,
  output clke,
  output clks
);

  wire register_1_q;
  wire [1:0] t_ff_1_q;
  wire [2:0] rom_1_data, rom_2_data;

  T_Flip_Flop t_ff_1 (.clk(clkin), .T(1'b1), .Q(t_ff_1_q[0]), .preset(reset));  // open: Qn, reset
  T_Flip_Flop #(.trigger("falling")) t_ff_2 (
    .clk(clkin), .T(1'b1), .Q(t_ff_1_q[1]), .reset(reset));  // open: Qn, preset
  Register #(.width(1)) register_1 (.D(init), .Q(register_1_q), .clk(reset));  // open: en, clr
  ROM #(.addrWidth(2), .dataWidth(3)) rom_1 (.addr(t_ff_1_q), .data(rom_1_data));
  ROM #(.addrWidth(2), .dataWidth(3)) rom_2 (.addr(t_ff_1_q), .data(rom_2_data));
  Multiplexer #(.enable("false"), .width(3)) multiplexer_1 (
    .in0(rom_1_data), .in1(rom_2_data), .out({clk, clke, clks}), .sel(register_1_q));

  // Notes on the sheet:
  //   contents of rom_1 (hex, n*v repeats v):
  //   2 0 7 6
  //   contents of rom_2 (hex, n*v repeats v):
  //   6 0 7 2
endmodule

module Address_Decoder (
  input  [15:0] addr,
  input  ld_gr,
  output i_o,
  output ram,
  output rom
);

  wire and_1_out, and_2_out, not_1_out, not_2_out, not_3_out;

  and and_1 (and_1_out, addr[4], addr[5], addr[6], addr[7], addr[8], addr[9], addr[10], addr[11], addr[12], addr[13], addr[14], addr[15]);
  not not_1 (not_1_out, and_1_out);
  not not_2 (not_2_out, addr[15]);
  and and_2 (and_2_out, not_1_out, addr[15]);
  not not_3 (not_3_out, ld_gr);
  and and_3 (i_o, and_1_out, not_3_out);
  and and_4 (ram, and_2_out, not_3_out);
  and and_5 (rom, not_2_out, not_3_out);
endmodule

module Stack_Pointer (
  input  read,
  input  set,
  input  set_hp,
  input  reset,
  input  i_d,
  input  [15:0] top_hp,
  output [15:0] sp,
  output [15:0] cont,
  output err
);

  wire and_1_out, and_2_out, comparator_1_gt, comparator_2_eq, not_1_out, not_2_out, not_3_out, or_1_out,
       or_2_out;
  wire [15:0] adder_1_s, multiplexer_1_out, multiplexer_2_out, n16_bit_register_2_dout,
       n16_bit_register_3_cont, n16_bit_register_4_cont;

  and and_1 (and_1_out, set, not_1_out);
  not not_1 (not_1_out, set_hp);
  or or_1 (or_1_out, and_1_out, reset);
  and and_2 (and_2_out, set_hp, set);
  Multiplexer #(.enable("false"), .width(16)) multiplexer_1 (
    .in0(adder_1_s), .in1(16'hffef), .out(multiplexer_1_out), .sel(reset));
  _16_Bit_Register u_16_bit_register_1 (
    .Dout(sp), .Cont(cont), .Din(multiplexer_1_out), .R(read), .W(or_1_out), .Reset(1'b0));
  _16_Bit_Register u_16_bit_register_2 (
    .Dout(n16_bit_register_2_dout), .Din(top_hp), .R(1'b1), .W(and_2_out), .Reset(reset));  // open: Cont
  not not_2 (not_2_out, or_1_out);
  Comparator #(.mode("unsigned"), .width(16)) comparator_1 (
    .a(cont), .b(16'hffef), .gt(comparator_1_gt));  // open: eq, lt
  Comparator #(.mode("unsigned"), .width(16)) comparator_2 (
    .a(cont), .b(n16_bit_register_2_dout), .eq(comparator_2_eq));  // open: gt, lt
  or or_2 (or_2_out, comparator_1_gt, comparator_2_eq);
  _16_Bit_Register u_16_bit_register_3 (
    .Cont(n16_bit_register_3_cont), .Din(cont), .W(not_2_out), .Reset(reset));  // open: Dout, R
  and and_3 (err, or_2_out, not_3_out);
  not not_3 (not_3_out, set);
  _16_Bit_Register u_16_bit_register_4 (
    .Cont(n16_bit_register_4_cont), .Din(n16_bit_register_3_cont), .W(or_1_out), .Reset(reset));  // open: Dout, R
  Multiplexer #(.enable("false"), .width(16)) multiplexer_2 (
    .in0(16'h1), .in1({16{1'b1}}), .out(multiplexer_2_out), .sel(i_d));
  Adder adder_1 (.S(adder_1_s), .Ci(1'b0), .X(n16_bit_register_4_cont), .Y(multiplexer_2_out));  // open: Co
endmodule

module Graphics_Foreground (
  input  set,
  input  [15:0] pos,
  input  [15:0] col,
  input  reset,
  input  en_ld,
  input  clk,
  output [15:0] data,
  output [7:0] Y,
  output [7:0] X,
  output scr_en,
  output scr_clk
);

  wire [15:0] divider_1_out, divider_1_rem, register_1_q;

  and and_1 (scr_clk, en_ld, clk);
  Register #(.width(16)) register_1 (.D(pos), .Q(register_1_q), .clk(set), .clr(reset));  // open: en
  Divider #(.mode("unsigned"), .width(16)) divider_1 (
    .a(register_1_q), .b(16'h100), .out(divider_1_out), .rem(divider_1_rem));  // open: upper
  Register #(.width(16)) register_2 (.D(col), .Q(data), .clk(set), .clr(reset));  // open: en
  Bit_Extender #(.in_width(16), .out_width(8), .\type ("zero")) bit_extender_1 (.in(divider_1_out), .out(Y));
  Bit_Extender #(.in_width(16), .out_width(8), .\type ("zero")) bit_extender_2 (.in(divider_1_rem), .out(X));

  assign scr_en = en_ld;
endmodule

module KBD_Controller (
  input  [6:0] data,
  input  clk_e,
  input  en,
  input  [3:0] id,
  input  reset,
  input  [3:0] addr,
  output [15:0] bus_out,
  output kbd_clk
);

  wire and_1_out;
  wire [3:0] xnor_1_out;
  wire [15:0] bit_extender_1_out, register_1_q;

  assign xnor_1_out = ~(id ^ addr);  // XNOR_Gate xnor_1, 4 bits wide
  and and_1 (and_1_out, xnor_1_out[0], xnor_1_out[1], xnor_1_out[2], xnor_1_out[3]);
  and and_2 (kbd_clk, clk_e, en, and_1_out);
  assign bit_extender_1_out = {{9{1'b0}}, data};  // Bit_Extender bit_extender_1
  assign bus_out = kbd_clk ? register_1_q : 16'bz;  // Controlled_Buffer controlled_buffer_1
  Register #(.width(16)) register_1 (.D(bit_extender_1_out), .Q(register_1_q), .clk(kbd_clk), .clr(reset));  // open: en
endmodule

module TTY_Controller (
  input  [15:0] bus_in,
  input  clk_s,
  input  en,
  input  [3:0] id,
  input  [3:0] addr,
  output [6:0] data,
  output clk
);

  wire and_1_out;
  wire [3:0] xnor_1_out;

  assign xnor_1_out = ~(id ^ addr);  // XNOR_Gate xnor_1, 4 bits wide
  Bit_Extender #(.in_width(16), .out_width(7), .\type ("zero")) bit_extender_1 (.in(bus_in), .out(data));
  and and_1 (and_1_out, xnor_1_out[0], xnor_1_out[1], xnor_1_out[2], xnor_1_out[3]);
  and and_2 (clk, clk_s, en, and_1_out);
endmodule

module Input_Device (
  input  [15:0] data,
  input  clk_e,
  input  en,
  input  [3:0] id,
  input  [3:0] addr,
  input  reset,
  output [15:0] bus_out
);

  wire and_1_out, and_2_out;
  wire [3:0] xnor_1_out;

  assign xnor_1_out = ~(id ^ addr);  // XNOR_Gate xnor_1, 4 bits wide
  and and_1 (and_1_out, xnor_1_out[0], xnor_1_out[1], xnor_1_out[2], xnor_1_out[3]);
  and and_2 (and_2_out, clk_e, en, and_1_out);
  _16_Bit_Register u_16_bit_register_1 (
    .Dout(bus_out), .Din(data), .R(and_2_out), .W(1'b1), .Reset(reset));  // open: Cont
endmodule

module Output_Device (
  input  [15:0] bus_in,
  input  clk_s,
  input  en,
  input  [3:0] id,
  input  reset,
  input  [3:0] addr,
  output [15:0] data
);

  wire and_1_out, and_2_out;
  wire [3:0] xnor_1_out;

  assign xnor_1_out = ~(id ^ addr);  // XNOR_Gate xnor_1, 4 bits wide
  and and_1 (and_1_out, clk_s, en, and_2_out);
  and and_2 (and_2_out, xnor_1_out[0], xnor_1_out[1], xnor_1_out[2], xnor_1_out[3]);
  _16_Bit_Register u_16_bit_register_1 (
    .Dout(data), .Din(bus_in), .R(1'b1), .W(and_1_out), .Reset(reset));  // open: Cont
endmodule

module _16_Bit_Register (
  input  [15:0] Din,
  input  W,
  input  Reset,
  input  R,
  output [15:0] Cont,
  output [15:0] Dout
);

  wire not_1_out, or_1_out;
  wire [15:0] and_1_out, controlled_buffer_1_out;

  not not_1 (not_1_out, Reset);
  assign controlled_buffer_1_out = Reset ? {16{1'b0}} : 16'bz;  // Controlled_Buffer controlled_buffer_1
  assign controlled_buffer_1_out = not_1_out ? Din : 16'bz;  // Controlled_Buffer controlled_buffer_2
  or or_1 (or_1_out, W, Reset);
  _1_Bit_Memory_Cell u_1_bit_memory_cell_1 (.Q(Cont[0]), .W(or_1_out), .D(controlled_buffer_1_out[0]));
  _1_Bit_Memory_Cell u_1_bit_memory_cell_2 (.Q(Cont[1]), .W(or_1_out), .D(controlled_buffer_1_out[1]));
  _1_Bit_Memory_Cell u_1_bit_memory_cell_3 (.Q(Cont[2]), .W(or_1_out), .D(controlled_buffer_1_out[2]));
  _1_Bit_Memory_Cell u_1_bit_memory_cell_4 (.Q(Cont[3]), .W(or_1_out), .D(controlled_buffer_1_out[3]));
  _1_Bit_Memory_Cell u_1_bit_memory_cell_5 (.Q(Cont[4]), .W(or_1_out), .D(controlled_buffer_1_out[4]));
  _1_Bit_Memory_Cell u_1_bit_memory_cell_6 (.Q(Cont[5]), .W(or_1_out), .D(controlled_buffer_1_out[5]));
  _1_Bit_Memory_Cell u_1_bit_memory_cell_7 (.Q(Cont[6]), .W(or_1_out), .D(controlled_buffer_1_out[6]));
  _1_Bit_Memory_Cell u_1_bit_memory_cell_8 (.Q(Cont[7]), .W(or_1_out), .D(controlled_buffer_1_out[7]));
  _1_Bit_Memory_Cell u_1_bit_memory_cell_9 (.Q(Cont[8]), .W(or_1_out), .D(controlled_buffer_1_out[8]));
  _1_Bit_Memory_Cell u_1_bit_memory_cell_10 (.Q(Cont[9]), .W(or_1_out), .D(controlled_buffer_1_out[9]));
  _1_Bit_Memory_Cell u_1_bit_memory_cell_11 (.Q(Cont[10]), .W(or_1_out), .D(controlled_buffer_1_out[10]));
  _1_Bit_Memory_Cell u_1_bit_memory_cell_12 (.Q(Cont[11]), .W(or_1_out), .D(controlled_buffer_1_out[11]));
  _1_Bit_Memory_Cell u_1_bit_memory_cell_13 (.Q(Cont[12]), .W(or_1_out), .D(controlled_buffer_1_out[12]));
  _1_Bit_Memory_Cell u_1_bit_memory_cell_14 (.Q(Cont[13]), .W(or_1_out), .D(controlled_buffer_1_out[13]));
  _1_Bit_Memory_Cell u_1_bit_memory_cell_15 (.Q(Cont[14]), .W(or_1_out), .D(controlled_buffer_1_out[14]));
  _1_Bit_Memory_Cell u_1_bit_memory_cell_16 (.Q(Cont[15]), .W(or_1_out), .D(controlled_buffer_1_out[15]));
  and and_1 (and_1_out[0], Cont[0], R);
  and and_2 (and_1_out[1], Cont[1], R);
  and and_3 (and_1_out[2], Cont[2], R);
  and and_4 (and_1_out[3], Cont[3], R);
  and and_5 (and_1_out[4], Cont[4], R);
  and and_6 (and_1_out[5], Cont[5], R);
  and and_7 (and_1_out[6], Cont[6], R);
  and and_8 (and_1_out[7], Cont[7], R);
  and and_9 (and_1_out[8], Cont[8], R);
  and and_10 (and_1_out[9], Cont[9], R);
  and and_11 (and_1_out[10], Cont[10], R);
  and and_12 (and_1_out[11], Cont[11], R);
  and and_13 (and_1_out[12], Cont[12], R);
  and and_14 (and_1_out[13], Cont[13], R);
  and and_15 (and_1_out[14], Cont[14], R);
  and and_16 (and_1_out[15], Cont[15], R);
  assign Dout = R ? and_1_out : 16'bz;  // Controlled_Buffer controlled_buffer_3
endmodule

module _6_Bit_Register (
  input  [5:0] Din,
  input  W,
  input  Reset,
  input  R,
  output [5:0] Cont,
  output [5:0] Dout
);

  wire not_1_out, or_1_out;
  wire [5:0] controlled_buffer_1_out;

  assign controlled_buffer_1_out = not_1_out ? Din : 6'bz;  // Controlled_Buffer controlled_buffer_1
  not not_1 (not_1_out, Reset);
  assign controlled_buffer_1_out = Reset ? {6{1'b0}} : 6'bz;  // Controlled_Buffer controlled_buffer_2
  or or_1 (or_1_out, W, Reset);
  _1_Bit_Memory_Cell u_1_bit_memory_cell_1 (.Q(Cont[0]), .W(or_1_out), .D(controlled_buffer_1_out[0]));
  _1_Bit_Memory_Cell u_1_bit_memory_cell_2 (.Q(Cont[1]), .W(or_1_out), .D(controlled_buffer_1_out[1]));
  _1_Bit_Memory_Cell u_1_bit_memory_cell_3 (.Q(Cont[2]), .W(or_1_out), .D(controlled_buffer_1_out[2]));
  _1_Bit_Memory_Cell u_1_bit_memory_cell_4 (.Q(Cont[3]), .W(or_1_out), .D(controlled_buffer_1_out[3]));
  _1_Bit_Memory_Cell u_1_bit_memory_cell_5 (.Q(Cont[4]), .W(or_1_out), .D(controlled_buffer_1_out[4]));
  _1_Bit_Memory_Cell u_1_bit_memory_cell_6 (.Q(Cont[5]), .W(or_1_out), .D(controlled_buffer_1_out[5]));
  and and_1 (Dout[0], Cont[0], R);
  and and_2 (Dout[1], Cont[1], R);
  and and_3 (Dout[2], Cont[2], R);
  and and_4 (Dout[3], Cont[3], R);
  and and_5 (Dout[4], Cont[4], R);
  and and_6 (Dout[5], Cont[5], R);
endmodule

module _1_Bit_Memory_Cell (
  input  D,
  input  W,
  output Q
);

  wire nand_1_out, nand_2_out, nand_4_out;

  nand nand_1 (nand_1_out, D, W);
  nand nand_2 (nand_2_out, nand_1_out, W);
  nand nand_3 (Q, nand_1_out, nand_4_out);
  nand nand_4 (nand_4_out, Q, nand_2_out);
endmodule

module Adder (
  input  [15:0] X,
  input  [15:0] Y,
  input  Ci,
  output Co,
  output [15:0] S
);

  wire full_adder_2_co, full_adder_3_co, full_adder_4_co, full_adder_5_co, full_adder_6_co, full_adder_7_co,
       full_adder_8_co, full_adder_9_co, full_adder_10_co, full_adder_11_co, full_adder_12_co,
       full_adder_13_co, full_adder_14_co, full_adder_15_co, full_adder_16_co;

  Full_Adder full_adder_1 (.Co(Co), .S(S[15]), .Ci(full_adder_2_co), .X(X[15]), .Y(Y[15]));
  Full_Adder full_adder_2 (.Co(full_adder_2_co), .S(S[14]), .Ci(full_adder_3_co), .X(X[14]), .Y(Y[14]));
  Full_Adder full_adder_3 (.Co(full_adder_3_co), .S(S[13]), .Ci(full_adder_4_co), .X(X[13]), .Y(Y[13]));
  Full_Adder full_adder_4 (.Co(full_adder_4_co), .S(S[12]), .Ci(full_adder_5_co), .X(X[12]), .Y(Y[12]));
  Full_Adder full_adder_5 (.Co(full_adder_5_co), .S(S[11]), .Ci(full_adder_6_co), .X(X[11]), .Y(Y[11]));
  Full_Adder full_adder_6 (.Co(full_adder_6_co), .S(S[10]), .Ci(full_adder_7_co), .X(X[10]), .Y(Y[10]));
  Full_Adder full_adder_7 (.Co(full_adder_7_co), .S(S[9]), .Ci(full_adder_8_co), .X(X[9]), .Y(Y[9]));
  Full_Adder full_adder_8 (.Co(full_adder_8_co), .S(S[8]), .Ci(full_adder_9_co), .X(X[8]), .Y(Y[8]));
  Full_Adder full_adder_9 (.Co(full_adder_9_co), .S(S[7]), .Ci(full_adder_10_co), .X(X[7]), .Y(Y[7]));
  Full_Adder full_adder_10 (.Co(full_adder_10_co), .S(S[6]), .Ci(full_adder_11_co), .X(X[6]), .Y(Y[6]));
  Full_Adder full_adder_11 (.Co(full_adder_11_co), .S(S[5]), .Ci(full_adder_12_co), .X(X[5]), .Y(Y[5]));
  Full_Adder full_adder_12 (.Co(full_adder_12_co), .S(S[4]), .Ci(full_adder_13_co), .X(X[4]), .Y(Y[4]));
  Full_Adder full_adder_13 (.Co(full_adder_13_co), .S(S[3]), .Ci(full_adder_14_co), .X(X[3]), .Y(Y[3]));
  Full_Adder full_adder_14 (.Co(full_adder_14_co), .S(S[2]), .Ci(full_adder_15_co), .X(X[2]), .Y(Y[2]));
  Full_Adder full_adder_15 (.Co(full_adder_15_co), .S(S[1]), .Ci(full_adder_16_co), .X(X[1]), .Y(Y[1]));
  Full_Adder full_adder_16 (.Co(full_adder_16_co), .S(S[0]), .Ci(Ci), .X(X[0]), .Y(Y[0]));
endmodule

module Full_Adder (
  input  X,
  input  Y,
  input  Ci,
  output S,
  output Co
);

  wire and_1_out, and_2_out, xor_1_out;

  xor xor_1 (xor_1_out, X, Y);
  xor xor_2 (S, xor_1_out, Ci);
  and and_1 (and_1_out, xor_1_out, Ci);
  and and_2 (and_2_out, X, Y);
  or or_1 (Co, and_1_out, and_2_out);
endmodule

module Shift_Left (
  input  [15:0] A,
  input  [15:0] n,
  output [15:0] B,
  output So
);

  wire [4:0] bit_extender_2_out;
  wire [16:0] bit_extender_1_out;

  assign bit_extender_1_out = {{1{1'b0}}, A};  // Bit_Extender bit_extender_1
  assign bit_extender_2_out = {{1{1'b0}}, n[3:0]};  // Bit_Extender bit_extender_2
  Shifter #(.width(17)) shifter_1 (.in(bit_extender_1_out), .\dist (bit_extender_2_out), .out({So, B}));
endmodule

module Shift_Right (
  input  [15:0] A,
  input  [15:0] n,
  input  asr,
  output [15:0] B,
  output So
);

  wire [4:0] bit_extender_1_out;
  wire [16:0] shifter_1_out, shifter_2_out;

  assign bit_extender_1_out = {{1{1'b0}}, n[3:0]};  // Bit_Extender bit_extender_1
  Shifter #(.shift("lr"), .width(17)) shifter_1 (.in({A, 1'b0}), .\dist (bit_extender_1_out), .out(shifter_1_out));
  Shifter #(.shift("ar"), .width(17)) shifter_2 (.in({A, 1'b0}), .\dist (bit_extender_1_out), .out(shifter_2_out));
  Multiplexer #(.enable("false"), .width(17)) multiplexer_1 (
    .in0(shifter_1_out), .in1(shifter_2_out), .out({B, So}), .sel(asr));
endmodule

module XOR_CMP (
  input  [15:0] A,
  input  [15:0] B,
  output [15:0] C,
  output EQ,
  output GT
);

  wire xor_cmp_cell_1_eq_o, xor_cmp_cell_1_gt_o, xor_cmp_cell_2_eq_o, xor_cmp_cell_2_gt_o,
       xor_cmp_cell_3_eq_o, xor_cmp_cell_3_gt_o, xor_cmp_cell_4_eq_o, xor_cmp_cell_4_gt_o,
       xor_cmp_cell_5_eq_o, xor_cmp_cell_5_gt_o, xor_cmp_cell_6_eq_o, xor_cmp_cell_6_gt_o,
       xor_cmp_cell_7_eq_o, xor_cmp_cell_7_gt_o, xor_cmp_cell_8_eq_o, xor_cmp_cell_8_gt_o,
       xor_cmp_cell_9_eq_o, xor_cmp_cell_9_gt_o, xor_cmp_cell_10_eq_o, xor_cmp_cell_10_gt_o,
       xor_cmp_cell_11_eq_o, xor_cmp_cell_11_gt_o, xor_cmp_cell_12_eq_o, xor_cmp_cell_12_gt_o,
       xor_cmp_cell_13_eq_o, xor_cmp_cell_13_gt_o, xor_cmp_cell_14_eq_o, xor_cmp_cell_14_gt_o,
       xor_cmp_cell_15_eq_o, xor_cmp_cell_15_gt_o;

  XOR_CMP_Cell xor_cmp_cell_1 (
    .eq_o(xor_cmp_cell_1_eq_o), .gt_o(xor_cmp_cell_1_gt_o), .c(C[15]), .eq_i(1'b1), .gt_i(1'b0), .a(A[15]),
    .b(B[15]));
  XOR_CMP_Cell xor_cmp_cell_2 (
    .eq_o(xor_cmp_cell_2_eq_o), .gt_o(xor_cmp_cell_2_gt_o), .c(C[14]), .eq_i(xor_cmp_cell_1_eq_o),
    .gt_i(xor_cmp_cell_1_gt_o), .a(A[14]), .b(B[14]));
  XOR_CMP_Cell xor_cmp_cell_3 (
    .eq_o(xor_cmp_cell_3_eq_o), .gt_o(xor_cmp_cell_3_gt_o), .c(C[13]), .eq_i(xor_cmp_cell_2_eq_o),
    .gt_i(xor_cmp_cell_2_gt_o), .a(A[13]), .b(B[13]));
  XOR_CMP_Cell xor_cmp_cell_4 (
    .eq_o(xor_cmp_cell_4_eq_o), .gt_o(xor_cmp_cell_4_gt_o), .c(C[12]), .eq_i(xor_cmp_cell_3_eq_o),
    .gt_i(xor_cmp_cell_3_gt_o), .a(A[12]), .b(B[12]));
  XOR_CMP_Cell xor_cmp_cell_5 (
    .eq_o(xor_cmp_cell_5_eq_o), .gt_o(xor_cmp_cell_5_gt_o), .c(C[11]), .eq_i(xor_cmp_cell_4_eq_o),
    .gt_i(xor_cmp_cell_4_gt_o), .a(A[11]), .b(B[11]));
  XOR_CMP_Cell xor_cmp_cell_6 (
    .eq_o(xor_cmp_cell_6_eq_o), .gt_o(xor_cmp_cell_6_gt_o), .c(C[10]), .eq_i(xor_cmp_cell_5_eq_o),
    .gt_i(xor_cmp_cell_5_gt_o), .a(A[10]), .b(B[10]));
  XOR_CMP_Cell xor_cmp_cell_7 (
    .eq_o(xor_cmp_cell_7_eq_o), .gt_o(xor_cmp_cell_7_gt_o), .c(C[9]), .eq_i(xor_cmp_cell_6_eq_o),
    .gt_i(xor_cmp_cell_6_gt_o), .a(A[9]), .b(B[9]));
  XOR_CMP_Cell xor_cmp_cell_8 (
    .eq_o(xor_cmp_cell_8_eq_o), .gt_o(xor_cmp_cell_8_gt_o), .c(C[8]), .eq_i(xor_cmp_cell_7_eq_o),
    .gt_i(xor_cmp_cell_7_gt_o), .a(A[8]), .b(B[8]));
  XOR_CMP_Cell xor_cmp_cell_9 (
    .eq_o(xor_cmp_cell_9_eq_o), .gt_o(xor_cmp_cell_9_gt_o), .c(C[7]), .eq_i(xor_cmp_cell_8_eq_o),
    .gt_i(xor_cmp_cell_8_gt_o), .a(A[7]), .b(B[7]));
  XOR_CMP_Cell xor_cmp_cell_10 (
    .eq_o(xor_cmp_cell_10_eq_o), .gt_o(xor_cmp_cell_10_gt_o), .c(C[6]), .eq_i(xor_cmp_cell_9_eq_o),
    .gt_i(xor_cmp_cell_9_gt_o), .a(A[6]), .b(B[6]));
  XOR_CMP_Cell xor_cmp_cell_11 (
    .eq_o(xor_cmp_cell_11_eq_o), .gt_o(xor_cmp_cell_11_gt_o), .c(C[5]), .eq_i(xor_cmp_cell_10_eq_o),
    .gt_i(xor_cmp_cell_10_gt_o), .a(A[5]), .b(B[5]));
  XOR_CMP_Cell xor_cmp_cell_12 (
    .eq_o(xor_cmp_cell_12_eq_o), .gt_o(xor_cmp_cell_12_gt_o), .c(C[4]), .eq_i(xor_cmp_cell_11_eq_o),
    .gt_i(xor_cmp_cell_11_gt_o), .a(A[4]), .b(B[4]));
  XOR_CMP_Cell xor_cmp_cell_13 (
    .eq_o(xor_cmp_cell_13_eq_o), .gt_o(xor_cmp_cell_13_gt_o), .c(C[3]), .eq_i(xor_cmp_cell_12_eq_o),
    .gt_i(xor_cmp_cell_12_gt_o), .a(A[3]), .b(B[3]));
  XOR_CMP_Cell xor_cmp_cell_14 (
    .eq_o(xor_cmp_cell_14_eq_o), .gt_o(xor_cmp_cell_14_gt_o), .c(C[2]), .eq_i(xor_cmp_cell_13_eq_o),
    .gt_i(xor_cmp_cell_13_gt_o), .a(A[2]), .b(B[2]));
  XOR_CMP_Cell xor_cmp_cell_15 (
    .eq_o(xor_cmp_cell_15_eq_o), .gt_o(xor_cmp_cell_15_gt_o), .c(C[1]), .eq_i(xor_cmp_cell_14_eq_o),
    .gt_i(xor_cmp_cell_14_gt_o), .a(A[1]), .b(B[1]));
  XOR_CMP_Cell xor_cmp_cell_16 (
    .eq_o(EQ), .gt_o(GT), .c(C[0]), .eq_i(xor_cmp_cell_15_eq_o), .gt_i(xor_cmp_cell_15_gt_o), .a(A[0]),
    .b(B[0]));
endmodule

module XOR_CMP_Cell (
  input  eq_i,
  input  gt_i,
  input  a,
  input  b,
  output c,
  output eq_o,
  output gt_o
);

  wire and_2_out, not_1_out;

  xor xor_1 (c, a, b);
  not not_1 (not_1_out, c);
  and and_1 (eq_o, not_1_out, eq_i);
  and and_2 (and_2_out, a, eq_i, c);
  or or_1 (gt_o, and_2_out, gt_i);
endmodule

module Set_To_One (
  input  [15:0] A,
  input  S,
  output [15:0] B
);

  wire not_1_out;

  and and_1 (B[15], A[15], not_1_out);
  and and_2 (B[14], A[14], not_1_out);
  and and_3 (B[13], A[13], not_1_out);
  and and_4 (B[12], A[12], not_1_out);
  and and_5 (B[11], A[11], not_1_out);
  and and_6 (B[10], A[10], not_1_out);
  and and_7 (B[9], A[9], not_1_out);
  and and_8 (B[8], A[8], not_1_out);
  and and_9 (B[7], A[7], not_1_out);
  and and_10 (B[6], A[6], not_1_out);
  and and_11 (B[5], A[5], not_1_out);
  and and_12 (B[4], A[4], not_1_out);
  and and_13 (B[3], A[3], not_1_out);
  and and_14 (B[2], A[2], not_1_out);
  and and_15 (B[1], A[1], not_1_out);
  not not_1 (not_1_out, S);
  or or_1 (B[0], A[0], S);
endmodule

module Jump_Decoder (
  input  c3,
  input  c2,
  input  c1,
  input  c0,
  input  e,
  input  z,
  input  c,
  input  a,
  input  n,
  input  v,
  output jmp
);

  wire and_1_out, and_2_out, and_3_out, and_4_out, and_5_out, and_6_out, and_7_out, and_8_out, and_9_out,
       and_10_out, and_11_out, and_12_out, and_13_out, and_14_out, demultiplexer_1_out0,
       demultiplexer_1_out1, demultiplexer_1_out2, demultiplexer_1_out3, demultiplexer_1_out4,
       demultiplexer_1_out5, demultiplexer_1_out6, demultiplexer_1_out7, demultiplexer_1_out8,
       demultiplexer_1_out9, demultiplexer_1_out10, demultiplexer_1_out11, demultiplexer_1_out12,
       demultiplexer_1_out13, not_1_out, not_2_out, not_3_out, not_4_out, not_5_out, not_6_out, or_2_out,
       or_3_out;

  Demultiplexer #(.enable("false"), .select(4)) demultiplexer_1 (
    .out0(demultiplexer_1_out0), .out1(demultiplexer_1_out1), .out2(demultiplexer_1_out2),
    .out3(demultiplexer_1_out3), .out4(demultiplexer_1_out4), .out5(demultiplexer_1_out5),
    .out6(demultiplexer_1_out6), .out7(demultiplexer_1_out7), .out8(demultiplexer_1_out8),
    .out9(demultiplexer_1_out9), .out10(demultiplexer_1_out10), .out11(demultiplexer_1_out11),
    .out12(demultiplexer_1_out12), .out13(demultiplexer_1_out13), .in(1'b1), .sel({c3, c2, c1, c0}));  // open: out14, out15
  and and_1 (and_1_out, demultiplexer_1_out0, e);
  and and_2 (and_2_out, demultiplexer_1_out1, not_1_out);
  not not_1 (not_1_out, e);
  and and_3 (and_3_out, demultiplexer_1_out2, z);
  and and_4 (and_4_out, demultiplexer_1_out3, not_2_out);
  not not_2 (not_2_out, z);
  and and_5 (and_5_out, demultiplexer_1_out4, c);
  and and_6 (and_6_out, demultiplexer_1_out5, not_3_out);
  not not_3 (not_3_out, c);
  or or_1 (jmp, and_1_out, and_2_out, and_3_out, and_4_out, and_5_out, and_6_out, and_7_out, and_8_out, and_9_out, and_10_out, and_11_out, and_12_out, and_13_out, and_14_out);
  and and_7 (and_7_out, demultiplexer_1_out6, a);
  and and_8 (and_8_out, demultiplexer_1_out7, or_2_out);
  and and_9 (and_9_out, demultiplexer_1_out8, not_1_out, not_4_out);
  or or_2 (or_2_out, e, a);
  not not_4 (not_4_out, a);
  and and_10 (and_10_out, demultiplexer_1_out9, or_3_out);
  and and_11 (and_11_out, demultiplexer_1_out10, not_2_out, not_5_out);
  or or_3 (or_3_out, e, not_4_out);
  not not_5 (not_5_out, n);
  and and_12 (and_12_out, demultiplexer_1_out11, not_2_out, n);
  and and_13 (and_13_out, demultiplexer_1_out12, v);
  and and_14 (and_14_out, demultiplexer_1_out13, not_6_out);
  not not_6 (not_6_out, v);
endmodule

module Zero (
  input  [15:0] A,
  output Z
);

  nor nor_1 (Z, A[0], A[1], A[2], A[3], A[4], A[5], A[6], A[7], A[8], A[9], A[10], A[11], A[12], A[13], A[14], A[15]);
endmodule

module _3_8_Demux (
  input  A,
  input  B,
  input  C,
  output [7:0] Out
);

  wire not_1_out, not_2_out, not_3_out, not_4_out, not_5_out, not_6_out, not_7_out, not_8_out, not_9_out,
       not_10_out, not_11_out, not_12_out;

  not not_1 (not_1_out, A);
  not not_2 (not_2_out, B);
  not not_3 (not_3_out, C);
  not not_4 (not_4_out, A);
  not not_5 (not_5_out, B);
  not not_6 (not_6_out, A);
  not not_7 (not_7_out, C);
  not not_8 (not_8_out, A);
  not not_9 (not_9_out, B);
  not not_10 (not_10_out, C);
  not not_11 (not_11_out, B);
  not not_12 (not_12_out, C);
  and and_1 (Out[7], A, B, C);
  and and_2 (Out[0], not_1_out, not_2_out, not_3_out);
  and and_3 (Out[1], not_4_out, not_5_out, C);
  and and_4 (Out[2], not_6_out, B, not_7_out);
  and and_5 (Out[3], not_8_out, B, C);
  and and_6 (Out[4], A, not_9_out, not_10_out);
  and and_7 (Out[5], A, not_11_out, C);
  and and_8 (Out[6], A, B, not_12_out);
endmodule
