// Logisim project SquareRooter.circ as structural Verilog: 10 circuits, main circuit Rooter
module Rooter (
  input  [15:0] X,
  input  clk,
  input  en,
  input  clear,
  output [15:0] SQRT,
  output NaN,
  output INF,
  output done
);

  wire adder_3_cout, classifier_1_subnorm, multiplexer_1_out, not_1_out, rounder_1_round, X0, Xinf, XNaN,
       Xnum;
  wire [3:0] lzc_shift_1_shift;
  wire [4:0] adder_1_out, adder_2_out, exp_adj_1_e_out, exp_subn_1_exp, multiplexer_2_out, multiplexer_3_out;
  wire [8:0] mant_root_1_sqrt_2;
  wire [9:0] adder_3_out, bit_extender_1_out, lzc_shift_1_m_out;
  wire [14:0] bit_extender_2_out;
  wire [31:0] mant_root_1_sqrt;

  Classifier classifier_1 (.inf(Xinf), .num(Xnum), .subnorm(classifier_1_subnorm), ._0(X0), .NaN(XNaN), .val(X));
  LZC_Shift lzc_shift_1 (
    .shift(lzc_shift_1_shift), .m_out(lzc_shift_1_m_out), .subnorm(classifier_1_subnorm), .m_in(X[9:0]));
  Multiplexer #(.enable("false")) multiplexer_1 (
    .in0(X[10]), .in1(not_1_out), .out(multiplexer_1_out), .sel(classifier_1_subnorm));
  not not_1 (not_1_out, lzc_shift_1_shift[0]);
  Exp_Adj exp_adj_1 (.e_out(exp_adj_1_e_out), .e_in(X[14:10]));
  Exp_SubN exp_subn_1 (.exp(exp_subn_1_exp), .shift(lzc_shift_1_shift));
  Mant_Root mant_root_1 (
    .SQRT({mant_root_1_sqrt[31], mant_root_1_sqrt_2, mant_root_1_sqrt[21:0]}), .done(done),
    .e_odd(multiplexer_1_out), .clk(clk), .en(en), .clear(clear), .X(lzc_shift_1_m_out));
  Multiplexer #(.enable("false"), .width(5)) multiplexer_2 (
    .in0(exp_adj_1_e_out), .in1(exp_subn_1_exp), .out(multiplexer_2_out), .sel(classifier_1_subnorm));
  Adder #(.width(5)) adder_1 (.a(multiplexer_2_out), .b(5'b01110), .out(adder_1_out));  // open: cin, cout
  Adder #(.width(5)) adder_2 (.a(multiplexer_2_out), .b(5'b01111), .out(adder_2_out));  // open: cin, cout
  Multiplexer #(.enable("false"), .width(5)) multiplexer_3 (
    .in0(adder_1_out), .in1(adder_2_out), .out(multiplexer_3_out), .sel(adder_3_cout));
  Rounder rounder_1 (.Round(rounder_1_round), .Mant_Lo(mant_root_1_sqrt[20:10]), .Mant_10(mant_root_1_sqrt[21]));
  assign bit_extender_1_out = {{9{1'b0}}, rounder_1_round};  // Bit_Extender bit_extender_1
  Adder #(.width(10)) adder_3 (
    .a({mant_root_1_sqrt_2, mant_root_1_sqrt[21]}), .b(bit_extender_1_out), .out(adder_3_out),
    .cout(adder_3_cout));  // open: cin
  Selector selector_1 (
    .res(SQRT), .exp(multiplexer_3_out), .mant(adder_3_out), .Xnum(Xnum), .X0(X0), .Xinf(Xinf), .XNaN(XNaN),
    .sign(X[15]));
  Bit_Extender #(.in_width(16), .out_width(15), .\type ("zero")) bit_extender_2 (.in(SQRT), .out(bit_extender_2_out));
  Comparator #(.mode("unsigned"), .width(15)) comparator_1 (
    .a(bit_extender_2_out), .b(15'h7c00), .gt(NaN), .eq(INF));  // open: lt
endmodule

module Classifier (
  input  [15:0] val,
  output NaN,
  output inf,
  output num,
  output subnorm,
  output _0
);

  wire comparator_1_eq, comparator_1_gt, comparator_1_lt, comparator_2_eq, comparator_2_gt, comparator_3_lt;

  Comparator #(.mode("unsigned"), .width(15)) comparator_1 (
    .a(val[14:0]), .b(15'h7c00), .gt(comparator_1_gt), .eq(comparator_1_eq), .lt(comparator_1_lt));
  Comparator #(.mode("unsigned"), .width(15)) comparator_2 (
    .a(val[14:0]), .b({15{1'b0}}), .gt(comparator_2_gt), .eq(comparator_2_eq));  // open: lt
  Comparator #(.mode("unsigned"), .width(15)) comparator_3 (
    .a(val[14:0]), .b(15'h400), .lt(comparator_3_lt));  // open: gt, eq
  Multiplexer #(.enable("false")) multiplexer_1 (.in0(comparator_1_gt), .in1(1'b0), .out(NaN), .sel(comparator_1_lt));
  Multiplexer #(.enable("false")) multiplexer_2 (.in0(comparator_1_eq), .in1(1'b0), .out(inf), .sel(comparator_1_lt));
  Multiplexer #(.enable("false")) multiplexer_3 (.in0(1'b0), .in1(comparator_2_gt), .out(num), .sel(comparator_1_lt));
  Multiplexer #(.enable("false")) multiplexer_4 (.in0(1'b0), .in1(comparator_2_eq), .out(_0), .sel(comparator_1_lt));
  and and_1 (subnorm, num, comparator_3_lt);
endmodule

module Exp_Adj (
  input  [4:0] e_in,
  output [4:0] e_out
);

  wire [5:0] adder_1_out, bit_extender_1_out, multiplexer_1_out, shifter_1_out, subtractor_1_out;

  assign bit_extender_1_out = {{1{1'b0}}, e_in};  // Bit_Extender bit_extender_1
  Subtractor #(.width(6)) subtractor_1 (
    .a(bit_extender_1_out), .b(6'b001111), .out(subtractor_1_out));  // open: bin, bout
  Multiplexer #(.enable("false"), .width(6)) multiplexer_1 (
    .in0(6'b000001), .in1(6'b000010), .out(multiplexer_1_out), .sel(bit_extender_1_out[0]));
  Adder #(.width(6)) adder_1 (.a(subtractor_1_out), .b(multiplexer_1_out), .out(adder_1_out));  // open: cin, cout
  Shifter #(.shift("ar"), .width(6)) shifter_1 (.in(adder_1_out), .\dist (3'b001), .out(shifter_1_out));
  Bit_Extender #(.in_width(6), .out_width(5), .\type ("zero")) bit_extender_2 (.in(shifter_1_out), .out(e_out));
endmodule

module Exp_SubN (
  input  [3:0] shift,
  output [4:0] exp
);

  wire not_1_out;
  wire [4:0] adder_1_out, bit_extender_1_out, bit_extender_2_out, not_2_out, shifter_1_out, subtractor_1_out;

  assign bit_extender_1_out = {{1{1'b0}}, shift};  // Bit_Extender bit_extender_1
  Adder #(.width(5)) adder_1 (.a(5'b01110), .b(bit_extender_1_out), .out(adder_1_out));  // open: cin, cout
  assign bit_extender_2_out = {{4{1'b0}}, bit_extender_1_out[0]};  // Bit_Extender bit_extender_2
  not not_1 (not_1_out, bit_extender_1_out[0]);
  Subtractor #(.width(5)) subtractor_1 (
    .a(adder_1_out), .b(bit_extender_2_out), .out(subtractor_1_out));  // open: bin, bout
  Shifter #(.shift("lr"), .width(5)) shifter_1 (.in(subtractor_1_out), .\dist (3'b001), .out(shifter_1_out));
  assign not_2_out = ~shifter_1_out;  // NOT_Gate not_2, 5 bits wide
  Adder #(.width(5)) adder_2 (.a(not_2_out), .b(5'b00001), .out(exp), .cin(not_1_out));  // open: cout
endmodule

module LZC_Shift (
  input  subnorm,
  input  [9:0] m_in,
  output [3:0] shift,
  output [9:0] m_out
);

  wire [3:0] bitfinder_1_index, subtractor_1_out;
  wire [9:0] shifter_1_out;

  BitFinder #(.\type ("high1"), .width(10)) bitfinder_1 (.in(m_in), .index(bitfinder_1_index));  // open: found
  Subtractor #(.width(4)) subtractor_1 (.a(4'b1010), .b(bitfinder_1_index), .out(subtractor_1_out));  // open: bin, bout
  Shifter #(.width(10)) shifter_1 (.in(m_in), .\dist (subtractor_1_out), .out(shifter_1_out));
  Multiplexer #(.enable("false"), .width(4)) multiplexer_1 (
    .in0(4'b0000), .in1(subtractor_1_out), .out(shift), .sel(subnorm));
  Multiplexer #(.enable("false"), .width(10)) multiplexer_2 (
    .in0(m_in), .in1(shifter_1_out), .out(m_out), .sel(subnorm));
endmodule

module Mant_Root (
  input  [9:0] X,
  input  e_odd,
  input  clk,
  input  en,
  input  clear,
  output [31:0] SQRT,
  output done
);

  wire and_1_out, comparator_1_lt, comparator_2_eq, comparator_3_lt, not_1_out, or_1_out, sr_latch_1_q;
  wire [4:0] multiplexer_1_out;
  wire [5:0] counter_1_q;
  wire [10:0] bit_extender_1_out;
  wire [31:0] adder_1_out, adder_2_out, adder_3_out, bit_extender_2_out, bit_extender_3_out,
       bit_extender_4_out, multiplexer_2_out, multiplexer_3_out, multiplexer_4_out, multiplexer_5_out,
       register_1_q, register_2_q, register_3_q, shifter_1_out, shifter_2_out, shifter_3_out, shifter_4_out,
       shifter_5_out, subtractor_1_out;

  assign bit_extender_1_out = {{1{1'b1}}, X};  // Bit_Extender bit_extender_1
  and and_1 (and_1_out, en, clk);
  or or_1 (or_1_out, clk, clear);
  Multiplexer #(.enable("false"), .width(5)) multiplexer_1 (
    .in0(5'b10101), .in1(5'b10100), .out(multiplexer_1_out), .sel(e_odd));
  assign bit_extender_2_out = {{21{1'b0}}, bit_extender_1_out};  // Bit_Extender bit_extender_2
  Counter #(.max('h3f), .ongoal("stay"), .width(6)) counter_1 (
    .load(sr_latch_1_q), .Q(counter_1_q), .clk(clk), .clr(clear));  // open: D, count, carry
  Multiplexer #(.enable("false"), .width(32)) multiplexer_2 (
    .in0(multiplexer_5_out), .in1({32{1'b0}}), .out(multiplexer_2_out), .sel(comparator_1_lt));
  Shifter #(.width(32)) shifter_1 (.in(bit_extender_2_out), .\dist (multiplexer_1_out), .out(shifter_1_out));
  Multiplexer #(.enable("false"), .width(32)) multiplexer_3 (
    .in0(adder_3_out), .in1({32{1'b0}}), .out(multiplexer_3_out), .sel(comparator_1_lt));
  Comparator #(.mode("unsigned"), .width(6)) comparator_1 (
    .a(counter_1_q), .b(6'b000001), .lt(comparator_1_lt));  // open: gt, eq
  Comparator #(.mode("unsigned"), .width(6)) comparator_2 (
    .a(counter_1_q), .b(6'b100001), .gt(done), .eq(comparator_2_eq));  // open: lt
  SR_Latch sr_latch_1 (.Q(sr_latch_1_q), .R(en), .S(or_1_out));
  Multiplexer #(.enable("false"), .width(32)) multiplexer_4 (
    .in0(shifter_3_out), .in1(shifter_1_out), .out(multiplexer_4_out), .sel(comparator_1_lt));
  Register #(.width(32)) register_1 (.D(multiplexer_2_out), .Q(register_1_q), .clk(and_1_out));  // open: en, clr
  Register #(.width(32)) register_2 (.D(multiplexer_4_out), .Q(register_2_q), .clk(and_1_out));  // open: en, clr
  Register #(.width(32)) register_3 (.D(multiplexer_3_out), .Q(register_3_q), .clk(and_1_out));  // open: en, clr
  Shifter #(.width(32)) shifter_2 (.in(register_1_q), .\dist (5'b00010), .out(shifter_2_out));
  assign bit_extender_3_out = {{30{1'b0}}, register_2_q[31:30]};  // Bit_Extender bit_extender_3
  Shifter #(.width(32)) shifter_3 (.in(register_2_q), .\dist (5'b00010), .out(shifter_3_out));
  Shifter #(.width(32)) shifter_4 (.in(register_3_q), .\dist (5'b00010), .out(shifter_4_out));
  Register #(.width(32)) register_4 (.D(multiplexer_3_out), .Q(SQRT), .clk(comparator_2_eq));  // open: en, clr
  Adder #(.width(32)) adder_1 (.a(shifter_2_out), .b(bit_extender_3_out), .out(adder_1_out));  // open: cin, cout
  Adder #(.width(32)) adder_2 (.a(shifter_4_out), .b(32'h1), .out(adder_2_out));  // open: cin, cout
  Subtractor #(.width(32)) subtractor_1 (.a(adder_1_out), .b(adder_2_out), .out(subtractor_1_out));  // open: bin, bout
  Comparator #(.mode("unsigned"), .width(32)) comparator_3 (
    .a(adder_1_out), .b(adder_2_out), .lt(comparator_3_lt));  // open: gt, eq
  not not_1 (not_1_out, comparator_3_lt);
  Multiplexer #(.enable("false"), .width(32)) multiplexer_5 (
    .in0(adder_1_out), .in1(subtractor_1_out), .out(multiplexer_5_out), .sel(not_1_out));
  assign bit_extender_4_out = {{31{1'b0}}, not_1_out};  // Bit_Extender bit_extender_4
  Shifter #(.width(32)) shifter_5 (.in(register_3_q), .\dist (5'b00001), .out(shifter_5_out));
  Adder #(.width(32)) adder_3 (.a(bit_extender_4_out), .b(shifter_5_out), .out(adder_3_out));  // open: cin, cout
endmodule

module Rounder (
  input  Mant_10,
  input  [10:0] Mant_Lo,
  output Round
);

  wire or_1_out, sticky_1_out;

  Sticky sticky_1 (.out(sticky_1_out), .in(Mant_Lo[9:0]));
  or or_1 (or_1_out, Mant_10, sticky_1_out);
  and and_1 (Round, or_1_out, Mant_Lo[10]);
endmodule

module Selector (
  input  [4:0] exp,
  input  [9:0] mant,
  input  Xnum,
  input  X0,
  input  Xinf,
  input  XNaN,
  input  sign,
  output [15:0] res
);

  wire or_1_out;
  wire [1:0] priority_encoder_1_out;

  or or_1 (or_1_out, XNaN, sign);
  Priority_Encoder #(.select(2)) priority_encoder_1 (
    .in0(Xnum), .in1(X0), .in2(Xinf), .in3(or_1_out), .out(priority_encoder_1_out));  // open: gs, en_out, en_in
  Multiplexer #(.enable("false"), .select(2), .width(15)) multiplexer_1 (
    .in0({exp, mant}), .in1({15{1'b0}}), .in2(15'h7c00), .in3(15'h7e00), .out(res[14:0]),
    .sel(priority_encoder_1_out));

  assign res[15] = 1'b0;
endmodule

module Sticky (
  input  [9:0] in,
  output out
);

  or or_1 (out, in[0], in[1], in[2], in[3], in[4], in[5], in[6], in[7], in[8], in[9]);
endmodule

module SR_Latch (
  input  S,
  input  R,
  output Q
);

  wire nor_1_out;

  nor nor_1 (nor_1_out, S, Q);
  nor nor_2 (Q, nor_1_out, R);
endmodule
